// Logisim project brojacuobasmjera.circ as structural Verilog: 1 circuit, main circuit main
module main (
  input  in_1,
  input  S0,
  input  S1,
  output [3:0] out_4
);

  wire and_1_out, and_2_out, and_3_out, and_4_out, and_5_out, and_6_out, buffer_1_out, buffer_2_out,
       buffer_3_out, buffer_4_out, buffer_5_out, buffer_6_out, buffer_7_out, d_ff_1_q, d_ff_1_qn, d_ff_2_q,
       d_ff_2_qn, d_ff_3_q, d_ff_3_qn, or_1_out, t_ff_1_qn, t_ff_2_qn, t_ff_3_qn, xor_1_out, xor_2_out,
       xor_3_out, xor_4_out, xor_5_out, xor_6_out, xor_7_out;

  or or_1 (or_1_out, S1, S0);
  buf buffer_1 (buffer_1_out, or_1_out);
  buf buffer_2 (buffer_2_out, buffer_1_out);
  buf buffer_3 (buffer_3_out, buffer_2_out);
  T_Flip_Flop t_ff_1 (.T(xor_1_out), .clk(buffer_7_out), .Q(out_4[0]), .Qn(t_ff_1_qn));  // open: reset, preset
  xor xor_1 (xor_1_out, S0, S1);
  buf buffer_4 (buffer_4_out, buffer_3_out);
  buf buffer_5 (buffer_5_out, buffer_4_out);
  buf buffer_6 (buffer_6_out, buffer_5_out);
  buf buffer_7 (buffer_7_out, buffer_6_out);
  xor xor_2 (xor_2_out, d_ff_1_q, 1'b1);
  D_Flip_Flop d_ff_1 (.D(xor_2_out), .clk(in_1), .Q(d_ff_1_q), .Qn(d_ff_1_qn));  // open: preset, reset
  and and_1 (and_1_out, S0, out_4[0]);
  T_Flip_Flop t_ff_2 (.T(xor_3_out), .clk(buffer_7_out), .Q(out_4[1]), .Qn(t_ff_2_qn));  // open: reset, preset
  xor xor_3 (xor_3_out, and_1_out, and_2_out);
  and and_2 (and_2_out, t_ff_1_qn, S1);
  D_Flip_Flop d_ff_2 (.D(xor_4_out), .clk(d_ff_1_q), .Q(d_ff_2_q), .Qn(d_ff_2_qn));  // open: preset, reset
  xor xor_4 (xor_4_out, d_ff_2_q, 1'b1);
  and and_3 (and_3_out, out_4[0], S0, out_4[1]);
  and and_4 (and_4_out, t_ff_2_qn, S1, t_ff_1_qn);
  D_Flip_Flop d_ff_3 (.D(xor_5_out), .clk(d_ff_2_q), .Q(d_ff_3_q), .Qn(d_ff_3_qn));  // open: preset, reset
  xor xor_5 (xor_5_out, d_ff_3_q, 1'b1);
  T_Flip_Flop t_ff_3 (.T(xor_6_out), .clk(buffer_7_out), .Q(out_4[2]), .Qn(t_ff_3_qn));  // open: reset, preset
  xor xor_6 (xor_6_out, and_3_out, and_4_out);
  and and_5 (and_5_out, out_4[0], out_4[1], out_4[2], S0);
  and and_6 (and_6_out, t_ff_3_qn, t_ff_2_qn, t_ff_1_qn, S1);
  T_Flip_Flop t_ff_4 (.T(xor_7_out), .clk(buffer_7_out), .Q(out_4[3]));  // open: Qn, reset, preset
  xor xor_7 (xor_7_out, and_5_out, and_6_out);
endmodule
