// Logisim project z2.circ as structural Verilog: 1 circuit, main circuit main
module main (
  input  [31:0] ulaz,
  input  [4:0] kontrola,
  output izlaz
);

  wire multiplexer_1_out, multiplexer_2_out, multiplexer_3_out, multiplexer_4_out, multiplexer_5_out,
       multiplexer_6_out, multiplexer_7_out, multiplexer_8_out, multiplexer_9_out, multiplexer_10_out;

  Multiplexer #(.select(2)) multiplexer_1 (
    .in0(ulaz[0]), .in1(ulaz[1]), .in2(ulaz[2]), .in3(ulaz[3]), .out(multiplexer_1_out), .sel(kontrola[1:0]));
  Multiplexer #(.select(2)) multiplexer_2 (
    .in0(ulaz[28]), .in1(ulaz[29]), .in2(ulaz[30]), .in3(ulaz[31]), .out(multiplexer_2_out),
    .sel(kontrola[1:0]));
  Multiplexer #(.select(2)) multiplexer_3 (
    .in0(ulaz[4]), .in1(ulaz[5]), .in2(ulaz[6]), .in3(ulaz[7]), .out(multiplexer_3_out), .sel(kontrola[1:0]));
  Multiplexer #(.select(2)) multiplexer_4 (
    .in0(ulaz[24]), .in1(ulaz[25]), .in2(ulaz[26]), .in3(ulaz[27]), .out(multiplexer_4_out),
    .sel(kontrola[1:0]));
  Multiplexer #(.select(2)) multiplexer_5 (
    .in0(ulaz[8]), .in1(ulaz[9]), .in2(ulaz[10]), .in3(ulaz[11]), .out(multiplexer_5_out), .sel(kontrola[1:0]));
  Multiplexer #(.select(2)) multiplexer_6 (
    .in0(ulaz[20]), .in1(ulaz[21]), .in2(ulaz[22]), .in3(ulaz[23]), .out(multiplexer_6_out),
    .sel(kontrola[1:0]));
  Multiplexer #(.select(2)) multiplexer_7 (
    .in0(ulaz[12]), .in1(ulaz[13]), .in2(ulaz[14]), .in3(ulaz[15]), .out(multiplexer_7_out),
    .sel(kontrola[1:0]));
  Multiplexer #(.select(2)) multiplexer_8 (
    .in0(ulaz[16]), .in1(ulaz[17]), .in2(ulaz[18]), .in3(ulaz[19]), .out(multiplexer_8_out),
    .sel(kontrola[1:0]));
  Multiplexer #(.select(2)) multiplexer_9 (
    .in0(multiplexer_1_out), .in1(multiplexer_3_out), .in2(multiplexer_5_out), .in3(multiplexer_7_out),
    .out(multiplexer_9_out), .sel(kontrola[3:2]));
  Multiplexer #(.select(2)) multiplexer_10 (
    .in0(multiplexer_8_out), .in1(multiplexer_6_out), .in2(multiplexer_4_out), .in3(multiplexer_2_out),
    .out(multiplexer_10_out), .sel(kontrola[3:2]));
  Multiplexer #(.select(2)) multiplexer_11 (
    .in0(multiplexer_9_out), .in1(multiplexer_10_out), .in2(1'b0), .in3(1'b0), .out(izlaz),
    .sel({1'b0, kontrola[4]}));
endmodule
