// Logisim project svasta.circ as structural Verilog
module main (
  input  in_1,
  input  in_2,
  output [1:0] out_3
);

  wire and_1_out, and_2_out, and_3_out, and_4_out, clock_1_out, clock_2_out, clock_3_out, d_ff_2_q, d_ff_3_q,
       j_k_ff_1_q, not_1_out, t_ff_1_q, t_ff_3_q, t_ff_4_q;

  Clock clock_1 (.out(clock_1_out));
  D_Flip_Flop d_ff_1 (.D(d_ff_2_q), .clk(clock_2_out));  // open: Q, Qn, preset, reset
  Clock clock_2 (.out(clock_2_out));
  T_Flip_Flop t_ff_1 (.T(1'b1), .clk(clock_1_out), .Q(t_ff_1_q), .Qn(out_3[0]), .preset(and_1_out));  // open: reset
  D_Flip_Flop d_ff_2 (.D(d_ff_3_q), .clk(clock_2_out), .Q(d_ff_2_q));  // open: Qn, preset, reset
  Clock clock_3 (.out(clock_3_out));
  T_Flip_Flop t_ff_2 (.T(1'b1), .clk(t_ff_1_q), .Qn(out_3[1]), .preset(and_1_out));  // open: Q, reset
  D_Flip_Flop d_ff_3 (.D(in_1), .clk(clock_2_out), .Q(d_ff_3_q));  // open: Qn, preset, reset
  J_K_Flip_Flop j_k_ff_1 (.J(in_2), .K(not_1_out), .clk(clock_3_out), .Q(j_k_ff_1_q));  // open: Qn, preset, reset
  not not_1 (not_1_out, in_2);
  and and_1 (and_1_out, out_3[1], out_3[0]);
  and and_2 (and_2_out, ~out_3[1], out_3[0]);  // AND_Gate
  and and_3 (and_3_out, and_2_out, d_ff_3_q);
  and and_4 (and_4_out, and_2_out, ~d_ff_3_q);  // AND_Gate
  T_Flip_Flop t_ff_3 (.T(1'b1), .clk(and_3_out), .Q(t_ff_3_q));  // open: Qn, reset, preset
  T_Flip_Flop t_ff_4 (.T(1'b1), .clk(t_ff_3_q), .Q(t_ff_4_q));  // open: Qn, reset, preset
  T_Flip_Flop t_ff_5 (.T(1'b1), .clk(t_ff_4_q));  // open: Q, Qn, reset, preset
endmodule

module osamkk (
  input  [2:0] ulaz,
  output [2:0] izlaz
);

  wire nor_1_out, not_1_out;

  nor nor_1 (nor_1_out, ulaz[0], ulaz[1]);
  xor xor_1 (izlaz[2], nor_1_out, not_1_out);
  not not_1 (not_1_out, ulaz[2]);
  xor xor_2 (izlaz[1], ulaz[0], ulaz[1]);

  assign izlaz[0] = ulaz[0];
endmodule

module kolo32u1preko4u1 (
  input  [31:0] ulaz,
  input  [4:0] kontrola,
  output izlaz
);

  wire multiplexer_1_out, multiplexer_2_out, multiplexer_3_out, multiplexer_4_out, multiplexer_5_out,
       multiplexer_6_out, multiplexer_7_out, multiplexer_8_out, multiplexer_9_out, multiplexer_10_out;

  Multiplexer #(.select(2)) multiplexer_1 (
    .in0(ulaz[0]), .in1(ulaz[1]), .in2(ulaz[2]), .in3(ulaz[3]), .out(multiplexer_1_out), .sel(kontrola[1:0]));
  Multiplexer #(.select(2)) multiplexer_2 (
    .in0(ulaz[28]), .in1(ulaz[29]), .in2(ulaz[30]), .in3(ulaz[31]), .out(multiplexer_2_out),
    .sel(kontrola[1:0]));
  Multiplexer #(.select(2)) multiplexer_3 (
    .in0(ulaz[4]), .in1(ulaz[5]), .in2(ulaz[6]), .in3(ulaz[7]), .out(multiplexer_3_out), .sel(kontrola[1:0]));
  Multiplexer #(.select(2)) multiplexer_4 (
    .in0(ulaz[24]), .in1(ulaz[25]), .in2(ulaz[26]), .in3(ulaz[27]), .out(multiplexer_4_out),
    .sel(kontrola[1:0]));
  Multiplexer #(.select(2)) multiplexer_5 (
    .in0(ulaz[8]), .in1(ulaz[9]), .in2(ulaz[10]), .in3(ulaz[11]), .out(multiplexer_5_out), .sel(kontrola[1:0]));
  Multiplexer #(.select(2)) multiplexer_6 (
    .in0(ulaz[20]), .in1(ulaz[21]), .in2(ulaz[22]), .in3(ulaz[23]), .out(multiplexer_6_out),
    .sel(kontrola[1:0]));
  Multiplexer #(.select(2)) multiplexer_7 (
    .in0(ulaz[12]), .in1(ulaz[13]), .in2(ulaz[14]), .in3(ulaz[15]), .out(multiplexer_7_out),
    .sel(kontrola[1:0]));
  Multiplexer #(.select(2)) multiplexer_8 (
    .in0(ulaz[16]), .in1(ulaz[17]), .in2(ulaz[18]), .in3(ulaz[19]), .out(multiplexer_8_out),
    .sel(kontrola[1:0]));
  Multiplexer #(.select(2)) multiplexer_9 (
    .in0(multiplexer_1_out), .in1(multiplexer_3_out), .in2(multiplexer_5_out), .in3(multiplexer_7_out),
    .out(multiplexer_9_out), .sel(kontrola[3:2]));
  Multiplexer #(.select(2)) multiplexer_10 (
    .in0(multiplexer_8_out), .in1(multiplexer_6_out), .in2(multiplexer_4_out), .in3(multiplexer_2_out),
    .out(multiplexer_10_out), .sel(kontrola[3:2]));
  Multiplexer #(.select(2)) multiplexer_11 (
    .in0(multiplexer_9_out), .in1(multiplexer_10_out), .in2(1'b0), .in3(1'b0), .out(izlaz),
    .sel({1'b0, kontrola[4]}));
endmodule

module alu (
  input  [3:0] A,
  input  [3:0] B,
  input  [1:0] C,
  input  [1:0] K,
  input  M,
  output [3:0] decA,
  output [3:0] decB,
  output [3:0] razlikaAiBdec,
  output overflow,
  output [3:0] negiranA,
  output [3:0] ABnegirano,
  output [3:0] zbirAiBdec,
  output [3:0] tempBin,
  output [3:0] tempDec,
  output [3:0] izlaz
);

  wire [3:0] fourbit2kk_1_complement, nor_1_out, nor_2_out, nor_3_out, shifterudesno_1_shiftano,
       shifterulijevo_1_shiftano;

  assign negiranA = ~A;  // NOT_Gate not_1, 4 bits wide
  shifterUlijevo shifterulijevo_1 (.ulaz(tempBin), .K(K), .shiftano(shifterulijevo_1_shiftano));
  shifterUdesno shifterudesno_1 (.ulaz(tempBin), .K(K), .shiftano(shifterudesno_1_shiftano));
  fourbit2kk fourbit2kk_1 (.x(B), .complement(fourbit2kk_1_complement));
  assign nor_1_out = ~(A | A);  // NOR_Gate nor_1, 4 bits wide
  assign nor_2_out = ~(B | B);  // NOR_Gate nor_2, 4 bits wide
  fourbitadderNAND fourbitaddernand_1 (.x(A), .y(B), .xPlusy(zbirAiBdec));  // open: overflow
  Multiplexer #(.width(4)) multiplexer_1 (
    .in0(shifterulijevo_1_shiftano), .in1(shifterudesno_1_shiftano), .out(izlaz), .sel(M));
  fourbitadder fourbitadder_1 (.x(A), .y(fourbit2kk_1_complement), .xPlusy(razlikaAiBdec), .overflow(overflow));
  assign nor_3_out = ~(nor_1_out | nor_2_out);  // NOR_Gate nor_3, 4 bits wide
  assign ABnegirano = ~(nor_3_out | nor_3_out);  // NOR_Gate nor_4, 4 bits wide
  Multiplexer #(.select(2), .width(4)) multiplexer_2 (
    .in0(razlikaAiBdec), .in1(negiranA), .in2(ABnegirano), .in3(zbirAiBdec), .out(tempBin), .sel(C));

  assign decA = A;
  assign decB = B;
  assign tempDec = tempBin;
endmodule

module fulladder (
  input  incarry,
  input  in1,
  input  in2,
  output outcarry,
  output out1
);

  wire and_1_out, and_2_out, xor_1_out;

  xor xor_1 (xor_1_out, in1, in2);
  and and_1 (and_1_out, in1, in2);
  xor xor_2 (out1, xor_1_out, incarry);
  and and_2 (and_2_out, incarry, xor_1_out);
  or or_1 (outcarry, and_2_out, and_1_out);
endmodule

module fourbitadder (
  input  [3:0] x,
  input  [3:0] y,
  output [3:0] xPlusy,
  output overflow
);

  wire fulladder_1_out1, fulladder_2_out1, fulladder_3_out1, fulladder_4_out1;

  fulladder fulladder_1 (.incarry(1'b0), .in1(x[0]), .in2(y[0]), .outcarry(xPlusy[0]), .out1(fulladder_1_out1));
  fulladder fulladder_2 (
    .incarry(fulladder_1_out1), .in1(x[1]), .in2(y[1]), .outcarry(xPlusy[1]), .out1(fulladder_2_out1));
  fulladder fulladder_3 (
    .incarry(fulladder_2_out1), .in1(x[2]), .in2(y[2]), .outcarry(xPlusy[2]), .out1(fulladder_3_out1));
  fulladder fulladder_4 (
    .incarry(fulladder_3_out1), .in1(x[3]), .in2(y[3]), .outcarry(xPlusy[3]), .out1(fulladder_4_out1));
  xor xor_1 (overflow, fulladder_4_out1, fulladder_3_out1);
endmodule

module fourbit2kk (
  input  [3:0] x,
  output [3:0] complement
);

  wire [3:0] not_1_out;

  assign not_1_out = ~x;  // NOT_Gate not_1, 4 bits wide
  fourbitadder fourbitadder_1 (.x(4'b0001), .y(not_1_out), .xPlusy(complement));  // open: overflow
endmodule

module fulladderNAND (
  input  incarry,
  input  in1,
  input  in2,
  output out1,
  output outcarry
);

  wire iksor_out_3, nand_1_out, nand_2_out, nand_3_out, nand_4_out;

  xorprekoNAND iksor (.in_1(in1), .in_2(in2), .out_3(iksor_out_3));
  nand nand_1 (nand_1_out, in1, in2);
  nand nand_2 (nand_2_out, nand_1_out, nand_1_out);
  xorprekoNAND iksor2 (.in_1(iksor_out_3), .in_2(incarry), .out_3(out1));
  nand nand_3 (nand_3_out, incarry, iksor_out_3);
  nand nand_4 (nand_4_out, nand_3_out, nand_3_out);
  iliprekoNAND ili (.in_1(nand_4_out), .in_2(nand_2_out), .out_3(outcarry));
endmodule

module iliprekoNAND (
  input  in_1,
  input  in_2,
  output out_3
);

  wire nand_1_out, nand_2_out;

  nand nand_1 (nand_1_out, in_1, in_1);
  nand nand_2 (nand_2_out, in_2, in_2);
  nand nand_3 (out_3, nand_1_out, nand_2_out);
endmodule

module xorprekoNAND (
  input  in_1,
  input  in_2,
  output out_3
);

  wire nand_1_out, nand_2_out, nand_3_out, nand_5_out;

  nand nand_1 (nand_1_out, in_1, in_1);
  nand nand_2 (nand_2_out, in_2, in_2);
  nand nand_3 (nand_3_out, nand_1_out, in_2);
  nand nand_4 (out_3, nand_3_out, nand_5_out);
  nand nand_5 (nand_5_out, in_1, nand_2_out);
endmodule

module fourbitadderNAND (
  input  [3:0] x,
  input  [3:0] y,
  output [3:0] xPlusy,
  output overflow
);

  wire fulladdernand_1_outcarry, fulladdernand_2_outcarry, fulladdernand_3_outcarry;

  fulladderNAND fulladdernand_1 (
    .incarry(1'b0), .in1(x[0]), .in2(y[0]), .out1(xPlusy[0]), .outcarry(fulladdernand_1_outcarry));
  fulladderNAND fulladdernand_2 (
    .incarry(fulladdernand_1_outcarry), .in1(x[1]), .in2(y[1]), .out1(xPlusy[1]),
    .outcarry(fulladdernand_2_outcarry));
  fulladderNAND fulladdernand_3 (
    .incarry(fulladdernand_2_outcarry), .in1(x[2]), .in2(y[2]), .out1(xPlusy[2]),
    .outcarry(fulladdernand_3_outcarry));
  fulladderNAND fulladdernand_4 (
    .incarry(fulladdernand_3_outcarry), .in1(x[3]), .in2(y[3]), .out1(xPlusy[3]), .outcarry(overflow));
endmodule

module shifterUdesno (
  input  [3:0] ulaz,
  input  [1:0] K,
  output [3:0] shiftano
);

  Multiplexer #(.select(2)) multiplexer_1 (
    .in0(ulaz[0]), .in1(ulaz[1]), .in2(ulaz[2]), .in3(ulaz[3]), .out(shiftano[0]), .sel(K));
  Multiplexer #(.select(2)) multiplexer_2 (
    .in0(ulaz[1]), .in1(ulaz[2]), .in2(ulaz[3]), .in3(1'b0), .out(shiftano[1]), .sel(K));
  Multiplexer #(.select(2)) multiplexer_3 (
    .in0(ulaz[2]), .in1(ulaz[3]), .in2(1'b0), .in3(1'b0), .out(shiftano[2]), .sel(K));
  Multiplexer #(.select(2)) multiplexer_4 (
    .in0(ulaz[3]), .in1(1'b0), .in2(1'b0), .in3(1'b0), .out(shiftano[3]), .sel(K));
endmodule

module shifterUlijevo (
  input  [3:0] ulaz,
  input  [1:0] K,
  output [3:0] shiftano
);

  Multiplexer #(.select(2)) multiplexer_1 (
    .in0(ulaz[0]), .in1(1'b0), .in2(1'b0), .in3(1'b0), .out(shiftano[0]), .sel(K));
  Multiplexer #(.select(2)) multiplexer_2 (
    .in0(ulaz[1]), .in1(ulaz[0]), .in2(1'b0), .in3(1'b0), .out(shiftano[1]), .sel(K));
  Multiplexer #(.select(2)) multiplexer_3 (
    .in0(ulaz[2]), .in1(ulaz[1]), .in2(ulaz[0]), .in3(1'b0), .out(shiftano[2]), .sel(K));
  Multiplexer #(.select(2)) multiplexer_4 (
    .in0(ulaz[3]), .in1(ulaz[2]), .in2(ulaz[1]), .in3(ulaz[0]), .out(shiftano[3]), .sel(K));
endmodule

module mul (
  input  [3:0] in_1,
  input  [3:0] in_2,
  output [3:0] out_3,
  output [3:0] out_4,
  output [7:0] out_5
);

  wire and_1_out, and_2_out, and_3_out, and_4_out, and_5_out, and_7_out, and_8_out, and_10_out, and_11_out,
       and_12_out, and_14_out, and_15_out, fulladder_1_p2, fulladder_1_p6, fulladder_2_p4, fulladder_2_p5,
       fulladder_4_outcarry, fulladder_5_p6, fulladder_5_p7, fulladder_6_out1, fulladder_7_out1,
       fulladder_7_outcarry, fulladder_8_p5, fulladder_8_p6, ha_1_p2, ha_1_p4, ha_1_p5, ha_3_carryu,
       ha_4_carryu;

  and and_1 (and_1_out, in_1[3], in_2[2]);
  and and_2 (and_2_out, in_1[3], in_1[2]);
  // fulladder fulladder_1: pin names not known; wires that end beside it: in_1[3], fulladder_1_p2, and_2_out, out_5[7], in_1[2], fulladder_1_p6, out_5[6]
  and and_3 (and_3_out, in_1[3], in_1[2]);
  // HA ha_1: pin names not known; wires that end beside it: and_3_out, ha_1_p2, in_1[2], ha_1_p4, ha_1_p5
  and and_4 (and_4_out, in_1[2], in_2[2]);
  // fulladder fulladder_2: pin names not known; wires that end beside it: and_1_out, ha_1_p2, fulladder_1_p2, fulladder_2_p4, fulladder_2_p5
  and and_5 (and_5_out, in_1[2], in_1[2]);
  fulladder fulladder_3 (.incarry(in_1[2]), .in1(in_1[2]), .in2(in_1[2]), .outcarry(out_5[5]), .out1(fulladder_1_p6));
  and and_6 (in_1[2], in_1[3], in_2[0]);
  and and_7 (and_7_out, in_1[2], in_1[2]);
  fulladder fulladder_4 (
    .incarry(in_1[2]), .in1(in_1[2]), .in2(in_1[2]), .outcarry(fulladder_4_outcarry), .out1(ha_1_p4));
  // fulladder fulladder_5: pin names not known; wires that end beside it: in_1[2], ha_1_p5, and_4_out, fulladder_2_p4, in_2[2], fulladder_5_p6, fulladder_5_p7
  and and_8 (and_8_out, in_1[2], in_1[2]);
  fulladder fulladder_6 (.incarry(in_1[2]), .in1(in_1[2]), .in2(in_1[2]), .outcarry(out_5[4]), .out1(fulladder_6_out1));
  and and_9 (in_1[2], in_1[2], in_2[0]);
  and and_10 (and_10_out, in_1[2], in_1[2]);
  fulladder fulladder_7 (
    .incarry(in_1[2]), .in1(in_1[2]), .in2(in_1[2]), .outcarry(fulladder_7_outcarry), .out1(fulladder_7_out1));
  and and_11 (and_11_out, in_1[2], in_2[2]);
  // fulladder fulladder_8: pin names not known; wires that end beside it: fulladder_4_outcarry, in_2[2], and_11_out, fulladder_5_p6, fulladder_8_p5, fulladder_8_p6
  HA ha_2 (.Y(fulladder_7_outcarry), .XplusY(out_5[2]), .carryu(fulladder_8_p5));  // open: X
  and and_12 (and_12_out, in_1[2], in_1[2]);
  HA ha_3 (.X(in_1[2]), .Y(in_1[2]), .XplusY(out_5[3]), .carryu(ha_3_carryu));
  and and_13 (in_1[2], in_1[2], in_2[0]);
  HA ha_4 (.X(in_1[2]), .Y(in_1[2]), .XplusY(out_5[1]), .carryu(ha_4_carryu));
  and and_14 (and_14_out, in_1[2], in_2[2]);
  and and_15 (and_15_out, in_1[2], in_1[2]);
  and and_16 (out_5[0], in_1[2], in_2[0]);

  assign in_1[1:0] = {2{in_1[2]}};
  assign {in_2[3], in_2[1]} = {2{in_1[2]}};
  assign out_3 = {in_1[3:2], {2{in_1[2]}}};
  assign out_4 = {in_1[2], in_2[2], in_1[2], in_2[0]};
endmodule

module HA (
  input  X,
  input  Y,
  output XplusY,
  output carryu
);

  xor xor_1 (XplusY, X, Y);
  and and_1 (carryu, X, Y);
endmodule

module poredjac (
  input  x,
  input  y,
  input  biloXmanjeY,
  input  biloXveceY,
  input  biliJednaki,
  output XmanjeY,
  output XveceY,
  output jednaki
);

  wire and_1_out, and_2_out, and_4_out, and_5_out, not_1_out, not_2_out, not_3_out, xor_1_out;

  not not_1 (not_1_out, x);
  not not_2 (not_2_out, y);
  xor xor_1 (xor_1_out, x, y);
  not not_3 (not_3_out, xor_1_out);
  and and_1 (and_1_out, not_3_out, biloXmanjeY);
  and and_2 (and_2_out, not_3_out, biloXveceY);
  and and_3 (jednaki, not_3_out, biliJednaki);
  and and_4 (and_4_out, not_1_out, y);
  and and_5 (and_5_out, not_2_out, x);
  or or_1 (XmanjeY, and_4_out, and_1_out);
  or or_2 (XveceY, and_5_out, and_2_out);
endmodule

module fourbitcomp (
  input  [3:0] x,
  input  [3:0] y,
  output out_3,
  output out_4,
  output out_5
);

  wire poredjac_1_jednaki, poredjac_1_xmanjey, poredjac_1_xvecey, poredjac_2_jednaki, poredjac_2_xmanjey,
       poredjac_2_xvecey, poredjac_3_jednaki, poredjac_3_xmanjey, poredjac_3_xvecey;

  poredjac poredjac_1 (
    .x(x[0]), .y(y[0]), .biloXmanjeY(1'b0), .biloXveceY(1'b0), .biliJednaki(1'b1),
    .XmanjeY(poredjac_1_xmanjey), .XveceY(poredjac_1_xvecey), .jednaki(poredjac_1_jednaki));
  poredjac poredjac_2 (
    .x(x[1]), .y(y[1]), .biloXmanjeY(poredjac_1_xmanjey), .biloXveceY(poredjac_1_xvecey),
    .biliJednaki(poredjac_1_jednaki), .XmanjeY(poredjac_2_xmanjey), .XveceY(poredjac_2_xvecey),
    .jednaki(poredjac_2_jednaki));
  poredjac poredjac_3 (
    .x(x[2]), .y(y[2]), .biloXmanjeY(poredjac_2_xmanjey), .biloXveceY(poredjac_2_xvecey),
    .biliJednaki(poredjac_2_jednaki), .XmanjeY(poredjac_3_xmanjey), .XveceY(poredjac_3_xvecey),
    .jednaki(poredjac_3_jednaki));
  poredjac poredjac_4 (
    .x(x[3]), .y(y[3]), .biloXmanjeY(poredjac_3_xmanjey), .biloXveceY(poredjac_3_xvecey),
    .biliJednaki(poredjac_3_jednaki), .XmanjeY(out_3), .XveceY(out_4), .jednaki(out_5));
endmodule

module signedporedjac (
  input  [3:0] x,
  input  [3:0] y,
  output [3:0] out_3,
  output XmanjeY,
  output [3:0] out_5,
  output XveceY,
  output jednaki
);

  wire not_1_out, not_2_out, poredjac_1_jednaki, poredjac_1_xmanjey, poredjac_1_xvecey, poredjac_2_jednaki,
       poredjac_2_xmanjey, poredjac_2_xvecey, poredjac_3_jednaki, poredjac_3_xmanjey, poredjac_3_xvecey,
       poredjac_4_jednaki, poredjac_4_xmanjey, poredjac_4_xvecey;

  poredjac poredjac_1 (
    .x(x[0]), .y(y[0]), .biloXmanjeY(1'b0), .biloXveceY(1'b0), .biliJednaki(1'b1),
    .XmanjeY(poredjac_1_xmanjey), .XveceY(poredjac_1_xvecey), .jednaki(poredjac_1_jednaki));
  poredjac poredjac_2 (
    .x(x[1]), .y(y[1]), .biloXmanjeY(poredjac_1_xmanjey), .biloXveceY(poredjac_1_xvecey),
    .biliJednaki(poredjac_1_jednaki), .XmanjeY(poredjac_2_xmanjey), .XveceY(poredjac_2_xvecey),
    .jednaki(poredjac_2_jednaki));
  poredjac poredjac_3 (
    .x(x[2]), .y(y[2]), .biloXmanjeY(poredjac_2_xmanjey), .biloXveceY(poredjac_2_xvecey),
    .biliJednaki(poredjac_2_jednaki), .XmanjeY(poredjac_3_xmanjey), .XveceY(poredjac_3_xvecey),
    .jednaki(poredjac_3_jednaki));
  poredjac poredjac_4 (
    .x(x[3]), .y(y[3]), .biloXmanjeY(poredjac_3_xmanjey), .biloXveceY(poredjac_3_xvecey),
    .biliJednaki(poredjac_3_jednaki), .XmanjeY(poredjac_4_xmanjey), .XveceY(poredjac_4_xvecey),
    .jednaki(poredjac_4_jednaki));
  not not_1 (not_1_out, poredjac_4_xvecey);
  not not_2 (not_2_out, poredjac_4_xmanjey);
  Multiplexer #(.select(2)) multiplexer_1 (
    .in0(poredjac_4_xmanjey), .in1(1'b1), .in2(1'b0), .in3(not_1_out), .out(XmanjeY), .sel({y[3], x[3]}));
  Multiplexer #(.select(2)) multiplexer_2 (
    .in0(poredjac_4_xvecey), .in1(1'b0), .in2(1'b1), .in3(not_2_out), .out(XveceY), .sel({y[3], x[3]}));
  Multiplexer #(.select(2)) multiplexer_3 (
    .in0(poredjac_4_jednaki), .in1(1'b0), .in2(1'b0), .in3(poredjac_4_jednaki), .out(jednaki),
    .sel({y[3], x[3]}));

  assign out_3 = x;
  assign out_5 = y;
endmodule

module mux2u1 (
  input  x0,
  input  x1,
  input  control,
  output xout
);

  wire and_1_out, and_2_out, not_1_out;

  and and_1 (and_1_out, x0, not_1_out);
  not not_1 (not_1_out, control);
  and and_2 (and_2_out, x1, control);
  or or_1 (xout, and_1_out, and_2_out);
endmodule

module mux2u1NOR (
  input  x0,
  input  x1,
  input  control,
  output xout
);

  wire nor_1_out, nor_2_out, nor_3_out, nor_4_out, nor_5_out, nor_6_out, nor_7_out, nor_8_out;

  nor nor_1 (nor_1_out, control, control);
  nor nor_2 (nor_2_out, x0, x0);
  nor nor_3 (nor_3_out, nor_1_out, nor_1_out);
  nor nor_4 (nor_4_out, x1, x1);
  nor nor_5 (nor_5_out, control, control);
  nor nor_6 (nor_6_out, nor_2_out, nor_3_out);
  nor nor_7 (nor_7_out, nor_6_out, nor_8_out);
  nor nor_8 (nor_8_out, nor_4_out, nor_5_out);
  nor nor_9 (xout, nor_7_out, nor_7_out);
endmodule

module mux4u1 (
  input  in_1,
  input  in_2,
  input  in_3,
  input  in_4,
  input  in_5,
  input  in_6,
  output out_7
);

  wire mux2u1_1_xout, mux2u1_2_xout;

  mux2u1 mux2u1_1 (.x0(in_1), .x1(in_2), .control(in_5), .xout(mux2u1_1_xout));
  mux2u1 mux2u1_2 (.x0(in_3), .x1(in_4), .control(in_5), .xout(mux2u1_2_xout));
  mux2u1 mux2u1_3 (.x0(mux2u1_1_xout), .x1(mux2u1_2_xout), .control(in_6), .xout(out_7));
endmodule

module mux8u1 (
  input  [7:0] in_1,
  input  [2:0] in_2,
  input  in_3,
  input  in_4,
  input  in_5,
  input  A,
  input  B,
  input  C,
  output out_9
);

  wire and_1_out, and_2_out, and_3_out, and_4_out, mux4u1_1_out_7, mux4u1_2_out_7, nand_1_out, nand_2_out,
       nand_3_out, not_1_out, not_2_out, or_1_out, or_2_out, xor_1_out, xor_2_out;

  nand nand_1 (nand_1_out, in_3, in_4);
  not not_1 (not_1_out, B);
  and and_1 (and_1_out, A, C);
  nand nand_2 (nand_2_out, nand_1_out, in_5);
  nand nand_3 (nand_3_out, in_3, in_4, in_5);
  not not_2 (not_2_out, A);
  and and_2 (and_2_out, A, not_1_out);
  and and_3 (and_3_out, not_1_out, C);
  xor xor_1 (xor_1_out, nand_2_out, nand_3_out);
  or or_1 (or_1_out, and_2_out, and_4_out);
  and and_4 (and_4_out, not_2_out, C);
  or or_2 (or_2_out, and_1_out, and_3_out);
  mux4u1 mux4u1_1 (
    .in_1(in_1[0]), .in_2(in_1[1]), .in_3(in_1[2]), .in_4(in_1[3]), .in_5(in_2[0]), .in_6(in_2[1]),
    .out_7(mux4u1_1_out_7));
  mux4u1 mux4u1_2 (
    .in_1(in_1[4]), .in_2(in_1[5]), .in_3(in_1[6]), .in_4(in_1[7]), .in_5(in_2[0]), .in_6(in_2[1]),
    .out_7(mux4u1_2_out_7));
  xor xor_2 (xor_2_out, or_1_out, or_2_out);
  mux2u1 mux2u1_1 (.x0(mux4u1_1_out_7), .x1(mux4u1_2_out_7), .control(in_2[2]), .xout(out_9));
endmodule

module alu1bit (
  input  X,
  input  Y,
  input  Cin,
  input  kontrol,
  output XplusYCout,
  output XplusYiliYneg
);

  wire and_1_out, and_2_out, not_1_out, xor_1_out, xor_2_out;

  xor xor_1 (xor_1_out, Cin, X);
  and and_1 (and_1_out, X, Cin);
  xor xor_2 (xor_2_out, xor_1_out, Y);
  and and_2 (and_2_out, xor_1_out, Y);
  or or_1 (XplusYCout, and_2_out, and_1_out);
  Multiplexer multiplexer_1 (.in0(xor_2_out), .in1(not_1_out), .out(XplusYiliYneg), .sel(kontrol));
  not not_1 (not_1_out, Y);
endmodule

module ALU4bitPrekoALU1bit (
  input  [3:0] X,
  input  [3:0] Y,
  input  kontrol,
  input  [3:0] in_4,
  input  [3:0] in_5,
  input  in_6,
  output [3:0] out_7,
  output [3:0] out_8,
  output [3:0] out_9,
  output [3:0] out_10,
  output [3:0] Rezultat,
  output [3:0] RezultatBin,
  output [3:0] out_13,
  output [3:0] out_14
);

  wire alu1bit_1_xplusycout, alu1bit_2_xplusycout, alu1bit_3_xplusycout;
  wire [3:0] multiplexer_3_out, multiplexer_4_out, not_1_out, not_2_out;

  assign not_1_out = ~Y;  // NOT_Gate not_1, 4 bits wide
  Multiplexer #(.width(4)) multiplexer_1 (.in0(X), .in1(4'b0001), .out(out_8), .sel(kontrol));
  Multiplexer #(.width(4)) multiplexer_2 (.in0(Y), .in1(not_1_out), .out(out_10), .sel(kontrol));
  Multiplexer #(.width(4)) multiplexer_3 (.in0(in_4), .in1(4'b0001), .out(multiplexer_3_out), .sel(kontrol));
  Multiplexer #(.width(4)) multiplexer_4 (.in0(in_5), .in1(not_2_out), .out(multiplexer_4_out), .sel(in_6));
  assign not_2_out = ~in_5;  // NOT_Gate not_2, 4 bits wide
  alu1bit alu1bit_1 (
    .X(out_8[0]), .Y(out_10[0]), .Cin(1'b0), .kontrol(1'b0), .XplusYCout(alu1bit_1_xplusycout),
    .XplusYiliYneg(Rezultat[0]));
  // AND_Gate and_1 has open pins: in0=multiplexer_4_out[0], out=open
  alu1bit alu1bit_2 (
    .X(out_8[1]), .Y(out_10[1]), .Cin(alu1bit_1_xplusycout), .kontrol(1'b0),
    .XplusYCout(alu1bit_2_xplusycout), .XplusYiliYneg(Rezultat[1]));
  alu1bit alu1bit_3 (
    .X(out_8[2]), .Y(out_10[2]), .Cin(alu1bit_2_xplusycout), .kontrol(1'b0),
    .XplusYCout(alu1bit_3_xplusycout), .XplusYiliYneg(Rezultat[2]));
  alu1bit alu1bit_4 (
    .X(out_8[3]), .Y(out_10[3]), .Cin(alu1bit_3_xplusycout), .kontrol(1'b0), .XplusYiliYneg(Rezultat[3]));  // open: XplusYCout

  assign out_7 = X;
  assign out_9 = Y;
  assign out_13 = in_4;
  assign out_14 = in_5;
  assign RezultatBin = Rezultat;

  // Other names for the same wires on the sheet: K = kontrol
endmodule

module bcdcompare (
  input  [3:0] in_1,
  input  [3:0] in_2
);

  // poredjac poredjac_1: pin names not known
endmodule

module FS (
  input  X,
  input  Y,
  input  Bin,
  output XminusY,
  output Bout
);

  wire and_1_out, and_2_out, xor_1_out;

  xor xor_1 (xor_1_out, X, Y);
  and and_1 (and_1_out, ~X, Y);  // AND_Gate
  xor xor_2 (XminusY, xor_1_out, Bin);
  and and_2 (and_2_out, ~xor_1_out, Bin);  // AND_Gate
  or or_1 (Bout, and_2_out, and_1_out);
endmodule

module fourbitsubtractor (
  input  [3:0] X,
  input  [3:0] Y,
  input  [3:0] in_3,
  input  [3:0] in_4,
  output [3:0] out_5,
  output [3:0] out_6,
  output [3:0] out_7,
  output [3:0] out_8,
  output [3:0] out_9,
  output [3:0] out_10
);

  wire fs_1_bout, fs_2_bout, fs_3_bout, fsmux_1_bout, fsmux_2_bout, fsmux_3_bout;

  FS fs_1 (.X(X[0]), .Y(Y[0]), .Bin(1'b0), .XminusY(out_7[0]), .Bout(fs_1_bout));
  FSmux fsmux_1 (.X(in_3[0]), .Y(in_4[0]), .Bin(1'b0), .XminusY(out_10[0]), .Bout(fsmux_1_bout));
  FS fs_2 (.X(X[1]), .Y(Y[1]), .Bin(fs_1_bout), .XminusY(out_7[1]), .Bout(fs_2_bout));
  FSmux fsmux_2 (.X(in_3[1]), .Y(in_4[1]), .Bin(fsmux_1_bout), .XminusY(out_10[1]), .Bout(fsmux_2_bout));
  FS fs_3 (.X(X[2]), .Y(Y[2]), .Bin(fs_2_bout), .XminusY(out_7[2]), .Bout(fs_3_bout));
  FSmux fsmux_3 (.X(in_3[2]), .Y(in_4[2]), .Bin(fsmux_2_bout), .XminusY(out_10[2]), .Bout(fsmux_3_bout));
  FS fs_4 (.X(X[3]), .Y(Y[3]), .Bin(fs_3_bout), .XminusY(out_7[3]));  // open: Bout
  FSmux fsmux_4 (.X(in_3[3]), .Y(in_4[3]), .Bin(fsmux_3_bout), .XminusY(out_10[3]));  // open: Bout

  assign out_5 = X;
  assign out_6 = Y;
  assign out_8 = in_3;
  assign out_9 = in_4;
endmodule

module FSmux (
  input  X,
  input  Y,
  input  Bin,
  output XminusY,
  output Bout
);

  wire multiplexer_1_out, multiplexer_2_out, multiplexer_4_out, not_1_out, not_2_out, not_3_out, not_4_out,
       not_5_out;

  Multiplexer multiplexer_1 (.in0(X), .in1(not_1_out), .out(multiplexer_1_out), .sel(Y));
  not not_1 (not_1_out, X);
  not not_2 (not_2_out, X);
  not not_3 (not_3_out, multiplexer_1_out);
  Multiplexer multiplexer_2 (.in0(1'b0), .in1(Y), .out(multiplexer_2_out), .sel(not_2_out));
  Multiplexer multiplexer_3 (.in0(multiplexer_1_out), .in1(not_3_out), .out(XminusY), .sel(Bin));
  not not_4 (not_4_out, multiplexer_1_out);
  Multiplexer multiplexer_4 (.in0(1'b0), .in1(Bin), .out(multiplexer_4_out), .sel(not_4_out));
  not not_5 (not_5_out, multiplexer_2_out);
  Multiplexer multiplexer_5 (.in0(multiplexer_2_out), .in1(multiplexer_4_out), .out(Bout), .sel(not_5_out));
endmodule

module jednobitniALU (
  input  A,
  input  B,
  input  CinILIBin,
  input  [1:0] kontrol,
  output Rezultat,
  output CoutILIBout
);

  wire multiplexer_1_out, multiplexer_2_out, multiplexer_3_out, multiplexer_4_out, nand_1_out, nand_2_out,
       nand_3_out, nor_1_out, nor_2_out, nor_3_out, nor_4_out, not_1_out, not_2_out, not_3_out, not_4_out,
       not_5_out;

  Multiplexer multiplexer_1 (.in0(A), .in1(not_1_out), .out(multiplexer_1_out), .sel(B));
  not not_1 (not_1_out, A);
  not not_2 (not_2_out, A);
  Multiplexer multiplexer_2 (.in0(not_2_out), .in1(B), .out(multiplexer_2_out), .sel(not_2_out));
  nor nor_1 (nor_1_out, A, A);
  nor nor_2 (nor_2_out, B, B);
  nand nand_1 (nand_1_out, A, A);
  nand nand_2 (nand_2_out, B, B);
  not not_3 (not_3_out, multiplexer_1_out);
  not not_4 (not_4_out, multiplexer_1_out);
  nor nor_3 (nor_3_out, nor_1_out, nor_2_out);
  nand nand_3 (nand_3_out, nand_1_out, nand_2_out);
  Multiplexer multiplexer_3 (.in0(multiplexer_1_out), .in1(not_3_out), .out(multiplexer_3_out), .sel(CinILIBin));
  Multiplexer multiplexer_4 (.in0(not_4_out), .in1(CinILIBin), .out(multiplexer_4_out), .sel(not_4_out));
  nor nor_4 (nor_4_out, nor_3_out, nor_3_out);
  Multiplexer multiplexer_5 (.in0(multiplexer_2_out), .in1(multiplexer_4_out), .out(CoutILIBout), .sel(not_5_out));
  not not_5 (not_5_out, multiplexer_2_out);
  Multiplexer #(.select(2)) multiplexer_6 (
    .in0(multiplexer_3_out), .in1(B), .in2(nor_4_out), .in3(nand_3_out), .out(Rezultat), .sel(kontrol));
endmodule

module FAnand (
  input  X,
  input  Y,
  input  Cin,
  output XplusY,
  output Cout
);

  wire nand_1_out, nand_2_out, nand_3_out, nand_4_out, nand_5_out, nand_7_out, xorprekonand_1_out_3;

  xorprekoNAND xorprekonand_1 (.in_1(X), .in_2(Y), .out_3(xorprekonand_1_out_3));
  nand nand_1 (nand_1_out, X, Y);
  nand nand_2 (nand_2_out, nand_1_out, nand_1_out);
  xorprekoNAND xorprekonand_2 (.in_1(xorprekonand_1_out_3), .in_2(Cin), .out_3(XplusY));
  nand nand_3 (nand_3_out, xorprekonand_1_out_3, Cin);
  nand nand_4 (nand_4_out, nand_3_out, nand_3_out);
  nand nand_5 (nand_5_out, nand_4_out, nand_4_out);
  nand nand_6 (Cout, nand_5_out, nand_7_out);
  nand nand_7 (nand_7_out, nand_2_out, nand_2_out);
endmodule

module ALUprekojednobitnih (
  input  [3:0] A,
  input  [3:0] B,
  input  [1:0] S,
  output [3:0] out_4,
  output [3:0] out_5,
  output [3:0] Rez,
  output [3:0] out_7
);

  wire jednobitnialu_1_coutilibout, jednobitnialu_2_coutilibout, jednobitnialu_3_coutilibout;

  jednobitniALU jednobitnialu_1 (
    .A(A[0]), .B(B[0]), .CinILIBin(1'b0), .kontrol(S), .Rezultat(out_7[0]),
    .CoutILIBout(jednobitnialu_1_coutilibout));
  jednobitniALU jednobitnialu_2 (
    .A(A[1]), .B(B[1]), .CinILIBin(jednobitnialu_1_coutilibout), .kontrol(S), .Rezultat(out_7[1]),
    .CoutILIBout(jednobitnialu_2_coutilibout));
  jednobitniALU jednobitnialu_3 (
    .A(A[2]), .B(B[2]), .CinILIBin(jednobitnialu_2_coutilibout), .kontrol(S), .Rezultat(out_7[2]),
    .CoutILIBout(jednobitnialu_3_coutilibout));
  jednobitniALU jednobitnialu_4 (
    .A(A[3]), .B(B[3]), .CinILIBin(jednobitnialu_3_coutilibout), .kontrol(S), .Rezultat(out_7[3]));  // open: CoutILIBout

  assign out_4 = A;
  assign out_5 = B;
  assign Rez = out_7;
endmodule

module cetiriIprekoMUX4u1 (
  input  in_1,
  input  in_2,
  input  in_3,
  input  in_4,
  input  in_5,
  input  in_6,
  input  in_7,
  input  in_8
);

  wire multiplexer_5_out, multiplexer_6_out;
  wire [1:0] multiplexer_1_out, multiplexer_3_out;

  Multiplexer #(.select(2)) multiplexer_1 (
    .in0(1'b0), .in1(1'b0), .in2(1'b0), .in3(1'b1), .out(multiplexer_1_out[0]), .sel({in_2, in_1}));
  Multiplexer #(.select(2)) multiplexer_2 (
    .in0(1'b0), .in1(1'b0), .in2(1'b0), .in3(1'b1), .out(multiplexer_1_out[1]), .sel({in_4, in_3}));
  Multiplexer #(.select(2)) multiplexer_3 (
    .in0(1'b0), .in1(1'b1), .in2(1'b1), .in3(1'b1), .out(multiplexer_3_out[0]), .sel({in_6, in_5}));
  Multiplexer #(.select(2)) multiplexer_4 (
    .in0(1'b0), .in1(1'b1), .in2(1'b1), .in3(1'b1), .out(multiplexer_3_out[1]), .sel({in_8, in_7}));
  Multiplexer #(.select(2)) multiplexer_5 (
    .in0(1'b0), .in1(1'b0), .in2(1'b0), .in3(1'b1), .out(multiplexer_5_out), .sel(multiplexer_1_out));
  Multiplexer #(.select(2)) multiplexer_6 (
    .in0(1'b0), .in1(1'b1), .in2(1'b1), .in3(1'b1), .out(multiplexer_6_out), .sel(multiplexer_3_out));
endmodule

module comparerprekomux (
  input  x,
  input  y,
  input  biloXmanjeY,
  input  biloXveceY,
  input  biliJednaki,
  input  A,
  input  B,
  input  Jin,
  input  Min,
  input  Vin,
  output XmanjeY,
  output XveceY,
  output XjednakoY,
  output Mout,
  output Vout,
  output Jout
);

  wire and_1_out, and_2_out, and_3_out, and_4_out, multiplexer_1_out, multiplexer_2_out, multiplexer_3_out,
       multiplexer_4_out, multiplexer_5_out, not_1_out, not_2_out, not_3_out, not_4_out, not_5_out,
       not_6_out, xnor_1_out;

  not not_1 (not_1_out, y);
  not not_2 (not_2_out, x);
  not not_3 (not_3_out, A);
  and and_1 (and_1_out, not_3_out, B);
  and and_2 (and_2_out, A, not_4_out);
  not not_4 (not_4_out, B);
  Multiplexer multiplexer_1 (.in0(1'b0), .in1(x), .out(multiplexer_1_out), .sel(not_1_out));
  Multiplexer multiplexer_2 (.in0(1'b0), .in1(y), .out(multiplexer_2_out), .sel(not_2_out));
  not not_5 (not_5_out, multiplexer_3_out);
  Multiplexer multiplexer_3 (.in0(x), .in1(not_6_out), .out(multiplexer_3_out), .sel(y));
  not not_6 (not_6_out, x);
  and and_3 (and_3_out, and_1_out, Jin);
  and and_4 (and_4_out, and_2_out, Jin);
  xnor xnor_1 (xnor_1_out, A, B);
  and and_5 (Jout, xnor_1_out, Jin);
  or or_1 (Mout, and_3_out, Min);
  or or_2 (Vout, and_4_out, Vin);
  Multiplexer multiplexer_4 (.in0(1'b0), .in1(not_5_out), .out(multiplexer_4_out), .sel(biloXmanjeY));
  Multiplexer multiplexer_5 (.in0(1'b0), .in1(not_5_out), .out(multiplexer_5_out), .sel(biloXveceY));
  Multiplexer multiplexer_6 (.in0(1'b0), .in1(not_5_out), .out(XjednakoY), .sel(biliJednaki));
  or or_3 (XmanjeY, multiplexer_2_out, multiplexer_4_out);
  or or_4 (XveceY, multiplexer_1_out, multiplexer_5_out);

  // Notes on the sheet:
  //   <out=<in + =in.a'.b
  //   >out=>in + =in.a.b'
endmodule

module RSlatch (
  input  RESET,
  input  SET,
  output Q,
  output Qneg
);

  nor nor_1 (Q, RESET, Qneg);
  nor nor_2 (Qneg, Q, SET);
endmodule

module DFFprekoJKFF (
  input  D,
  input  clocc,
  input  J,
  input  K,
  input  cloc,
  input  M,
  output Q,
  output Qneg,
  output out_9,
  output out_10,
  output [2:0] out_11,
  output [2:0] out_12,
  output [2:0] out_13,
  output [2:0] out_14,
  output [2:0] out_15,
  output [4:0] out_16,
  output [4:0] out_17,
  output [2:0] out_18,
  output [2:0] out_19
);

  wire and_1_out, and_2_out, and_3_out, and_4_out, and_5_out, and_6_out, and_7_out, and_8_out, and_9_out,
       and_10_out, and_11_out, and_12_out, and_14_out, and_15_out, and_16_out, and_18_out, and_19_out,
       and_20_out, and_21_out, and_22_out, and_23_out, and_24_out, and_26_out, and_27_out, and_28_out,
       and_29_out, and_30_out, and_31_out, and_32_out, and_33_out, clock_1_out, clock_2_out, clock_3_out,
       clock_4_out, clock_5_out, clock_6_out, clock_7_out, clock_8_out, d_ff_1_q, d_ff_1_qn, d_ff_2_q,
       d_ff_2_qn, d_ff_3_q, d_ff_3_qn, j_k_ff_2_q, j_k_ff_2_qn, j_k_ff_3_q, j_k_ff_3_qn, j_k_ff_4_q,
       j_k_ff_4_qn, j_k_ff_5_qn, j_k_ff_6_qn, Mn, not_2_out, not_3_out, not_4_out, or_1_out, or_2_out,
       or_3_out, or_5_out, or_6_out, or_7_out, Q0n, Q1n, Q2n, T0, T1, T2, t_ff_1_qn, undriven, undriven_2,
       undriven_3, undriven_4, xnor_1_out, xor_1_out, xor_2_out, xor_3_out, xor_4_out, xor_5_out;

  Clock clock_1 (.out(clock_1_out));
  not not_1 (Mn, M);
  not not_2 (not_2_out, D);
  and and_1 (and_1_out, J, out_10);
  and and_2 (and_2_out, K, out_9);
  T_Flip_Flop t_ff_1 (
    .T(or_1_out), .clk(clock_1_out), .Q(out_13[2]), .Qn(t_ff_1_qn), .reset(undriven));  // open: preset
  or or_1 (or_1_out, out_13[2], and_3_out);
  and and_3 (and_3_out, out_13[0], out_13[1]);
  T_Flip_Flop t_ff_2 (
    .T(out_13[0]), .clk(clock_1_out), .Q(out_13[1]), .reset(undriven_2), .preset(undriven));  // open: Qn
  T_Flip_Flop t_ff_3 (.T(t_ff_1_qn), .clk(clock_1_out), .Q(out_13[0]), .preset(undriven_2));  // open: Qn, reset
  and and_4 (and_4_out, d_ff_1_q, d_ff_2_qn);
  and and_5 (and_5_out, d_ff_2_q, d_ff_3_q);
  and and_6 (and_6_out, j_k_ff_3_q, j_k_ff_2_q);
  and and_7 (and_7_out, out_18[1], out_18[0], Mn);
  xor xor_1 (xor_1_out, out_18[1], out_18[2]);
  T_Flip_Flop u_T2 (.T(T2), .clk(clock_2_out), .Q(out_18[2]), .Qn(Q2n));  // open: reset, preset
  Clock clock_2 (.out(clock_2_out));
  J_K_Flip_Flop j_k_ff_1 (.J(D), .K(not_2_out), .clk(clocc), .Q(Q), .Qn(Qneg));  // open: preset, reset
  T_Flip_Flop t_ff_4 (.T(or_2_out), .clk(cloc), .Q(out_9), .Qn(out_10));  // open: reset, preset
  or or_2 (or_2_out, and_1_out, and_2_out);
  D_Flip_Flop d_ff_1 (.D(or_3_out), .clk(clock_3_out), .Q(d_ff_1_q), .Qn(d_ff_1_qn));  // open: preset, reset
  or or_3 (or_3_out, and_4_out, and_5_out);
  Clock clock_3 (.out(clock_3_out));
  J_K_Flip_Flop j_k_ff_2 (
    .J(and_8_out), .K(and_6_out), .clk(clock_4_out), .Q(j_k_ff_2_q), .Qn(j_k_ff_2_qn));  // open: preset, reset
  and and_8 (and_8_out, j_k_ff_3_q, j_k_ff_4_q);
  Clock clock_4 (.out(clock_4_out));
  and and_9 (and_9_out, M, Q0n, xor_1_out);
  D_Flip_Flop d_ff_2 (.D(xor_2_out), .clk(clock_3_out), .Q(d_ff_2_q), .Qn(d_ff_2_qn));  // open: preset, reset
  or or_4 (T2, and_7_out, and_9_out);
  T_Flip_Flop u_T1 (.T(T1), .clk(clock_2_out), .Q(out_18[1]), .Qn(Q1n));  // open: reset, preset
  Clock clock_5 (.out(clock_5_out));
  and and_10 (and_10_out, d_ff_1_qn, d_ff_2_q);
  J_K_Flip_Flop j_k_ff_3 (
    .J(j_k_ff_4_q), .K(or_5_out), .clk(clock_4_out), .Q(j_k_ff_3_q), .Qn(j_k_ff_3_qn));  // open: preset, reset
  or or_5 (or_5_out, and_6_out, and_11_out);
  and and_11 (and_11_out, j_k_ff_3_q, j_k_ff_4_q);
  T_Flip_Flop u_T0 (.T(T0), .clk(clock_2_out), .Q(out_18[0]), .Qn(Q0n));  // open: reset, preset
  T_Flip_Flop t_ff_5 (.T(out_11[1]), .clk(clock_5_out), .Q(out_11[2]));  // open: Qn, reset, preset
  T_Flip_Flop t_ff_6 (.T(1'b1), .clk(clock_5_out), .Q(out_11[1]));  // open: Qn, reset, preset
  and and_12 (and_12_out, d_ff_1_q, d_ff_2_q);
  xor xor_2 (xor_2_out, and_10_out, d_ff_3_q);
  D_Flip_Flop d_ff_3 (.D(xor_3_out), .clk(clock_3_out), .Q(d_ff_3_q), .Qn(d_ff_3_qn));  // open: preset, reset
  or or_6 (or_6_out, Mn, xnor_1_out);
  xnor xnor_1 (xnor_1_out, out_18[2], out_18[1]);
  xor xor_3 (xor_3_out, and_12_out, d_ff_3_qn);
  J_K_Flip_Flop j_k_ff_4 (
    .J(or_7_out), .K(j_k_ff_4_q), .clk(clock_4_out), .Q(j_k_ff_4_q), .Qn(j_k_ff_4_qn));  // open: preset, reset
  or or_7 (or_7_out, j_k_ff_2_qn, j_k_ff_3_qn);
  and and_13 (T1, or_6_out, out_18[0]);
  Clock clock_6 (.out(clock_6_out));
  T_Flip_Flop t_ff_7 (.T(out_15[1]), .clk(clock_7_out), .Q(out_15[2]));  // open: Qn, reset, preset
  Clock clock_7 (.out(clock_7_out));
  and and_14 (and_14_out, d_ff_1_q, d_ff_2_qn, d_ff_3_qn);
  and and_15 (and_15_out, d_ff_1_qn, d_ff_2_qn, d_ff_3_q);
  and and_16 (and_16_out, out_14[2], out_14[1]);
  T_Flip_Flop t_ff_8 (.T(1'b1), .clk(clock_7_out), .Q(out_15[1]));  // open: Qn, reset, preset
  or or_8 (out_16[4], and_14_out, and_15_out);
  and and_17 (out_16[3], d_ff_1_q, d_ff_3_q);
  and and_18 (and_18_out, Q2n, not_3_out);
  not not_3 (not_3_out, xor_4_out);
  xor xor_4 (xor_4_out, out_18[1], out_18[0]);
  and and_19 (and_19_out, xor_4_out, out_18[2]);
  Clock clock_8 (.out(clock_8_out));
  J_K_Flip_Flop j_k_ff_5 (
    .J(and_20_out), .K(and_16_out), .clk(clock_6_out), .Q(out_14[2]), .Qn(j_k_ff_5_qn));  // open: preset, reset
  and and_20 (and_20_out, j_k_ff_5_qn, out_14[1]);
  J_K_Flip_Flop j_k_ff_6 (
    .J(j_k_ff_6_qn), .K(out_14[1]), .clk(clock_6_out), .Q(out_14[1]), .Qn(j_k_ff_6_qn));  // open: preset, reset
  and and_21 (and_21_out, d_ff_1_qn, d_ff_2_q);
  or or_9 (out_16[2], and_21_out, d_ff_3_q);
  and and_22 (and_22_out, j_k_ff_2_q, j_k_ff_3_qn, j_k_ff_4_qn);
  and and_23 (and_23_out, j_k_ff_2_qn, j_k_ff_3_qn, j_k_ff_4_q);
  or or_10 (T0, Mn, and_18_out, and_19_out);
  D_Flip_Flop d_ff_4 (.D(xor_5_out), .clk(clock_8_out), .Q(out_12[2]), .reset(undriven_3));  // open: Qn, preset
  D_Flip_Flop d_ff_5 (
    .D(not_4_out), .clk(clock_8_out), .Q(out_12[1]), .preset(undriven_3), .reset(undriven_4));  // open: Qn
  D_Flip_Flop d_ff_6 (.D(1'b0), .clk(clock_8_out), .Q(out_12[0]), .preset(undriven_4));  // open: Qn, reset
  and and_24 (and_24_out, d_ff_1_q, d_ff_2_q);
  or or_11 (out_17[4], and_22_out, and_23_out);
  and and_25 (out_17[3], j_k_ff_2_q, j_k_ff_4_q);
  not not_4 (not_4_out, out_12[1]);
  or or_12 (out_16[1], and_24_out, and_26_out);
  and and_26 (and_26_out, d_ff_2_q, d_ff_3_q);
  and and_27 (and_27_out, j_k_ff_2_qn, j_k_ff_3_q);
  or or_13 (out_17[2], and_27_out, j_k_ff_4_q);
  xor xor_5 (xor_5_out, out_12[2], out_12[1]);
  and and_28 (and_28_out, d_ff_2_qn, d_ff_3_qn);
  and and_29 (and_29_out, j_k_ff_2_q, j_k_ff_3_q);
  or or_14 (out_16[0], and_28_out, and_30_out);
  and and_30 (and_30_out, d_ff_1_qn, d_ff_2_q);
  or or_15 (out_17[1], and_29_out, and_31_out);
  and and_31 (and_31_out, j_k_ff_3_q, j_k_ff_4_q);
  and and_32 (and_32_out, j_k_ff_3_qn, j_k_ff_4_qn);
  and and_33 (and_33_out, j_k_ff_2_qn, j_k_ff_3_q);
  or or_16 (out_17[0], and_32_out, and_33_out);

  assign out_11[0] = 1'b0;
  assign out_14[0] = 1'b0;
  assign out_15[0] = 1'b0;
  assign out_19 = out_18;

  // Other names for the same wires on the sheet: Q0 = out_18[0]; Q1 = out_18[1]; Q2 = out_18[2]
endmodule

module T7Z9 (
  input  in_1,
  output [2:0] out_2,
  output T,
  output K,
  output D
);

  wire d_ff_1_qn, j_k_ff_1_qn, nand_1_out, xnor_1_out, xor_1_out;

  xor xor_1 (xor_1_out, out_2[1], out_2[2]);
  T_Flip_Flop t_ff_1 (.T(T), .clk(in_1), .Q(out_2[2]));  // open: Qn, reset, preset
  and and_1 (T, d_ff_1_qn, xor_1_out);
  and and_2 (K, out_2[2], out_2[1]);
  nand nand_1 (nand_1_out, out_2[2], j_k_ff_1_qn, d_ff_1_qn);
  J_K_Flip_Flop j_k_ff_1 (.J(nand_1_out), .K(K), .clk(in_1), .Q(out_2[1]), .Qn(j_k_ff_1_qn));  // open: preset, reset
  xnor xnor_1 (xnor_1_out, out_2[2], out_2[0]);
  D_Flip_Flop d_ff_1 (.D(D), .clk(in_1), .Q(out_2[0]), .Qn(d_ff_1_qn));  // open: preset, reset
  and and_3 (D, xnor_1_out, out_2[1]);
endmodule

module T7Z7 (
  input  [2:0] X,
  input  ulaz,
  input  kloc,
  output [1:0] out_4,
  output [2:0] out_5
);

  wire and_1_out, and_2_out, and_3_out, and_4_out, and_5_out, buffer_1_out, buffer_2_out, buffer_3_out,
       buffer_4_out, buffer_5_out, buffer_6_out, buffer_7_out, buffer_8_out, buffer_9_out, buffer_10_out,
       buffer_11_out, buffer_12_out, buffer_13_out, buffer_14_out, buffer_15_out, buffer_16_out,
       buffer_17_out, buffer_18_out, buffer_19_out, buffer_20_out, buffer_21_out, buffer_22_out,
       buffer_23_out, buffer_24_out, buffer_25_out, buffer_26_out, buffer_27_out, buffer_28_out,
       buffer_29_out, buffer_30_out, buffer_31_out, buffer_32_out, buffer_33_out, buffer_34_out,
       buffer_35_out, buffer_36_out, buffer_37_out, buffer_38_out, buffer_39_out, buffer_40_out,
       buffer_41_out, buffer_42_out, buffer_43_out, buffer_44_out, buffer_45_out, buffer_46_out,
       buffer_47_out, buffer_48_out, buffer_49_out, d_ff_1_qn, d_ff_2_qn, d_ff_8_qn, demultiplexer_1_out0,
       demultiplexer_1_out1, demultiplexer_1_out2, demultiplexer_2_out0, demultiplexer_2_out1,
       demultiplexer_2_out2, nor_1_out, not_1_out, not_2_out, not_3_out, or_1_out, or_2_out, or_3_out,
       xor_2_out, xor_3_out;
  wire [2:0] d_ff_5_q, xor_1_out;

  buf buffer_1 (buffer_1_out, buffer_10_out);
  buf buffer_2 (buffer_2_out, buffer_1_out);
  D_Flip_Flop d_ff_1 (.D(out_4[0]), .clk(kloc), .Q(out_4[1]), .Qn(d_ff_1_qn));  // open: preset, reset
  buf buffer_3 (buffer_3_out, kloc);
  buf buffer_4 (buffer_4_out, buffer_3_out);
  buf buffer_5 (buffer_5_out, buffer_4_out);
  buf buffer_6 (buffer_6_out, buffer_5_out);
  buf buffer_7 (buffer_7_out, buffer_6_out);
  buf buffer_8 (buffer_8_out, buffer_7_out);
  Demultiplexer #(.select(2)) demultiplexer_1 (
    .out0(demultiplexer_1_out0), .out1(demultiplexer_1_out1), .out2(demultiplexer_1_out2), .in(ulaz),
    .sel(out_4));  // open: out3
  buf buffer_9 (buffer_9_out, buffer_8_out);
  buf buffer_10 (buffer_10_out, buffer_11_out);
  buf buffer_11 (buffer_11_out, buffer_9_out);
  buf buffer_12 (buffer_12_out, buffer_2_out);
  buf buffer_13 (buffer_13_out, buffer_12_out);
  buf buffer_14 (buffer_14_out, buffer_13_out);
  Demultiplexer #(.select(2)) demultiplexer_2 (
    .out0(demultiplexer_2_out0), .out1(demultiplexer_2_out1), .out2(demultiplexer_2_out2),
    .in(buffer_14_out), .sel(out_4));  // open: out3
  buf buffer_15 (buffer_15_out, out_4[1]);
  buf buffer_16 (buffer_16_out, buffer_15_out);
  buf buffer_17 (buffer_17_out, buffer_16_out);
  and and_1 (and_1_out, d_ff_1_qn, d_ff_2_qn);
  not not_1 (not_1_out, out_4[1]);
  buf buffer_18 (buffer_18_out, not_1_out);
  buf buffer_19 (buffer_19_out, buffer_17_out);
  buf buffer_20 (buffer_20_out, buffer_19_out);
  buf buffer_21 (buffer_21_out, buffer_20_out);
  buf buffer_22 (buffer_22_out, buffer_21_out);
  D_Flip_Flop d_ff_2 (.D(and_1_out), .clk(kloc), .Q(out_4[0]), .Qn(d_ff_2_qn));  // open: preset, reset
  or or_1 (or_1_out, demultiplexer_1_out2, d_ff_5_q[2]);
  D_Flip_Flop d_ff_3 (
    .D(or_1_out), .clk(demultiplexer_2_out2), .Q(d_ff_5_q[2]), .reset(and_2_out));  // open: Qn, preset
  buf buffer_23 (buffer_23_out, buffer_18_out);
  not not_2 (not_2_out, buffer_23_out);
  buf buffer_24 (buffer_24_out, not_2_out);
  buf buffer_25 (buffer_25_out, buffer_24_out);
  buf buffer_26 (buffer_26_out, buffer_22_out);
  buf buffer_27 (buffer_27_out, buffer_26_out);
  buf buffer_28 (buffer_28_out, buffer_27_out);
  buf buffer_29 (buffer_29_out, buffer_28_out);
  or or_2 (or_2_out, demultiplexer_1_out1, d_ff_5_q[1]);
  D_Flip_Flop d_ff_4 (
    .D(or_2_out), .clk(demultiplexer_2_out1), .Q(d_ff_5_q[1]), .reset(and_2_out));  // open: Qn, preset
  and and_2 (and_2_out, not_1_out, buffer_30_out);
  buf buffer_30 (buffer_30_out, buffer_25_out);
  buf buffer_31 (buffer_31_out, buffer_29_out);
  buf buffer_32 (buffer_32_out, buffer_31_out);
  buf buffer_33 (buffer_33_out, buffer_32_out);
  buf buffer_34 (buffer_34_out, buffer_33_out);
  buf buffer_35 (buffer_35_out, buffer_34_out);
  buf buffer_36 (buffer_36_out, buffer_35_out);
  buf buffer_37 (buffer_37_out, buffer_36_out);
  buf buffer_38 (buffer_38_out, buffer_37_out);
  or or_3 (or_3_out, demultiplexer_1_out0, d_ff_5_q[0]);
  D_Flip_Flop d_ff_5 (
    .D(or_3_out), .clk(demultiplexer_2_out0), .Q(d_ff_5_q[0]), .reset(and_2_out));  // open: Qn, preset
  not not_3 (not_3_out, buffer_38_out);
  buf buffer_39 (buffer_39_out, not_3_out);
  buf buffer_40 (buffer_40_out, buffer_39_out);
  buf buffer_41 (buffer_41_out, buffer_40_out);
  and and_3 (and_3_out, buffer_36_out, buffer_41_out);
  buf buffer_42 (buffer_42_out, and_3_out);
  buf buffer_43 (buffer_43_out, buffer_42_out);
  buf buffer_44 (buffer_44_out, buffer_43_out);
  buf buffer_45 (buffer_45_out, buffer_44_out);
  buf buffer_46 (buffer_46_out, buffer_45_out);
  buf buffer_47 (buffer_47_out, buffer_46_out);
  assign xor_1_out = d_ff_5_q ^ X;  // XOR_Gate xor_1, 3 bits wide
  xor xor_2 (xor_2_out, and_5_out, out_5[2]);
  D_Flip_Flop d_ff_6 (.D(xor_2_out), .clk(and_4_out), .Q(out_5[2]));  // open: Qn, preset, reset
  buf buffer_48 (buffer_48_out, buffer_47_out);
  buf buffer_49 (buffer_49_out, buffer_48_out);
  and and_4 (and_4_out, buffer_49_out, nor_1_out);
  nor nor_1 (nor_1_out, xor_1_out[2], xor_1_out[1], xor_1_out[0]);
  and and_5 (and_5_out, out_5[0], out_5[1]);
  xor xor_3 (xor_3_out, out_5[1], out_5[0]);
  D_Flip_Flop d_ff_7 (.D(xor_3_out), .clk(and_4_out), .Q(out_5[1]));  // open: Qn, preset, reset
  D_Flip_Flop d_ff_8 (.D(d_ff_8_qn), .clk(and_4_out), .Q(out_5[0]), .Qn(d_ff_8_qn));  // open: preset, reset
endmodule

module T7Z8 (
  input  ulaz
);

  wire and_1_out, and_2_out, and_3_out, and_4_out, and_5_out, and_6_out, and_7_out, and_8_out, clock_1_out,
       d_ff_1_q, d_ff_2_q, d_ff_3_q, d_ff_3_qn, d_ff_4_q, d_ff_5_q, d_ff_5_qn, d_ff_6_q, d_ff_7_q, d_ff_8_q,
       d_ff_9_q, d_ff_10_q, d_ff_10_qn, d_ff_11_q, d_ff_12_q, d_ff_12_qn, or_1_out, xor_1_out, xor_2_out,
       xor_3_out, xor_4_out;

  Clock clock_1 (.out(clock_1_out));
  D_Flip_Flop d_ff_1 (.D(ulaz), .clk(clock_1_out), .Q(d_ff_1_q));  // open: Qn, preset, reset
  D_Flip_Flop d_ff_2 (.D(d_ff_1_q), .clk(clock_1_out), .Q(d_ff_2_q));  // open: Qn, preset, reset
  D_Flip_Flop d_ff_3 (.D(xor_1_out), .clk(clock_1_out), .Q(d_ff_3_q), .Qn(d_ff_3_qn));  // open: preset, reset
  xor xor_1 (xor_1_out, d_ff_3_q, d_ff_5_q);
  D_Flip_Flop d_ff_4 (.D(d_ff_2_q), .clk(clock_1_out), .Q(d_ff_4_q));  // open: Qn, preset, reset
  D_Flip_Flop d_ff_5 (.D(d_ff_5_qn), .clk(clock_1_out), .Q(d_ff_5_q), .Qn(d_ff_5_qn));  // open: preset, reset
  D_Flip_Flop d_ff_6 (.D(d_ff_4_q), .clk(clock_1_out), .Q(d_ff_6_q));  // open: Qn, preset, reset
  and and_1 (and_1_out, d_ff_3_qn, d_ff_5_q);
  and and_2 (and_2_out, d_ff_2_q, d_ff_4_q, d_ff_6_q);
  and and_3 (and_3_out, d_ff_3_qn, d_ff_5_qn);
  and and_4 (and_4_out, and_3_out, ~and_5_out);  // AND_Gate
  D_Flip_Flop #(.trigger("falling")) d_ff_7 (
    .D(and_4_out), .clk(clock_1_out), .Q(d_ff_7_q), .reset(and_1_out));  // open: Qn, preset
  or or_1 (or_1_out, d_ff_1_q, and_2_out);
  and and_5 (and_5_out, and_3_out, or_1_out);
  and and_6 (and_6_out, d_ff_11_q, d_ff_12_q);
  D_Flip_Flop d_ff_8 (.D(xor_2_out), .clk(and_8_out), .Q(d_ff_8_q));  // open: Qn, preset, reset
  xor xor_2 (xor_2_out, d_ff_8_q, and_6_out);
  D_Flip_Flop d_ff_9 (.D(xor_3_out), .clk(and_7_out), .Q(d_ff_9_q), .reset(d_ff_7_q));  // open: Qn, preset
  xor xor_3 (xor_3_out, d_ff_9_q, d_ff_10_q);
  and and_7 (and_7_out, ~and_8_out, and_5_out);  // AND_Gate
  xor xor_4 (xor_4_out, d_ff_11_q, d_ff_12_q);
  and and_8 (and_8_out, d_ff_9_q, ~d_ff_10_q);  // AND_Gate
  D_Flip_Flop d_ff_10 (
    .D(d_ff_10_qn), .clk(and_7_out), .Q(d_ff_10_q), .Qn(d_ff_10_qn), .reset(d_ff_7_q));  // open: preset
  D_Flip_Flop d_ff_11 (.D(xor_4_out), .clk(and_8_out), .Q(d_ff_11_q));  // open: Qn, preset, reset
  D_Flip_Flop d_ff_12 (.D(d_ff_12_qn), .clk(and_8_out), .Q(d_ff_12_q), .Qn(d_ff_12_qn));  // open: preset, reset

  // Notes on the sheet:
  //   registar sa serijskim ulazom
  //   okida se kada se unese 4. bit
  //   FF za reset zbog sinhronizacije
  //   prepoznaje 1xxx i 0111
  //   brojac uzastopnih koji stane nakon 2
  //   brojac uzastopnih sekvenci
endmodule

module Z7v2 (
  input  [2:0] X,
  input  ulaz,
  output out_3,
  output [2:0] out_4
);

  wire and_1_out, buffer_1_out, buffer_2_out, buffer_3_out, buffer_4_out, clock_1_out, d_ff_4_q, nor_1_out,
       not_1_out, t_ff_1_q, t_ff_2_q, undriven;
  wire [2:0] d_ff_3_q, xor_1_out;

  Clock clock_1 (.out(clock_1_out));
  D_Flip_Flop d_ff_1 (.D(ulaz), .clk(clock_1_out), .Q(d_ff_3_q[2]), .reset(d_ff_4_q));  // open: Qn, preset
  D_Flip_Flop d_ff_2 (.D(d_ff_3_q[2]), .clk(clock_1_out), .Q(d_ff_3_q[1]), .reset(d_ff_4_q));  // open: Qn, preset
  D_Flip_Flop d_ff_3 (.D(d_ff_3_q[1]), .clk(clock_1_out), .Q(d_ff_3_q[0]), .reset(d_ff_4_q));  // open: Qn, preset
  assign xor_1_out = X ^ d_ff_3_q;  // XOR_Gate xor_1, 3 bits wide
  nor nor_1 (nor_1_out, xor_1_out[0], xor_1_out[1], xor_1_out[2]);
  T_Flip_Flop t_ff_1 (.T(1'b1), .clk(nor_1_out), .Q(t_ff_1_q), .Qn(out_4[0]));  // open: reset, preset
  T_Flip_Flop t_ff_2 (.T(1'b1), .clk(t_ff_1_q), .Q(t_ff_2_q), .Qn(out_4[1]));  // open: reset, preset
  T_Flip_Flop t_ff_3 (.T(1'b1), .clk(t_ff_2_q), .Qn(out_4[2]));  // open: Q, reset, preset
  buf buffer_1 (buffer_1_out, undriven);
  buf buffer_2 (buffer_2_out, buffer_1_out);
  D_Flip_Flop d_ff_4 (.D(nor_1_out), .clk(nor_1_out), .Q(d_ff_4_q), .reset(d_ff_4_q));  // open: Qn, preset
  and and_1 (and_1_out, undriven, not_1_out);
  not not_1 (not_1_out, buffer_4_out);
  buf buffer_3 (buffer_3_out, buffer_2_out);
  buf buffer_4 (buffer_4_out, buffer_3_out);
  D_Flip_Flop d_ff_5 (.D(d_ff_4_q), .clk(d_ff_4_q), .Q(out_3), .reset(and_1_out));  // open: Qn, preset
endmodule

module ispitni (
  input  [5:0] in_1,
  output [5:0] out_2,
  output [5:0] out_3
);

  wire ha_1_xplusy, ha_2_xplusy, ha_3_xplusy, ha_4_xplusy, ha_5_xplusy;
  wire [5:0] ha_1_carryu, not_1_out;

  assign not_1_out = ~in_1;  // NOT_Gate not_1, 6 bits wide
  Multiplexer #(.width(6)) multiplexer_1 (.in0(in_1), .in1(ha_1_carryu), .out(out_2), .sel(in_1[5]));
  HA ha_1 (.X(not_1_out[0]), .Y(1'b1), .XplusY(ha_1_xplusy), .carryu(ha_1_carryu[0]));
  HA ha_2 (.X(not_1_out[1]), .Y(ha_1_xplusy), .XplusY(ha_2_xplusy), .carryu(ha_1_carryu[1]));
  HA ha_3 (.X(not_1_out[2]), .Y(ha_2_xplusy), .XplusY(ha_3_xplusy), .carryu(ha_1_carryu[2]));
  HA ha_4 (.X(not_1_out[3]), .Y(ha_3_xplusy), .XplusY(ha_4_xplusy), .carryu(ha_1_carryu[3]));
  HA ha_5 (.X(not_1_out[4]), .Y(ha_4_xplusy), .XplusY(ha_5_xplusy), .carryu(ha_1_carryu[4]));
  HA ha_6 (.X(not_1_out[5]), .Y(ha_5_xplusy), .carryu(ha_1_carryu[5]));  // open: XplusY

  assign out_3 = in_1;
endmodule

module ispitni2 (
  input  [3:0] in_1,
  input  [3:0] x,
  input  reset,
  input  [3:0] in_4,
  input  [3:0] iks,
  input  reset2,
  input  [3:0] ipsilon,
  input  [3:0] iks1,
  input  reset3,
  input  [3:0] ipsilon1,
  input  in_11,
  input  [3:0] in_12,
  input  [3:0] in_13,
  input  in_14,
  input  [3:0] in_15,
  input  in_16,
  input  [3:0] in_17,
  input  in_18,
  output [3:0] out_19,
  output [3:0] out_20,
  output [3:0] out_21,
  output [3:0] out_22,
  output [3:0] out_23,
  output [3:0] out_24,
  output [3:0] out_25,
  output [3:0] out_26,
  output [3:0] out_27,
  output [3:0] out_28,
  output [3:0] out_29,
  output [3:0] out_30,
  output XmanjeYk,
  output XveceYk,
  output [3:0] out_33,
  output [3:0] out_34,
  output jednaki,
  output [3:0] out_36,
  output [3:0] out_37,
  output [3:0] out_38,
  output [3:0] out_39,
  output [3:0] out_40,
  output [3:0] out_41,
  output XmanjeY2,
  output XveceY2,
  output [3:0] out_44,
  output [3:0] out_45,
  output XjednakoY
);

  wire and_1_out, and_2_out, and_3_out, and_4_out, and_5_out, and_6_out, and_7_out, and_8_out, and_9_out,
       and_10_out, carry2_q, carry_q, clock_1_out, clock_2_out, clock_3_out, d_ff_1_q, d_ff_2_q,
       fulladder_1_out1, fulladder_1_outcarry, ha_1_carryu, ha_1_xplusy, ha_2_carryu, ha_2_xplusy, isneg_q,
       kloc3_out, klok_out, klokeroni_out, multiplexer_1_out, multiplexer_2_out, not_1_out, not_2_out,
       not_3_out, onebitcompare_1_xmanjey, onebitcompare_1_xvecey, onebitcompare_2_xmanjey,
       onebitcompare_2_xvecey, or_1_out, or_2_out, procitanPrvi_q, sreg_1_serout, sreg_2_serout,
       sreg_3_serout, sreg_4_serout, sregunazad_1_serout, sregunazad_2_serout, sregunazad_3_serout,
       sregunazad_4_serout;

  Clock klok (.out(klok_out));
  Clock klokeroni (.out(klokeroni_out));
  Clock kloc3 (.out(kloc3_out));
  Clock clock_1 (.out(clock_1_out));
  Clock clock_2 (.out(clock_2_out));
  D_Flip_Flop procitanPrvi (.D(1'b1), .clk(clock_2_out), .Q(procitanPrvi_q), .reset(in_16));  // open: Qn, preset
  not not_1 (not_1_out, sreg_1_serout);
  SREG sreg_1 (.X(x), .Clock(klok_out), .ParIn(reset), .SerOut(sreg_1_serout), .ParOut(out_20));  // open: SerIn
  SREG sreg_2 (.X(iks), .Clock(klokeroni_out), .ParIn(reset2), .SerOut(sreg_2_serout), .ParOut(out_23));  // open: SerIn
  SREG sreg_3 (
    .X(ipsilon), .Clock(klokeroni_out), .ParIn(reset2), .SerOut(sreg_3_serout), .ParOut(out_25));  // open: SerIn
  SREGunazad sregunazad_1 (
    .X(iks1), .Clock(kloc3_out), .ParIn(reset3), .SerOut(sregunazad_1_serout), .ParOut(out_29));  // open: SerIn
  SREGunazad sregunazad_2 (
    .X(ipsilon1), .Clock(kloc3_out), .ParIn(reset3), .SerOut(sregunazad_2_serout), .ParOut(out_33));  // open: SerIn
  not not_2 (not_2_out, sreg_4_serout);
  SREG sreg_4 (.X(in_13), .Clock(clock_1_out), .ParIn(in_14), .SerOut(sreg_4_serout), .ParOut(out_37));  // open: SerIn
  SREGunazad sregunazad_3 (
    .X(in_15), .Clock(clock_2_out), .ParIn(in_16), .SerOut(sregunazad_3_serout), .ParOut(out_40));  // open: SerIn
  SREGunazad sregunazad_4 (
    .X(in_17), .Clock(clock_2_out), .ParIn(in_16), .SerOut(sregunazad_4_serout), .ParOut(out_44));  // open: SerIn
  Multiplexer multiplexer_1 (.in0(sreg_1_serout), .in1(not_1_out), .out(multiplexer_1_out), .sel(isneg_q));
  D_Flip_Flop isneg (.D(1'b1), .clk(out_20[3]), .Q(isneg_q));  // open: Qn, preset, reset
  Multiplexer multiplexer_2 (.in0(sreg_4_serout), .in1(not_2_out), .out(multiplexer_2_out), .sel(not_3_out));
  D_Flip_Flop d_ff_1 (.D(1'b1), .clk(out_37[3]), .Q(d_ff_1_q));  // open: Qn, preset, reset
  and and_1 (and_1_out, ~out_40[3], out_44[3], ~procitanPrvi_q);  // AND_Gate
  D_Flip_Flop carry (.D(ha_1_carryu), .clk(klok_out), .Q(carry_q), .preset(reset));  // open: Qn, reset
  D_Flip_Flop carry2 (.D(fulladder_1_outcarry), .clk(klokeroni_out), .Q(carry2_q), .reset(reset2));  // open: Qn, preset
  not not_3 (not_3_out, d_ff_1_q);
  D_Flip_Flop d_ff_2 (.D(ha_2_carryu), .clk(clock_1_out), .Q(d_ff_2_q), .preset(in_14));  // open: Qn, reset
  and and_2 (and_2_out, sregunazad_3_serout, procitanPrvi_q);
  and and_3 (and_3_out, sregunazad_4_serout, procitanPrvi_q);
  and and_4 (and_4_out, out_40[3], ~out_44[3], ~procitanPrvi_q);  // AND_Gate
  and and_5 (and_5_out, isneg_q, carry_q);
  fulladder fulladder_1 (
    .incarry(carry2_q), .in1(sreg_2_serout), .in2(sreg_3_serout), .outcarry(fulladder_1_outcarry),
    .out1(fulladder_1_out1));
  onebitcompare onebitcompare_1 (
    .x(sregunazad_1_serout), .y(sregunazad_2_serout), .XmanjeY(onebitcompare_1_xmanjey),
    .XveceY(onebitcompare_1_xvecey));  // open: jednaki
  and and_6 (and_6_out, not_3_out, d_ff_2_q);
  Clock clock_3 (.out(clock_3_out));
  D_Flip_Flop XmanjeY (.D(1'b1), .clk(and_7_out), .Q(XmanjeYk), .reset(in_11));  // open: Qn, preset
  and and_7 (and_7_out, onebitcompare_1_xmanjey, ~XveceYk);  // AND_Gate
  D_Flip_Flop XveceY (.D(1'b1), .clk(and_8_out), .Q(XveceYk), .reset(in_11));  // open: Qn, preset
  and and_8 (and_8_out, onebitcompare_1_xvecey, ~XmanjeYk);  // AND_Gate
  onebitcompare onebitcompare_2 (
    .x(and_2_out), .y(and_3_out), .XmanjeY(onebitcompare_2_xmanjey), .XveceY(onebitcompare_2_xvecey));  // open: jednaki
  HA ha_1 (.X(multiplexer_1_out), .Y(and_5_out), .XplusY(ha_1_xplusy), .carryu(ha_1_carryu));
  SREG sreg_5 (
    .X(in_4), .SerIn(fulladder_1_out1), .Clock(clock_3_out), .ParIn(reset2), .ParOut(out_27));  // open: SerOut
  HA ha_2 (.X(multiplexer_2_out), .Y(and_6_out), .XplusY(ha_2_xplusy), .carryu(ha_2_carryu));
  D_Flip_Flop d_ff_3 (.D(1'b1), .clk(and_9_out), .Q(XmanjeY2), .reset(in_18));  // open: Qn, preset
  or or_1 (or_1_out, onebitcompare_2_xmanjey, and_4_out);
  and and_9 (and_9_out, or_1_out, ~XveceY2);  // AND_Gate
  D_Flip_Flop d_ff_4 (.D(1'b1), .clk(and_10_out), .Q(XveceY2), .reset(in_18));  // open: Qn, preset
  or or_2 (or_2_out, onebitcompare_2_xvecey, and_1_out);
  and and_10 (and_10_out, or_2_out, ~XmanjeY2);  // AND_Gate
  xnor xnor_1 (jednaki, XmanjeYk, XveceYk);
  SREG sreg_6 (.X(in_1), .SerIn(ha_1_xplusy), .Clock(klok_out), .ParIn(ha_1_carryu), .ParOut(out_19));  // open: SerOut
  SREG sreg_7 (
    .X(in_12), .SerIn(ha_2_xplusy), .Clock(clock_1_out), .ParIn(ha_2_carryu), .ParOut(out_36));  // open: SerOut
  xnor xnor_2 (XjednakoY, XmanjeY2, XveceY2);

  assign out_21 = out_19;
  assign out_22 = out_20;
  assign out_24 = out_23;
  assign out_26 = out_25;
  assign out_28 = out_27;
  assign out_30 = out_29;
  assign out_34 = out_33;
  assign out_38 = out_36;
  assign out_39 = out_37;
  assign out_41 = out_40;
  assign out_45 = out_44;
endmodule

module SREG (
  input  [3:0] X,
  input  SerIn,
  input  Clock,
  input  ParIn,
  output SerOut,
  output [3:0] ParOut
);

  wire multiplexer_1_out, multiplexer_2_out, multiplexer_3_out, multiplexer_4_out, not_1_out;

  not not_1 (not_1_out, ParIn);
  D_Flip_Flop d_ff_1 (.D(multiplexer_1_out), .clk(Clock), .Q(ParOut[3]));  // open: Qn, preset, reset
  Multiplexer multiplexer_1 (.in0(X[3]), .in1(SerIn), .out(multiplexer_1_out), .sel(not_1_out));
  D_Flip_Flop d_ff_2 (.D(multiplexer_2_out), .clk(Clock), .Q(ParOut[2]));  // open: Qn, preset, reset
  Multiplexer multiplexer_2 (.in0(X[2]), .in1(ParOut[3]), .out(multiplexer_2_out), .sel(not_1_out));
  Multiplexer multiplexer_3 (.in0(X[1]), .in1(ParOut[2]), .out(multiplexer_3_out), .sel(not_1_out));
  D_Flip_Flop d_ff_3 (.D(multiplexer_3_out), .clk(Clock), .Q(ParOut[1]));  // open: Qn, preset, reset
  D_Flip_Flop d_ff_4 (.D(multiplexer_4_out), .clk(Clock), .Q(ParOut[0]));  // open: Qn, preset, reset
  Multiplexer multiplexer_4 (.in0(X[0]), .in1(ParOut[1]), .out(multiplexer_4_out), .sel(not_1_out));

  assign SerOut = ParOut[0];
endmodule

module onebitcompare (
  input  x,
  input  y,
  output XmanjeY,
  output XveceY,
  output jednaki
);

  and and_1 (XmanjeY, ~x, y);  // AND_Gate
  and and_2 (XveceY, x, ~y);  // AND_Gate
  xnor xnor_1 (jednaki, x, y);
endmodule

module SREGunazad (
  input  [3:0] X,
  input  SerIn,
  input  Clock,
  input  ParIn,
  output SerOut,
  output [3:0] ParOut
);

  wire multiplexer_1_out, multiplexer_2_out, multiplexer_3_out, multiplexer_4_out, not_1_out;

  not not_1 (not_1_out, ParIn);
  D_Flip_Flop d_ff_1 (.D(multiplexer_1_out), .clk(Clock), .Q(ParOut[3]));  // open: Qn, preset, reset
  Multiplexer multiplexer_1 (.in0(X[3]), .in1(ParOut[2]), .out(multiplexer_1_out), .sel(not_1_out));
  D_Flip_Flop d_ff_2 (.D(multiplexer_2_out), .clk(Clock), .Q(ParOut[2]));  // open: Qn, preset, reset
  Multiplexer multiplexer_2 (.in0(X[2]), .in1(ParOut[1]), .out(multiplexer_2_out), .sel(not_1_out));
  Multiplexer multiplexer_3 (.in0(X[1]), .in1(ParOut[0]), .out(multiplexer_3_out), .sel(not_1_out));
  D_Flip_Flop d_ff_3 (.D(multiplexer_3_out), .clk(Clock), .Q(ParOut[1]));  // open: Qn, preset, reset
  D_Flip_Flop d_ff_4 (.D(multiplexer_4_out), .clk(Clock), .Q(ParOut[0]));  // open: Qn, preset, reset
  Multiplexer multiplexer_4 (.in0(X[0]), .in1(SerIn), .out(multiplexer_4_out), .sel(not_1_out));

  assign SerOut = ParOut[3];
endmodule

module ispitni3 (
  input  [3:0] in_1,
  input  N,
  input  M,
  output [3:0] vrijednost,
  output [3:0] out_5,
  output [3:0] out_6,
  output znak
);

  wire [3:0] fourbitaddernand_1_xplusy, fourbitaddernand_2_xplusy, multiplexer_1_out, not_1_out, not_2_out;

  assign not_1_out = ~in_1;  // NOT_Gate not_1, 4 bits wide
  assign not_2_out = ~multiplexer_1_out;  // NOT_Gate not_2, 4 bits wide
  Multiplexer #(.width(4)) multiplexer_1 (
    .in0(in_1), .in1(fourbitaddernand_1_xplusy), .out(multiplexer_1_out), .sel(in_1[3]));
  fourbitadderNAND fourbitaddernand_1 (
    .x(not_1_out), .y(4'b0001), .xPlusy(fourbitaddernand_1_xplusy));  // open: overflow
  fourbitadderNAND fourbitaddernand_2 (
    .x(not_2_out), .y(4'b0001), .xPlusy(fourbitaddernand_2_xplusy));  // open: overflow
  Multiplexer #(.select(2), .width(4)) multiplexer_2 (
    .in0(multiplexer_1_out), .in1(fourbitaddernand_2_xplusy), .in2(multiplexer_1_out),
    .in3(fourbitaddernand_2_xplusy), .out(out_6), .sel({M, N}));
  Multiplexer multiplexer_3 (.in0(1'b0), .in1(N), .out(znak), .sel(M));

  assign out_5 = in_1;
  assign vrijednost = out_6;
endmodule

module ispitni4 (
  input  ulaz,
  input  in_2,
  output [2:0] out_3,
  output [1:0] out_4,
  output [2:0] out_5,
  output [3:0] neparni,
  output [3:0] parni,
  output out_8,
  output [1:0] out_9
);

  wire and_1_out, and_2_out, and_3_out, and_4_out, and_5_out, and_6_out, and_7_out, and_8_out, and_9_out,
       and_10_out, and_11_out, and_12_out, and_13_out, and_14_out, and_15_out, and_16_out, and_17_out,
       and_18_out, and_19_out, and_20_out, clock_1_out, clock_2_out, clock_3_out, clock_4_out, clock_5_out,
       clock_6_out, clock_7_out, d_ff_1_q, d_ff_3_q, s0_out, s1_out, t_ff_1_q, t_ff_2_q, t_ff_3_q, t_ff_4_q,
       t_ff_5_q, t_ff_6_q, t_ff_7_qn, t_ff_8_q, t_ff_9_q, t_ff_10_q, t_ff_11_q, t_ff_14_qn, t_ff_15_qn,
       xor_1_out, xor_2_out, xor_3_out, xor_4_out, xor_5_out, xor_6_out, xor_7_out;

  Clock clock_1 (.out(clock_1_out));
  Clock clock_2 (.out(clock_2_out));
  D_Flip_Flop d_ff_1 (.D(ulaz), .clk(clock_1_out), .Q(d_ff_1_q));  // open: Qn, preset, reset
  T_Flip_Flop t_ff_1 (.T(1'b1), .clk(clock_3_out), .Q(t_ff_1_q), .Qn(out_4[0]), .preset(and_3_out));  // open: reset
  Clock clock_3 (.out(clock_3_out));
  D_Flip_Flop d_ff_2 (.D(in_2), .clk(clock_2_out), .Q(out_5[2]));  // open: Qn, preset, reset
  T_Flip_Flop t_ff_2 (.T(1'b1), .clk(clock_4_out), .Q(t_ff_2_q), .Qn(out_9[0]), .preset(and_4_out));  // open: reset
  Clock clock_4 (.out(clock_4_out));
  D_Flip_Flop d_ff_3 (.D(d_ff_1_q), .clk(clock_1_out), .Q(d_ff_3_q));  // open: Qn, preset, reset
  and and_1 (and_1_out, t_ff_1_q, ~t_ff_3_q);  // AND_Gate
  T_Flip_Flop t_ff_3 (.T(1'b1), .clk(t_ff_1_q), .Q(t_ff_3_q), .Qn(out_4[1]), .preset(and_3_out));  // open: reset
  D_Flip_Flop d_ff_4 (.D(out_5[2]), .clk(clock_2_out), .Q(out_5[1]));  // open: Qn, preset, reset
  and and_2 (and_2_out, t_ff_2_q, ~t_ff_4_q);  // AND_Gate
  T_Flip_Flop t_ff_4 (.T(1'b1), .clk(t_ff_2_q), .Q(t_ff_4_q), .Qn(out_9[1]), .preset(and_4_out));  // open: reset
  D_Flip_Flop d_ff_5 (.D(d_ff_3_q), .clk(clock_1_out));  // open: Q, Qn, preset, reset
  and and_3 (and_3_out, out_4[1], out_4[0]);
  D_Flip_Flop d_ff_6 (.D(out_5[1]), .clk(clock_2_out), .Q(out_5[0]));  // open: Qn, preset, reset
  and and_4 (and_4_out, out_9[1], out_9[0]);
  and s0 (s0_out, d_ff_1_q, and_1_out);
  and s1 (s1_out, ~d_ff_1_q, and_1_out);  // AND_Gate
  and and_5 (and_5_out, out_5[0], and_2_out);
  and and_6 (and_6_out, ~out_5[0], and_2_out);  // AND_Gate
  and and_7 (and_7_out, ~and_11_out, s0_out);  // AND_Gate
  and and_8 (and_8_out, s1_out, ~and_12_out);  // AND_Gate
  T_Flip_Flop t_ff_5 (.T(1'b1), .clk(and_5_out), .Q(t_ff_5_q), .Qn(neparni[0]));  // open: reset, preset
  T_Flip_Flop t_ff_6 (.T(1'b1), .clk(and_6_out), .Q(t_ff_6_q), .Qn(parni[0]));  // open: reset, preset
  T_Flip_Flop #(.trigger("falling")) t_ff_7 (
    .T(xor_1_out), .clk(clock_5_out), .Q(out_3[0]), .Qn(t_ff_7_qn));  // open: reset, preset
  xor xor_1 (xor_1_out, and_7_out, and_8_out);
  Clock clock_5 (.out(clock_5_out));
  T_Flip_Flop t_ff_8 (.T(1'b1), .clk(t_ff_5_q), .Q(t_ff_8_q), .Qn(neparni[1]));  // open: reset, preset
  T_Flip_Flop t_ff_9 (.T(1'b1), .clk(t_ff_6_q), .Q(t_ff_9_q), .Qn(parni[1]));  // open: reset, preset
  T_Flip_Flop t_ff_10 (.T(1'b1), .clk(t_ff_8_q), .Q(t_ff_10_q), .Qn(neparni[2]));  // open: reset, preset
  T_Flip_Flop t_ff_11 (.T(1'b1), .clk(t_ff_9_q), .Q(t_ff_11_q), .Qn(parni[2]));  // open: reset, preset
  and and_9 (and_9_out, and_7_out, out_3[0]);
  and and_10 (and_10_out, and_8_out, t_ff_7_qn);
  T_Flip_Flop t_ff_12 (.T(1'b1), .clk(t_ff_10_q), .Qn(neparni[3]));  // open: Q, reset, preset
  T_Flip_Flop t_ff_13 (.T(1'b1), .clk(t_ff_11_q), .Qn(parni[3]));  // open: Q, reset, preset
  and and_11 (and_11_out, out_3[0], out_3[1], out_3[2]);
  T_Flip_Flop #(.trigger("falling")) t_ff_14 (
    .T(xor_2_out), .clk(clock_6_out), .Q(out_3[1]), .Qn(t_ff_14_qn));  // open: reset, preset
  xor xor_2 (xor_2_out, and_9_out, and_10_out);
  Clock clock_6 (.out(clock_6_out));
  and and_12 (and_12_out, t_ff_7_qn, t_ff_14_qn, t_ff_15_qn);
  and and_13 (and_13_out, and_9_out, out_3[1]);
  and and_14 (and_14_out, and_10_out, t_ff_14_qn);
  T_Flip_Flop #(.trigger("falling")) t_ff_15 (
    .T(xor_3_out), .clk(clock_7_out), .Q(out_3[2]), .Qn(t_ff_15_qn));  // open: reset, preset
  xor xor_3 (xor_3_out, and_13_out, and_14_out);
  Clock clock_7 (.out(clock_7_out));
  xor xor_4 (xor_4_out, neparni[3], parni[3]);
  xor xor_5 (xor_5_out, neparni[2], parni[2]);
  and and_15 (and_15_out, ~xor_4_out, ~xor_5_out);  // AND_Gate
  xor xor_6 (xor_6_out, neparni[1], parni[1]);
  and and_16 (and_16_out, ~xor_4_out, ~xor_5_out, ~xor_6_out);  // AND_Gate
  xor xor_7 (xor_7_out, neparni[0], parni[0]);
  and and_17 (and_17_out, xor_4_out, ~neparni[3]);  // AND_Gate
  and and_18 (and_18_out, xor_5_out, ~xor_4_out, ~neparni[2]);  // AND_Gate
  and and_19 (and_19_out, xor_6_out, and_15_out, ~neparni[1]);  // AND_Gate
  and and_20 (and_20_out, xor_7_out, and_16_out, ~neparni[0]);  // AND_Gate
  nor nor_1 (out_8, and_17_out, and_18_out, and_19_out, and_20_out);
endmodule
