// Logisim project vremenskaiteracijairegistri.circ as structural Verilog
module PROFREG (
  input  [7:0] P_In,
  input  S_In,
  input  Shift,
  input  Side,
  input  ParLoad,
  input  Clk,
  output [7:0] P_Out,
  output S_Out
);

  wire and_1_out, multiplexer_1_out, multiplexer_2_out, multiplexer_3_out, multiplexer_4_out,
       multiplexer_5_out, multiplexer_6_out, multiplexer_7_out, multiplexer_8_out;
  wire [1:0] and_2_out;

  and and_1 (and_1_out, Shift, Side);
  and and_2 (and_2_out[0], Shift, ~ParLoad);  // AND_Gate
  or or_1 (and_2_out[1], and_1_out, ParLoad);
  D_Flip_Flop d_ff_1 (.D(multiplexer_1_out), .clk(Clk), .Q(P_Out[0]));  // open: Qn, preset, reset
  Multiplexer #(.select(2)) multiplexer_1 (
    .in0(P_Out[0]), .in1(S_In), .in2(P_In[0]), .in3(P_Out[1]), .out(multiplexer_1_out), .sel(and_2_out));
  D_Flip_Flop d_ff_2 (.D(multiplexer_2_out), .clk(Clk), .Q(P_Out[1]));  // open: Qn, preset, reset
  Multiplexer #(.select(2)) multiplexer_2 (
    .in0(P_Out[1]), .in1(P_Out[0]), .in2(P_In[1]), .in3(P_Out[2]), .out(multiplexer_2_out), .sel(and_2_out));
  D_Flip_Flop d_ff_3 (.D(multiplexer_3_out), .clk(Clk), .Q(P_Out[2]));  // open: Qn, preset, reset
  Multiplexer #(.select(2)) multiplexer_3 (
    .in0(P_Out[2]), .in1(P_Out[1]), .in2(P_In[2]), .in3(P_Out[3]), .out(multiplexer_3_out), .sel(and_2_out));
  D_Flip_Flop d_ff_4 (.D(multiplexer_4_out), .clk(Clk), .Q(P_Out[3]));  // open: Qn, preset, reset
  Multiplexer #(.select(2)) multiplexer_4 (
    .in0(P_Out[3]), .in1(P_Out[2]), .in2(P_In[3]), .in3(P_Out[4]), .out(multiplexer_4_out), .sel(and_2_out));
  D_Flip_Flop d_ff_5 (.D(multiplexer_5_out), .clk(Clk), .Q(P_Out[4]));  // open: Qn, preset, reset
  Multiplexer #(.select(2)) multiplexer_5 (
    .in0(P_Out[4]), .in1(P_Out[3]), .in2(P_In[4]), .in3(P_Out[5]), .out(multiplexer_5_out), .sel(and_2_out));
  Multiplexer #(.select(2)) multiplexer_6 (
    .in0(P_Out[5]), .in1(P_Out[4]), .in2(P_In[5]), .in3(P_Out[6]), .out(multiplexer_6_out), .sel(and_2_out));
  D_Flip_Flop d_ff_6 (.D(multiplexer_6_out), .clk(Clk), .Q(P_Out[5]));  // open: Qn, preset, reset
  D_Flip_Flop d_ff_7 (.D(multiplexer_7_out), .clk(Clk), .Q(P_Out[6]));  // open: Qn, preset, reset
  Multiplexer #(.select(2)) multiplexer_7 (
    .in0(P_Out[6]), .in1(P_Out[5]), .in2(P_In[6]), .in3(P_Out[7]), .out(multiplexer_7_out), .sel(and_2_out));
  // Probe on P_Out
  D_Flip_Flop d_ff_8 (.D(multiplexer_8_out), .clk(Clk), .Q(P_Out[7]));  // open: Qn, preset, reset
  Multiplexer #(.select(2)) multiplexer_8 (
    .in0(P_Out[7]), .in1(P_Out[6]), .in2(P_In[7]), .in3(S_In), .out(multiplexer_8_out), .sel(and_2_out));
  Multiplexer multiplexer_9 (.in0(P_Out[7]), .in1(P_Out[0]), .out(S_Out), .sel(Side));
endmodule

module SHIFTREGDESNO (
  input  [3:0] ParallelIn,
  input  SerialIn,
  input  Clock,
  input  ParallelLoad,
  output SerialOut,
  output [3:0] ParallelOut
);

  wire multiplexer_1_out, multiplexer_2_out, multiplexer_3_out, multiplexer_4_out;

  Multiplexer multiplexer_1 (.in0(SerialIn), .in1(ParallelIn[3]), .out(multiplexer_1_out), .sel(ParallelLoad));
  D_Flip_Flop d_ff_1 (.D(multiplexer_1_out), .clk(Clock), .Q(ParallelOut[3]));  // open: Qn, preset, reset
  D_Flip_Flop d_ff_2 (.D(multiplexer_2_out), .clk(Clock), .Q(ParallelOut[2]));  // open: Qn, preset, reset
  Multiplexer multiplexer_2 (.in0(ParallelOut[3]), .in1(ParallelIn[2]), .out(multiplexer_2_out), .sel(ParallelLoad));
  D_Flip_Flop d_ff_3 (.D(multiplexer_3_out), .clk(Clock), .Q(ParallelOut[1]));  // open: Qn, preset, reset
  Multiplexer multiplexer_3 (.in0(ParallelOut[2]), .in1(ParallelIn[1]), .out(multiplexer_3_out), .sel(ParallelLoad));
  D_Flip_Flop d_ff_4 (.D(multiplexer_4_out), .clk(Clock), .Q(ParallelOut[0]));  // open: Qn, preset, reset
  Multiplexer multiplexer_4 (.in0(ParallelOut[1]), .in1(ParallelIn[0]), .out(multiplexer_4_out), .sel(ParallelLoad));

  assign SerialOut = ParallelOut[0];
endmodule

module SHIFTREGLIJEVO (
  input  SerialIn,
  input  [3:0] ParallelIn,
  input  Clock,
  input  ParallelLoad,
  output SerialOut,
  output [3:0] ParallelOut
);

  wire multiplexer_1_out, multiplexer_2_out, multiplexer_3_out, multiplexer_4_out;

  Multiplexer multiplexer_1 (.in0(ParallelOut[2]), .in1(ParallelIn[3]), .out(multiplexer_1_out), .sel(ParallelLoad));
  D_Flip_Flop d_ff_1 (.D(multiplexer_1_out), .clk(Clock), .Q(ParallelOut[3]));  // open: Qn, preset, reset
  D_Flip_Flop d_ff_2 (.D(multiplexer_2_out), .clk(Clock), .Q(ParallelOut[2]));  // open: Qn, preset, reset
  Multiplexer multiplexer_2 (.in0(ParallelOut[1]), .in1(ParallelIn[2]), .out(multiplexer_2_out), .sel(ParallelLoad));
  D_Flip_Flop d_ff_3 (.D(multiplexer_3_out), .clk(Clock), .Q(ParallelOut[1]));  // open: Qn, preset, reset
  Multiplexer multiplexer_3 (.in0(ParallelOut[0]), .in1(ParallelIn[1]), .out(multiplexer_3_out), .sel(ParallelLoad));
  D_Flip_Flop d_ff_4 (.D(multiplexer_4_out), .clk(Clock), .Q(ParallelOut[0]));  // open: Qn, preset, reset
  Multiplexer multiplexer_4 (.in0(SerialIn), .in1(ParallelIn[0]), .out(multiplexer_4_out), .sel(ParallelLoad));

  assign SerialOut = ParallelOut[3];
endmodule

module PRVIPRIMJER (
  input  [3:0] in_1,
  input  [3:0] X,
  input  ParallelLoad,
  output [3:0] out_4,
  output [3:0] out_5
);

  wire clock_1_out, not_1_out, shiftregdesno_1_serialout;

  Clock clock_1 (.out(clock_1_out));
  SHIFTREGDESNO shiftregdesno_1 (
    .ParallelIn(X), .Clock(clock_1_out), .ParallelLoad(ParallelLoad), .SerialOut(shiftregdesno_1_serialout),
    .ParallelOut(out_5));  // open: SerialIn
  not not_1 (not_1_out, shiftregdesno_1_serialout);
  SHIFTREGDESNO shiftregdesno_2 (
    .ParallelIn(in_1), .SerialIn(not_1_out), .Clock(clock_1_out), .ParallelLoad(ParallelLoad),
    .ParallelOut(out_4));  // open: SerialOut
endmodule

module DRUGIPRIMJER (
  input  [3:0] in_1,
  input  [3:0] X,
  input  ParallelLoad,
  output [3:0] out_4,
  output [3:0] out_5,
  output [3:0] out_6
);

  wire clock_1_out, d_ff_1_q, multiplexer_1_out, not_1_out, shiftregdesno_1_serialout;

  Clock clock_1 (.out(clock_1_out));
  SHIFTREGDESNO shiftregdesno_1 (
    .ParallelIn(X), .Clock(clock_1_out), .ParallelLoad(ParallelLoad), .SerialOut(shiftregdesno_1_serialout),
    .ParallelOut(out_6));  // open: SerialIn
  not not_1 (not_1_out, shiftregdesno_1_serialout);
  D_Flip_Flop d_ff_1 (.D(1'b1), .clk(out_6[3]), .Q(d_ff_1_q));  // open: Qn, preset, reset
  Multiplexer multiplexer_1 (.in0(shiftregdesno_1_serialout), .in1(not_1_out), .out(multiplexer_1_out), .sel(d_ff_1_q));
  SHIFTREGDESNO shiftregdesno_2 (
    .ParallelIn(in_1), .SerialIn(multiplexer_1_out), .Clock(clock_1_out), .ParallelLoad(ParallelLoad),
    .ParallelOut(out_5));  // open: SerialOut

  assign out_4 = X;
endmodule

module HA (
  input  X,
  input  Y,
  output XplusY,
  output carry
);

  xor xor_1 (XplusY, X, Y);
  and and_1 (carry, X, Y);
endmodule

module FA (
  input  X,
  input  Y,
  input  carryIn,
  output XplusY,
  output carryOut
);

  wire ha_1_carry, ha_1_xplusy, ha_2_carry;

  HA ha_1 (.X(X), .Y(Y), .XplusY(ha_1_xplusy), .carry(ha_1_carry));
  HA ha_2 (.X(ha_1_xplusy), .Y(carryIn), .XplusY(XplusY), .carry(ha_2_carry));
  or or_1 (carryOut, ha_2_carry, ha_1_carry);
endmodule

module TRECIPRIMJER (
  input  [3:0] X,
  input  [3:0] in_2,
  input  [3:0] Y,
  input  ParallelLoad,
  output [3:0] out_5,
  output [3:0] out_6,
  output [3:0] out_7,
  output [3:0] out_8,
  output [3:0] out_9,
  output [3:0] out_10,
  output [3:0] out_11,
  output [3:0] out_12,
  output out_13
);

  wire clock_1_out, clock_2_out, clock_3_out, clock_4_out, d_ff_1_q, d_ff_2_q, d_ff_3_q, fa_1_carryout,
       fa_1_xplusy, Xreg_serialout, Yreg_serialout;

  Clock clock_1 (.out(clock_1_out));
  SHIFTREGDESNO Xreg (
    .ParallelIn(X), .Clock(clock_1_out), .ParallelLoad(ParallelLoad), .SerialOut(Xreg_serialout),
    .ParallelOut(out_6));  // open: SerialIn
  SHIFTREGDESNO Yreg (
    .ParallelIn(Y), .Clock(clock_1_out), .ParallelLoad(ParallelLoad), .SerialOut(Yreg_serialout),
    .ParallelOut(out_11));  // open: SerialIn
  D_Flip_Flop d_ff_1 (.D(fa_1_carryout), .clk(clock_2_out), .Q(d_ff_1_q), .reset(ParallelLoad));  // open: Qn, preset
  Clock clock_2 (.out(clock_2_out));
  FA fa_1 (.X(Xreg_serialout), .Y(Yreg_serialout), .carryIn(d_ff_1_q), .XplusY(fa_1_xplusy), .carryOut(fa_1_carryout));
  Clock clock_3 (.out(clock_3_out));
  Clock clock_4 (.out(clock_4_out));
  D_Flip_Flop d_ff_2 (.D(fa_1_carryout), .clk(clock_3_out), .Q(d_ff_2_q));  // open: Qn, preset, reset
  D_Flip_Flop d_ff_3 (.D(d_ff_2_q), .clk(clock_3_out), .Q(d_ff_3_q));  // open: Qn, preset, reset
  SHIFTREGDESNO shiftregdesno_1 (
    .ParallelIn(in_2), .SerialIn(fa_1_xplusy), .Clock(clock_4_out), .ParallelLoad(ParallelLoad),
    .ParallelOut(out_9));  // open: SerialOut
  xor xor_1 (out_13, d_ff_2_q, d_ff_3_q);

  assign out_5 = X;
  assign out_7 = out_6;
  assign out_8 = Y;
  assign out_10 = out_9;
  assign out_12 = out_11;
endmodule

module CETVRTIPRIMJER (
  input  [3:0] in_1,
  input  [3:0] Y,
  input  ParallelLoad,
  output [3:0] out_4,
  output [3:0] out_5,
  output [3:0] out_6,
  output [3:0] out_7,
  output [3:0] out_8
);

  wire and_1_out, carry_q, clock_1_out, clock_2_out, clock_3_out, ha_1_carry, ha_1_xplusy, multiplexer_1_out,
       negativan_q, not_1_out, not_2_out, shiftregdesno_1_serialout;

  Clock clock_1 (.out(clock_1_out));
  SHIFTREGDESNO shiftregdesno_1 (
    .ParallelIn(Y), .Clock(clock_1_out), .ParallelLoad(ParallelLoad), .SerialOut(shiftregdesno_1_serialout),
    .ParallelOut(out_7));  // open: SerialIn
  D_Flip_Flop negativan (.D(1'b1), .clk(out_7[3]), .Q(negativan_q));  // open: Qn, preset, reset
  Multiplexer multiplexer_1 (
    .in0(shiftregdesno_1_serialout), .in1(not_1_out), .out(multiplexer_1_out), .sel(not_2_out));
  not not_1 (not_1_out, shiftregdesno_1_serialout);
  and and_1 (and_1_out, not_2_out, carry_q);
  not not_2 (not_2_out, negativan_q);
  D_Flip_Flop carry (.D(ha_1_carry), .clk(clock_2_out), .Q(carry_q), .preset(ParallelLoad));  // open: Qn, reset
  Clock clock_2 (.out(clock_2_out));
  HA ha_1 (.X(multiplexer_1_out), .Y(and_1_out), .XplusY(ha_1_xplusy), .carry(ha_1_carry));
  Clock clock_3 (.out(clock_3_out));
  SHIFTREGDESNO shiftregdesno_2 (
    .ParallelIn(in_1), .SerialIn(ha_1_xplusy), .Clock(clock_3_out), .ParallelLoad(ParallelLoad),
    .ParallelOut(out_5));  // open: SerialOut

  assign out_4 = Y;
  assign out_6 = out_5;
  assign out_8 = out_7;
endmodule

module FS (
  input  X,
  input  Y,
  input  Bin,
  output XminusY,
  output Bout
);

  wire and_1_out, and_2_out, xor_1_out;

  xor xor_1 (xor_1_out, X, Y);
  xor xor_2 (XminusY, xor_1_out, Bin);
  and and_1 (and_1_out, ~xor_1_out, Bin);  // AND_Gate
  and and_2 (and_2_out, ~X, Y);  // AND_Gate
  or or_1 (Bout, and_1_out, and_2_out);
endmodule

module PETIPRIMJER (
  input  [3:0] X,
  input  [3:0] in_2,
  input  [3:0] Y,
  input  ParallelLoad,
  output [3:0] out_5,
  output [3:0] out_6,
  output [3:0] out_7,
  output [3:0] out_8,
  output [3:0] out_9,
  output [3:0] out_10,
  output [3:0] out_11,
  output [3:0] out_12
);

  wire clock_1_out, clock_2_out, clock_3_out, d_ff_1_q, fs_1_bout, fs_1_xminusy, Xreg_serialout,
       Yreg_serialout;

  Clock clock_1 (.out(clock_1_out));
  SHIFTREGDESNO Xreg (
    .ParallelIn(X), .Clock(clock_1_out), .ParallelLoad(ParallelLoad), .SerialOut(Xreg_serialout),
    .ParallelOut(out_6));  // open: SerialIn
  SHIFTREGDESNO Yreg (
    .ParallelIn(Y), .Clock(clock_1_out), .ParallelLoad(ParallelLoad), .SerialOut(Yreg_serialout),
    .ParallelOut(out_11));  // open: SerialIn
  D_Flip_Flop d_ff_1 (.D(fs_1_bout), .clk(clock_2_out), .Q(d_ff_1_q), .reset(ParallelLoad));  // open: Qn, preset
  Clock clock_2 (.out(clock_2_out));
  FS fs_1 (.X(Xreg_serialout), .Y(Yreg_serialout), .Bin(d_ff_1_q), .XminusY(fs_1_xminusy), .Bout(fs_1_bout));
  Clock clock_3 (.out(clock_3_out));
  SHIFTREGDESNO shiftregdesno_1 (
    .ParallelIn(in_2), .SerialIn(fs_1_xminusy), .Clock(clock_3_out), .ParallelLoad(ParallelLoad),
    .ParallelOut(out_9));  // open: SerialOut

  assign out_5 = X;
  assign out_7 = out_6;
  assign out_8 = Y;
  assign out_10 = out_9;
  assign out_12 = out_11;
endmodule

module SESTIPRIMJER (
  input  [3:0] X,
  input  [3:0] Y,
  input  ParallelLoad,
  output [3:0] out_4,
  output XveceY,
  output [3:0] out_6,
  output XjednakoY,
  output [3:0] out_8,
  output [3:0] out_9,
  output XmanjeY,
  output [3:0] out_11,
  output [3:0] out_12
);

  wire and_1_out, and_2_out, clock_1_out, onebitcompare_1_xmanjey, onebitcompare_1_xvecey,
       shiftreglijevo_1_serialout, shiftreglijevo_2_serialout;

  Clock clock_1 (.out(clock_1_out));
  SHIFTREGLIJEVO shiftreglijevo_1 (
    .ParallelIn(X), .Clock(clock_1_out), .ParallelLoad(ParallelLoad), .SerialOut(shiftreglijevo_1_serialout),
    .ParallelOut(out_6));  // open: SerialIn
  SHIFTREGLIJEVO shiftreglijevo_2 (
    .ParallelIn(Y), .Clock(clock_1_out), .ParallelLoad(ParallelLoad), .SerialOut(shiftreglijevo_2_serialout),
    .ParallelOut(out_11));  // open: SerialIn
  ONEBITCOMPARE onebitcompare_1 (
    .X(shiftreglijevo_1_serialout), .Y(shiftreglijevo_2_serialout), .XveceY(onebitcompare_1_xvecey),
    .XmanjeY(onebitcompare_1_xmanjey));  // open: jednaki
  D_Flip_Flop d_ff_1 (.D(1'b1), .clk(and_1_out), .Q(XveceY));  // open: Qn, preset, reset
  and and_1 (and_1_out, onebitcompare_1_xvecey, ~XmanjeY);  // AND_Gate
  D_Flip_Flop d_ff_2 (.D(1'b1), .clk(and_2_out), .Q(XmanjeY));  // open: Qn, preset, reset
  and and_2 (and_2_out, ~XveceY, onebitcompare_1_xmanjey);  // AND_Gate
  xnor xnor_1 (XjednakoY, XveceY, XmanjeY);

  assign out_4 = X;
  assign out_8 = out_6;
  assign out_9 = Y;
  assign out_12 = out_11;
endmodule

module ONEBITCOMPARE (
  input  X,
  input  Y,
  output XveceY,
  output XmanjeY,
  output jednaki
);

  and and_1 (XveceY, X, ~Y);  // AND_Gate
  and and_2 (XmanjeY, ~X, Y);  // AND_Gate
  xnor xnor_1 (jednaki, X, Y);
endmodule

module SEDMIPRIMJER (
  input  [3:0] X,
  input  [3:0] Y,
  input  ParallelLoad,
  output [3:0] out_4,
  output XveceY,
  output [3:0] out_6,
  output XjednakoY,
  output [3:0] out_8,
  output [3:0] out_9,
  output XmanjeY,
  output [3:0] out_11,
  output [3:0] out_12
);

  wire and_1_out, and_2_out, and_3_out, and_4_out, and_5_out, and_6_out, clock_1_out,
       onebitcompare_1_xmanjey, onebitcompare_1_xvecey, or_1_out, or_2_out, procitanPrvi_q,
       shiftreglijevo_1_serialout, shiftreglijevo_2_serialout;

  Clock clock_1 (.out(clock_1_out));
  D_Flip_Flop procitanPrvi (.D(1'b1), .clk(clock_1_out), .Q(procitanPrvi_q), .reset(ParallelLoad));  // open: Qn, preset
  SHIFTREGLIJEVO shiftreglijevo_1 (
    .ParallelIn(X), .Clock(clock_1_out), .ParallelLoad(ParallelLoad), .SerialOut(shiftreglijevo_1_serialout),
    .ParallelOut(out_6));  // open: SerialIn
  SHIFTREGLIJEVO shiftreglijevo_2 (
    .ParallelIn(Y), .Clock(clock_1_out), .ParallelLoad(ParallelLoad), .SerialOut(shiftreglijevo_2_serialout),
    .ParallelOut(out_11));  // open: SerialIn
  and and_1 (and_1_out, shiftreglijevo_1_serialout, procitanPrvi_q);
  and and_2 (and_2_out, shiftreglijevo_2_serialout, procitanPrvi_q);
  and and_3 (and_3_out, shiftreglijevo_1_serialout, ~shiftreglijevo_2_serialout, ~procitanPrvi_q);  // AND_Gate
  and and_4 (and_4_out, ~shiftreglijevo_1_serialout, shiftreglijevo_2_serialout, ~procitanPrvi_q);  // AND_Gate
  ONEBITCOMPARE onebitcompare_1 (
    .X(and_1_out), .Y(and_2_out), .XveceY(onebitcompare_1_xvecey), .XmanjeY(onebitcompare_1_xmanjey));  // open: jednaki
  D_Flip_Flop d_ff_1 (.D(1'b1), .clk(and_5_out), .Q(XveceY));  // open: Qn, preset, reset
  or or_1 (or_1_out, onebitcompare_1_xvecey, and_4_out);
  and and_5 (and_5_out, or_1_out, ~XmanjeY);  // AND_Gate
  D_Flip_Flop d_ff_2 (.D(1'b1), .clk(and_6_out), .Q(XmanjeY));  // open: Qn, preset, reset
  and and_6 (and_6_out, ~XveceY, or_2_out);  // AND_Gate
  or or_2 (or_2_out, onebitcompare_1_xmanjey, and_3_out);
  xnor xnor_1 (XjednakoY, XveceY, XmanjeY);

  assign out_4 = X;
  assign out_8 = out_6;
  assign out_9 = Y;
  assign out_12 = out_11;
endmodule

module OSMIPRIMJER (
  input  Sin,
  output [1:0] out_2,
  output [2:0] out_3,
  output [2:0] out_4,
  output [1:0] out_5
);

  wire and_1_out, and_2_out, and_3_out, clock_1_out, clock_2_out, d_ff_1_q, nor_1_out, procitaneTri_q,
       t_ff_1_q, trobitniregdesno_1_serialout;
  wire [2:0] xor_1_out;

  Clock clock_1 (.out(clock_1_out));
  T_Flip_Flop t_ff_1 (.T(1'b1), .clk(clock_1_out), .Q(t_ff_1_q), .Qn(out_5[0]), .preset(and_1_out));  // open: reset
  TROBITNIREGDESNO trobitniregdesno_1 (
    .SerialIn(Sin), .Clock(clock_1_out), .SerialOut(trobitniregdesno_1_serialout), .ParallelOut(out_4));  // open: ParallelIn, ParallelLoad
  T_Flip_Flop t_ff_2 (.T(1'b1), .clk(t_ff_1_q), .Qn(out_5[1]), .preset(and_1_out));  // open: Q, reset
  D_Flip_Flop procitaneTri (.D(1'b1), .clk(and_2_out), .Q(procitaneTri_q));  // open: Qn, preset, reset
  Clock clock_2 (.out(clock_2_out));
  D_Flip_Flop d_ff_1 (.D(procitaneTri_q), .clk(and_2_out), .Q(d_ff_1_q));  // open: Qn, preset, reset
  and and_1 (and_1_out, out_5[0], out_5[1]);
  and and_2 (and_2_out, ~out_5[0], out_5[1]);  // AND_Gate
  TROBITNIREGDESNO trobitniregdesno_2 (
    .SerialIn(trobitniregdesno_1_serialout), .Clock(clock_2_out), .ParallelOut(out_3));  // open: ParallelIn, ParallelLoad, SerialOut
  assign xor_1_out = out_3 ^ out_4;  // XOR_Gate xor_1, 3 bits wide
  nor nor_1 (nor_1_out, xor_1_out[0], xor_1_out[1], xor_1_out[2]);
  and and_3 (and_3_out, nor_1_out, and_2_out, d_ff_1_q);
  Multiplexer #(.width(2)) multiplexer_1 (.in0(2'b01), .in1(2'b10), .out(out_2), .sel(and_3_out));
endmodule

module TROBITNIREGDESNO (
  input  [2:0] ParallelIn,
  input  SerialIn,
  input  Clock,
  input  ParallelLoad,
  output SerialOut,
  output [2:0] ParallelOut
);

  wire multiplexer_1_out, multiplexer_2_out, multiplexer_3_out;

  Multiplexer multiplexer_1 (.in0(SerialIn), .in1(ParallelIn[2]), .out(multiplexer_1_out), .sel(ParallelLoad));
  D_Flip_Flop d_ff_1 (.D(multiplexer_1_out), .clk(Clock), .Q(ParallelOut[2]));  // open: Qn, preset, reset
  D_Flip_Flop d_ff_2 (.D(multiplexer_2_out), .clk(Clock), .Q(ParallelOut[1]));  // open: Qn, preset, reset
  Multiplexer multiplexer_2 (.in0(ParallelOut[2]), .in1(ParallelIn[1]), .out(multiplexer_2_out), .sel(ParallelLoad));
  D_Flip_Flop d_ff_3 (.D(multiplexer_3_out), .clk(Clock), .Q(ParallelOut[0]));  // open: Qn, preset, reset
  Multiplexer multiplexer_3 (.in0(ParallelOut[1]), .in1(ParallelIn[0]), .out(multiplexer_3_out), .sel(ParallelLoad));

  assign SerialOut = ParallelOut[0];
endmodule
