// Logisim project zadaca2.circ as structural Verilog
module Z1Moore (
  input  u,
  output y
);

  wire and_1_out, and_2_out, and_3_out, and_4_out, and_5_out, and_6_out, and_7_out, and_8_out, and_9_out,
       and_10_out, and_11_out, and_12_out, and_14_out, and_15_out, and_16_out, clock_1_out, j0, j1, j2, j3,
       not_2_out, not_3_out, not_4_out, q0, q0n, q1, q1n, q2, q2n, q3, q3n, un;

  not not_1 (un, u);
  Clock clock_1 (.out(clock_1_out));
  D_Flip_Flop d_ff_1 (.D(j3), .clk(clock_1_out), .Q(q3), .Qn(q3n));  // open: preset, reset
  and and_1 (and_1_out, q2, q1n, q0n, u);
  and and_2 (and_2_out, q3n, q2, q1, q0);
  and and_3 (and_3_out, q3n, un, q1, q0);
  D_Flip_Flop d_ff_2 (.D(j2), .clk(clock_1_out), .Q(q2), .Qn(q2n));  // open: preset, reset
  or or_1 (j3, and_1_out, and_2_out, and_3_out);
  D_Flip_Flop d_ff_3 (.D(j1), .clk(clock_1_out), .Q(q1), .Qn(q1n));  // open: preset, reset
  and and_4 (and_4_out, q2n, q1n, q0n, un);
  and and_5 (and_5_out, q3n, q0, u);
  and and_6 (and_6_out, q3n, q1, q0);
  and and_7 (and_7_out, q3n, q2, q0);
  and and_8 (and_8_out, q3n, q2, q1);
  D_Flip_Flop d_ff_4 (.D(j0), .clk(clock_1_out), .Q(q0), .Qn(q0n));  // open: preset, reset
  or or_2 (j2, and_4_out, and_5_out, and_6_out, and_7_out, and_8_out);
  and and_9 (and_9_out, q1n, q0);
  and and_10 (and_10_out, q1, q0n);
  and and_11 (and_11_out, q3n, q0, un);
  and and_12 (and_12_out, q3n, q2, q0);
  not not_2 (not_2_out, q0);
  not not_3 (not_3_out, q1);
  not not_4 (not_4_out, q2);
  or or_3 (j1, and_9_out, and_10_out, and_11_out, and_12_out);
  and and_13 (y, not_2_out, not_3_out, not_4_out, q3);
  and and_14 (and_14_out, q2n, q0n);
  and and_15 (and_15_out, q3n, q2, q1);
  or or_4 (j0, and_14_out, and_15_out, and_16_out);
  and and_16 (and_16_out, q3n, q1, un);
endmodule

module Z1Mealy (
  input  u,
  output y
);

  wire and_1_out, and_2_out, and_3_out, and_4_out, and_5_out, and_6_out, and_7_out, and_8_out, and_9_out,
       and_10_out, and_11_out, and_13_out, and_14_out, and_15_out, clock_1_out, j0, j1, j2, j3, q0, q0n, q1,
       q1n, q2, q2n, q3, q3n, un;

  not not_1 (un, u);
  Clock clock_1 (.out(clock_1_out));
  D_Flip_Flop d_ff_1 (.D(j3), .clk(clock_1_out), .Q(q3), .Qn(q3n));  // open: preset, reset
  and and_1 (and_1_out, q3n, q2, q1, q0);
  and and_2 (and_2_out, q3n, un, q1, q0);
  D_Flip_Flop d_ff_2 (.D(j2), .clk(clock_1_out), .Q(q2), .Qn(q2n));  // open: preset, reset
  or or_1 (j3, and_1_out, and_2_out);
  D_Flip_Flop d_ff_3 (.D(j1), .clk(clock_1_out), .Q(q1), .Qn(q1n));  // open: preset, reset
  and and_3 (and_3_out, q2n, q1n, q0n, un);
  and and_4 (and_4_out, q3n, q0, u);
  and and_5 (and_5_out, q3n, q1, q0);
  and and_6 (and_6_out, q3n, q2, q0);
  and and_7 (and_7_out, q3n, q2, q1);
  D_Flip_Flop d_ff_4 (.D(j0), .clk(clock_1_out), .Q(q0), .Qn(q0n));  // open: preset, reset
  or or_2 (j2, and_3_out, and_4_out, and_5_out, and_6_out, and_7_out);
  and and_8 (and_8_out, q1n, q0);
  and and_9 (and_9_out, q1, q0n);
  and and_10 (and_10_out, q3n, q0, un);
  and and_11 (and_11_out, q3n, q2, q0);
  or or_3 (j1, and_8_out, and_9_out, and_10_out, and_11_out);
  and and_12 (y, u, q3n, q2, q1n, q0n);
  and and_13 (and_13_out, q2n, q0n);
  and and_14 (and_14_out, q3n, q2, q1);
  or or_4 (j0, and_13_out, and_14_out, and_15_out);
  and and_15 (and_15_out, q3n, q1, un);
endmodule

module Z2 (
  input  [5:0] X,
  input  RESET,
  input  [5:0] Y,
  output [5:0] out_4,
  output [5:0] out_5,
  output XveceodY,
  output [5:0] out_7,
  output XmanjeodY,
  output XjednakoY,
  output [5:0] out_10,
  output [5:0] out_11,
  output [5:0] out_12
);

  wire and_1_out, and_2_out, and_3_out, and_4_out, and_5_out, and_6_out, and_7_out, and_8_out, and_9_out,
       clock_1_out, comp1bit_1_xmanjey, comp1bit_1_xvecey, not_1_out, not_2_out, not_3_out, not_4_out,
       or_1_out, or_2_out, or_3_out, ProcitanPrvi_q, XnegYpos_out, Xreg_s_out, YnegXpos_out, Yreg_s_out;

  Clock clock_1 (.out(clock_1_out));
  not not_1 (not_1_out, ProcitanPrvi_q);
  REG6BIT Xreg (
    .P_In(X), .Shift(1'b1), .Side(1'b1), .ParLoad(RESET), .Clk(clock_1_out), .P_Out(out_4), .S_Out(Xreg_s_out));
  REG6BIT Yreg (
    .P_In(Y), .Shift(1'b1), .Side(1'b1), .ParLoad(RESET), .Clk(clock_1_out), .P_Out(out_11),
    .S_Out(Yreg_s_out));
  T_Flip_Flop ProcitanPrvi (.T(not_1_out), .clk(clock_1_out), .Q(ProcitanPrvi_q), .reset(RESET));  // open: Qn, preset
  and and_1 (and_1_out, Xreg_s_out, not_2_out);
  and and_2 (and_2_out, Yreg_s_out, not_2_out);
  not not_2 (not_2_out, RESET);
  and YnegXpos (YnegXpos_out, and_2_out, ~and_1_out);  // AND_Gate
  and XnegYpos (XnegYpos_out, and_1_out, ~and_2_out);  // AND_Gate
  COMP1BIT comp1bit_1 (
    .x(and_1_out), .y(and_2_out), .XveceY(comp1bit_1_xvecey), .XmanjeY(comp1bit_1_xmanjey));  // open: jednaki
  and and_3 (and_3_out, ~ProcitanPrvi_q, YnegXpos_out);  // AND_Gate
  and and_4 (and_4_out, ~ProcitanPrvi_q, XnegYpos_out);  // AND_Gate
  and and_5 (and_5_out, ProcitanPrvi_q, comp1bit_1_xvecey);
  and and_6 (and_6_out, ProcitanPrvi_q, comp1bit_1_xmanjey);
  or or_1 (or_1_out, and_3_out, and_5_out);
  or or_2 (or_2_out, and_4_out, and_6_out);
  T_Flip_Flop XveceY (.T(not_3_out), .clk(and_7_out), .Q(XveceodY), .reset(or_3_out));  // open: Qn, preset
  not not_3 (not_3_out, XveceodY);
  and and_7 (and_7_out, or_1_out, ~XmanjeodY);  // AND_Gate
  T_Flip_Flop XmanjeY (.T(not_4_out), .clk(and_8_out), .Q(XmanjeodY), .reset(or_3_out));  // open: Qn, preset
  not not_4 (not_4_out, XmanjeodY);
  and and_8 (and_8_out, or_2_out, ~XveceodY);  // AND_Gate
  or or_3 (or_3_out, RESET, and_9_out);
  and and_9 (and_9_out, XveceodY, XmanjeodY);
  nor nor_1 (XjednakoY, XveceodY, XmanjeodY);

  assign out_5 = out_4;
  assign out_7 = X;
  assign out_10 = Y;
  assign out_12 = out_11;

  // Notes on the sheet:
  //   UPUTE:
  //   1. postavite zeljene brojeve X i Y
  //   2. upalite RESET i okinite sat
  //   3. ugasite RESET i okidajte sat
endmodule

module COMP1BIT (
  input  x,
  input  y,
  output XveceY,
  output XmanjeY,
  output jednaki
);

  wire and_1_out, and_2_out, and_4_out, and_5_out, not_1_out, not_2_out, not_3_out, xor_1_out;

  not not_1 (not_1_out, x);
  not not_2 (not_2_out, y);
  xor xor_1 (xor_1_out, x, y);
  not not_3 (not_3_out, xor_1_out);
  and and_1 (and_1_out, not_3_out, 1'b0);
  and and_2 (and_2_out, not_3_out, 1'b0);
  and and_3 (jednaki, not_3_out, 1'b1);
  and and_4 (and_4_out, not_1_out, y);
  and and_5 (and_5_out, not_2_out, x);
  or or_1 (XmanjeY, and_4_out, and_1_out);
  or or_2 (XveceY, and_5_out, and_2_out);
endmodule

module REG6BIT (
  input  [5:0] P_In,
  input  Shift,
  input  Side,
  input  ParLoad,
  input  Clk,
  output [5:0] P_Out,
  output S_Out
);

  wire and_1_out, multiplexer_1_out, multiplexer_2_out, multiplexer_3_out, multiplexer_4_out,
       multiplexer_5_out, multiplexer_6_out;
  wire [1:0] and_2_out;

  and and_1 (and_1_out, Shift, Side);
  and and_2 (and_2_out[0], Shift, ~ParLoad);  // AND_Gate
  or or_1 (and_2_out[1], and_1_out, ParLoad);
  D_Flip_Flop d_ff_1 (.D(multiplexer_1_out), .clk(Clk), .Q(P_Out[5]));  // open: Qn, preset, reset
  Multiplexer #(.select(2)) multiplexer_1 (
    .in0(P_Out[5]), .in1(1'b0), .in2(P_In[5]), .in3(P_Out[4]), .out(multiplexer_1_out), .sel(and_2_out));
  D_Flip_Flop d_ff_2 (.D(multiplexer_2_out), .clk(Clk), .Q(P_Out[4]));  // open: Qn, preset, reset
  Multiplexer #(.select(2)) multiplexer_2 (
    .in0(P_Out[4]), .in1(P_Out[5]), .in2(P_In[4]), .in3(P_Out[3]), .out(multiplexer_2_out), .sel(and_2_out));
  D_Flip_Flop d_ff_3 (.D(multiplexer_3_out), .clk(Clk), .Q(P_Out[3]));  // open: Qn, preset, reset
  Multiplexer #(.select(2)) multiplexer_3 (
    .in0(P_Out[3]), .in1(P_Out[4]), .in2(P_In[3]), .in3(P_Out[2]), .out(multiplexer_3_out), .sel(and_2_out));
  D_Flip_Flop d_ff_4 (.D(multiplexer_4_out), .clk(Clk), .Q(P_Out[2]));  // open: Qn, preset, reset
  Multiplexer #(.select(2)) multiplexer_4 (
    .in0(P_Out[2]), .in1(P_Out[3]), .in2(P_In[2]), .in3(P_Out[1]), .out(multiplexer_4_out), .sel(and_2_out));
  D_Flip_Flop d_ff_5 (.D(multiplexer_5_out), .clk(Clk), .Q(P_Out[1]));  // open: Qn, preset, reset
  Multiplexer #(.select(2)) multiplexer_5 (
    .in0(P_Out[1]), .in1(P_Out[2]), .in2(P_In[1]), .in3(P_Out[0]), .out(multiplexer_5_out), .sel(and_2_out));
  Multiplexer #(.select(2)) multiplexer_6 (
    .in0(P_Out[0]), .in1(P_Out[1]), .in2(P_In[0]), .in3(1'b0), .out(multiplexer_6_out), .sel(and_2_out));
  D_Flip_Flop d_ff_6 (.D(multiplexer_6_out), .clk(Clk), .Q(P_Out[0]));  // open: Qn, preset, reset
  // Probe on P_Out
  Multiplexer multiplexer_7 (.in0(P_Out[0]), .in1(P_Out[5]), .out(S_Out), .sel(Side));
endmodule
