// Logisim project LD_T8_Logisim.circ as structural Verilog
module Z1 (
);

  wire and_1_out, button_1_out, clock_1_out, not_1_out, t_ff_1_q, t_ff_1_qn, t_ff_2_q, xor_1_out;

  T_Flip_Flop t_ff_1 (
    .T(xor_1_out), .clk(clock_1_out), .Q(t_ff_1_q), .Qn(t_ff_1_qn), .reset(button_1_out));  // open: preset
  Button button_1 (.out(button_1_out));
  T_Flip_Flop t_ff_2 (.T(not_1_out), .clk(clock_1_out), .Q(t_ff_2_q), .reset(button_1_out));  // open: Qn, preset
  not not_1 (not_1_out, xor_1_out);
  Clock clock_1 (.out(clock_1_out));
  LED led_1 (.in(t_ff_1_qn));
  xor xor_1 (xor_1_out, t_ff_2_q, t_ff_1_q);
  LED led_2 (.in(xor_1_out));
  LED led_3 (.in(and_1_out));
  and and_1 (and_1_out, t_ff_2_q, t_ff_1_q);
endmodule

module Z2 (
);

  wire and_1_out, and_2_out, and_3_out, clock_1_out, or_1_out, or_2_out, t_ff_1_q, t_ff_1_qn, t_ff_2_q,
       t_ff_2_qn, t_ff_3_q, t_ff_3_qn, t_ff_4_q, t_ff_4_qn;

  Clock clock_1 (.out(clock_1_out));
  LED led_1 (.in(t_ff_1_qn));
  LED led_2 (.in(and_2_out));
  LED led_3 (.in(and_1_out));
  and and_1 (and_1_out, or_1_out, t_ff_1_q);
  T_Flip_Flop t_ff_1 (.T(and_2_out), .clk(clock_1_out), .Q(t_ff_1_q), .Qn(t_ff_1_qn));  // open: reset, preset
  and and_2 (and_2_out, t_ff_2_q, t_ff_4_q);
  or or_1 (or_1_out, t_ff_3_qn, t_ff_2_qn);
  T_Flip_Flop t_ff_2 (.T(and_3_out), .clk(clock_1_out), .Q(t_ff_2_q), .Qn(t_ff_2_qn));  // open: reset, preset
  and and_3 (and_3_out, t_ff_3_q, t_ff_4_q);
  or or_2 (or_2_out, t_ff_4_q, t_ff_2_q);
  T_Flip_Flop t_ff_3 (.T(or_2_out), .clk(clock_1_out), .Q(t_ff_3_q), .Qn(t_ff_3_qn));  // open: reset, preset
  T_Flip_Flop t_ff_4 (.T(1'b1), .clk(clock_1_out), .Q(t_ff_4_q), .Qn(t_ff_4_qn));  // open: reset, preset
endmodule

module Z3 (
  input  [7:0] Crveno,
  input  [7:0] CrvenoZuto,
  input  [7:0] Zeleno,
  input  [7:0] Zuto,
  input  [7:0] Treper,
  input  alt,
  input  enable,
  output [7:0] out_8,
  output [7:0] out_9
);

  wire and_1_out, and_2_out, and_3_out, and_4_out, and_5_out, and_6_out, and_7_out, and_8_out, and_9_out,
       and_10_out, and_11_out, and_12_out, and_13_out, and_14_out, and_15_out, clock_1_out, d_ff_1_qn,
       d_ff_2_qn, d_ff_3_qn, nor_1_out, or_1_out, or_2_out, or_3_out, or_4_out, or_5_out, or_6_out, t_ff_1_q,
       t_ff_2_q, t_ff_3_q, t_ff_4_q, t_ff_5_q, t_ff_6_q, t_ff_7_q, xor_1_out;
  wire [2:0] d_ff_3_q;
  wire [7:0] xor_2_out;

  or or_1 (or_1_out, ~enable, alt);  // OR_Gate
  D_Flip_Flop d_ff_1 (.D(or_1_out), .clk(nor_1_out), .Q(d_ff_3_q[2]), .Qn(d_ff_1_qn));  // open: preset, reset
  D_Flip_Flop d_ff_2 (.D(or_2_out), .clk(nor_1_out), .Q(d_ff_3_q[1]), .Qn(d_ff_2_qn));  // open: preset, reset
  or or_2 (or_2_out, ~enable, and_1_out);  // OR_Gate
  and and_1 (and_1_out, ~alt, d_ff_1_qn, d_ff_3_q[0]);  // AND_Gate
  D_Flip_Flop d_ff_3 (.D(or_3_out), .clk(nor_1_out), .Q(d_ff_3_q[0]), .Qn(d_ff_3_qn));  // open: preset, reset
  and and_2 (and_2_out, ~alt, d_ff_1_qn, d_ff_2_qn);  // AND_Gate
  and and_3 (and_3_out, alt, d_ff_3_q[2], d_ff_2_qn, d_ff_3_qn);
  or or_3 (or_3_out, ~enable, and_2_out, and_3_out);  // OR_Gate
  Multiplexer #(.select(3), .width(8)) multiplexer_1 (
    .in0(Crveno), .in1(CrvenoZuto), .in2(Zuto), .in3(Zeleno), .in4(Treper), .in5(Treper), .out(out_9),
    .sel(d_ff_3_q));  // open: in6, in7
  and and_4 (and_4_out, d_ff_1_qn, d_ff_2_qn);
  or or_4 (or_4_out, and_4_out, and_5_out);
  and and_5 (and_5_out, d_ff_3_q[2], d_ff_3_qn);
  or or_5 (or_5_out, d_ff_3_q[2], d_ff_3_q[1]);
  xor xor_1 (xor_1_out, or_5_out, d_ff_3_q[0]);
  and and_6 (and_6_out, d_ff_3_qn, d_ff_3_q[2]);
  or or_6 (or_6_out, and_6_out, and_7_out);
  and and_7 (and_7_out, d_ff_3_q[0], d_ff_3_q[1], d_ff_1_qn);
  and and_8 (and_8_out, 1'b1, nor_1_out);
  T_Flip_Flop t_ff_1 (.T(1'b1), .clk(clock_1_out), .Q(t_ff_1_q), .Qn(out_8[0]), .preset(and_8_out));  // open: reset
  Clock clock_1 (.out(clock_1_out));
  LED led_1 (.in(or_4_out));
  LED led_2 (.in(xor_1_out));
  LED led_3 (.in(or_6_out));
  and and_9 (and_9_out, 1'b1, nor_1_out);
  T_Flip_Flop t_ff_2 (.T(1'b1), .clk(t_ff_1_q), .Q(t_ff_2_q), .Qn(out_8[1]), .preset(and_9_out));  // open: reset
  assign xor_2_out = out_8 ^ out_9;  // XOR_Gate xor_2, 8 bits wide
  and and_10 (and_10_out, 1'b1, nor_1_out);
  T_Flip_Flop t_ff_3 (.T(1'b1), .clk(t_ff_2_q), .Q(t_ff_3_q), .Qn(out_8[2]), .preset(and_10_out));  // open: reset
  nor nor_1 (nor_1_out, xor_2_out[3], xor_2_out[0], xor_2_out[1], xor_2_out[2], xor_2_out[4], xor_2_out[5], xor_2_out[6], xor_2_out[7]);
  and and_11 (and_11_out, 1'b1, nor_1_out);
  T_Flip_Flop t_ff_4 (.T(1'b1), .clk(t_ff_3_q), .Q(t_ff_4_q), .Qn(out_8[3]), .preset(and_11_out));  // open: reset
  and and_12 (and_12_out, 1'b1, nor_1_out);
  T_Flip_Flop t_ff_5 (.T(1'b1), .clk(t_ff_4_q), .Q(t_ff_5_q), .Qn(out_8[4]), .preset(and_12_out));  // open: reset
  and and_13 (and_13_out, 1'b1, nor_1_out);
  T_Flip_Flop t_ff_6 (.T(1'b1), .clk(t_ff_5_q), .Q(t_ff_6_q), .Qn(out_8[5]), .preset(and_13_out));  // open: reset
  and and_14 (and_14_out, 1'b1, nor_1_out);
  T_Flip_Flop t_ff_7 (.T(1'b1), .clk(t_ff_6_q), .Q(t_ff_7_q), .Qn(out_8[6]), .preset(and_14_out));  // open: reset
  and and_15 (and_15_out, 1'b1, nor_1_out);
  T_Flip_Flop t_ff_8 (.T(1'b1), .clk(t_ff_7_q), .Qn(out_8[7]), .preset(and_15_out));  // open: Q, reset
endmodule

module OgledniProcesor_ALU1bit (
  input  A,
  input  B,
  input  Cin,
  input  F1,
  input  F0,
  output Result,
  output Cout
);

  wire and_1_out, and_2_out, and_3_out, not_1_out, or_1_out, xor_1_out, xor_2_out;

  xor xor_1 (xor_1_out, A, B);
  xor xor_2 (xor_2_out, xor_1_out, Cin);
  and and_1 (and_1_out, A, B);
  and and_2 (and_2_out, Cin, xor_1_out);
  or or_1 (or_1_out, and_1_out, and_2_out);
  and and_3 (and_3_out, ~F0, ~F1);  // AND_Gate
  not not_1 (not_1_out, A);
  and and_4 (Cout, or_1_out, and_3_out);
  Multiplexer #(.select(2)) multiplexer_1 (
    .in0(xor_2_out), .in1(and_1_out), .in2(A), .in3(not_1_out), .out(Result), .sel({F1, F0}));
endmodule

module OgledniProcesor_ALU16bit (
  input  [15:0] A,
  input  [15:0] B,
  input  [1:0] F,
  output [15:0] Result,
  output N,
  output z
);

  wire ogledniprocesor_alu1bit_1_cout, ogledniprocesor_alu1bit_2_cout, ogledniprocesor_alu1bit_3_cout,
       ogledniprocesor_alu1bit_4_cout, ogledniprocesor_alu1bit_5_cout, ogledniprocesor_alu1bit_6_cout,
       ogledniprocesor_alu1bit_7_cout, ogledniprocesor_alu1bit_8_cout, ogledniprocesor_alu1bit_9_cout,
       ogledniprocesor_alu1bit_10_cout, ogledniprocesor_alu1bit_11_cout, ogledniprocesor_alu1bit_12_cout,
       ogledniprocesor_alu1bit_13_cout, ogledniprocesor_alu1bit_14_cout, ogledniprocesor_alu1bit_15_cout;

  // Probe on A
  // Probe on A
  // Probe on {N, Result[14:0]}
  // Probe on {N, Result[14:0]}
  nor nor_1 (z, N, Result[14], Result[13], Result[12], Result[11], Result[10], Result[9], Result[8], Result[7], Result[6], Result[5], Result[4], Result[3], Result[2], Result[1], Result[0]);
  OgledniProcesor_ALU1bit ogledniprocesor_alu1bit_1 (
    .A(A[0]), .B(B[0]), .Cin(1'b0), .F1(F[1]), .F0(F[0]), .Result(Result[0]),
    .Cout(ogledniprocesor_alu1bit_1_cout));
  OgledniProcesor_ALU1bit ogledniprocesor_alu1bit_2 (
    .A(A[1]), .B(B[1]), .Cin(ogledniprocesor_alu1bit_1_cout), .F1(F[1]), .F0(F[0]), .Result(Result[1]),
    .Cout(ogledniprocesor_alu1bit_2_cout));
  OgledniProcesor_ALU1bit ogledniprocesor_alu1bit_3 (
    .A(A[2]), .B(B[2]), .Cin(ogledniprocesor_alu1bit_2_cout), .F1(F[1]), .F0(F[0]), .Result(Result[2]),
    .Cout(ogledniprocesor_alu1bit_3_cout));
  // Probe on B
  // Probe on B
  OgledniProcesor_ALU1bit ogledniprocesor_alu1bit_4 (
    .A(A[3]), .B(B[3]), .Cin(ogledniprocesor_alu1bit_3_cout), .F1(F[1]), .F0(F[0]), .Result(Result[3]),
    .Cout(ogledniprocesor_alu1bit_4_cout));
  OgledniProcesor_ALU1bit ogledniprocesor_alu1bit_5 (
    .A(A[4]), .B(B[4]), .Cin(ogledniprocesor_alu1bit_4_cout), .F1(F[1]), .F0(F[0]), .Result(Result[4]),
    .Cout(ogledniprocesor_alu1bit_5_cout));
  OgledniProcesor_ALU1bit ogledniprocesor_alu1bit_6 (
    .A(A[5]), .B(B[5]), .Cin(ogledniprocesor_alu1bit_5_cout), .F1(F[1]), .F0(F[0]), .Result(Result[5]),
    .Cout(ogledniprocesor_alu1bit_6_cout));
  OgledniProcesor_ALU1bit ogledniprocesor_alu1bit_7 (
    .A(A[6]), .B(B[6]), .Cin(ogledniprocesor_alu1bit_6_cout), .F1(F[1]), .F0(F[0]), .Result(Result[6]),
    .Cout(ogledniprocesor_alu1bit_7_cout));
  OgledniProcesor_ALU1bit ogledniprocesor_alu1bit_8 (
    .A(A[7]), .B(B[7]), .Cin(ogledniprocesor_alu1bit_7_cout), .F1(F[1]), .F0(F[0]), .Result(Result[7]),
    .Cout(ogledniprocesor_alu1bit_8_cout));
  OgledniProcesor_ALU1bit ogledniprocesor_alu1bit_9 (
    .A(A[8]), .B(B[8]), .Cin(ogledniprocesor_alu1bit_8_cout), .F1(F[1]), .F0(F[0]), .Result(Result[8]),
    .Cout(ogledniprocesor_alu1bit_9_cout));
  OgledniProcesor_ALU1bit ogledniprocesor_alu1bit_10 (
    .A(A[9]), .B(B[9]), .Cin(ogledniprocesor_alu1bit_9_cout), .F1(F[1]), .F0(F[0]), .Result(Result[9]),
    .Cout(ogledniprocesor_alu1bit_10_cout));
  OgledniProcesor_ALU1bit ogledniprocesor_alu1bit_11 (
    .A(A[10]), .B(B[10]), .Cin(ogledniprocesor_alu1bit_10_cout), .F1(F[1]), .F0(F[0]), .Result(Result[10]),
    .Cout(ogledniprocesor_alu1bit_11_cout));
  OgledniProcesor_ALU1bit ogledniprocesor_alu1bit_12 (
    .A(A[11]), .B(B[11]), .Cin(ogledniprocesor_alu1bit_11_cout), .F1(F[1]), .F0(F[0]), .Result(Result[11]),
    .Cout(ogledniprocesor_alu1bit_12_cout));
  OgledniProcesor_ALU1bit ogledniprocesor_alu1bit_13 (
    .A(A[12]), .B(B[12]), .Cin(ogledniprocesor_alu1bit_12_cout), .F1(F[1]), .F0(F[0]), .Result(Result[12]),
    .Cout(ogledniprocesor_alu1bit_13_cout));
  OgledniProcesor_ALU1bit ogledniprocesor_alu1bit_14 (
    .A(A[13]), .B(B[13]), .Cin(ogledniprocesor_alu1bit_13_cout), .F1(F[1]), .F0(F[0]), .Result(Result[13]),
    .Cout(ogledniprocesor_alu1bit_14_cout));
  OgledniProcesor_ALU1bit ogledniprocesor_alu1bit_15 (
    .A(A[14]), .B(B[14]), .Cin(ogledniprocesor_alu1bit_14_cout), .F1(F[1]), .F0(F[0]), .Result(Result[14]),
    .Cout(ogledniprocesor_alu1bit_15_cout));
  OgledniProcesor_ALU1bit ogledniprocesor_alu1bit_16 (
    .A(A[15]), .B(B[15]), .Cin(ogledniprocesor_alu1bit_15_cout), .F1(F[1]), .F0(F[0]), .Result(N));  // open: Cout

  assign Result[15] = N;

  // Other names for the same wires on the sheet: R0 = Result[0]; R1 = Result[1]; R2 = Result[2]; R3 = Result[3];
  //   R4 = Result[4]; R5 = Result[5]; R6 = Result[6]; R7 = Result[7]; R8 = Result[8]; R9 = Result[9];
  //   R10 = Result[10]; R11 = Result[11]; R12 = Result[12]; R13 = Result[13]; R14 = Result[14]; R15 = N
endmodule

module OgledniProcesor_Shifter (
  input  [15:0] ALU_Out,
  input  [1:0] S,
  output [15:0] C
);

  wire and_1_out, and_2_out, and_3_out, and_4_out, and_5_out, and_6_out, and_7_out, and_8_out, and_9_out,
       and_10_out, and_11_out, and_12_out, and_13_out, and_14_out, and_15_out, and_16_out, and_17_out,
       and_18_out, and_19_out, and_20_out, and_21_out, and_22_out, and_23_out, and_24_out, and_25_out,
       and_26_out, and_27_out, and_28_out, and_29_out, and_30_out, and_31_out, and_32_out, and_33_out,
       and_34_out, and_35_out, and_36_out, and_37_out, and_38_out, and_39_out, and_40_out, and_41_out,
       and_42_out, and_43_out, and_44_out, and_45_out, and_46_out, and_47_out, and_48_out, and_49_out,
       not_1_out, not_2_out;

  not not_1 (not_1_out, S[1]);
  and and_1 (and_1_out, not_1_out, not_2_out);
  and and_2 (and_2_out, not_1_out, S[0]);
  and and_3 (and_3_out, S[1], not_2_out);
  not not_2 (not_2_out, S[0]);
  and and_4 (and_4_out, and_1_out, ALU_Out[15]);
  and and_5 (and_5_out, and_2_out, ALU_Out[15]);
  or or_1 (C[15], and_4_out, and_5_out, and_6_out);
  and and_6 (and_6_out, and_3_out, ALU_Out[14]);
  and and_7 (and_7_out, and_1_out, ALU_Out[14]);
  and and_8 (and_8_out, and_2_out, ALU_Out[14]);
  or or_2 (C[14], and_5_out, and_7_out, and_9_out);
  and and_9 (and_9_out, and_3_out, ALU_Out[13]);
  and and_10 (and_10_out, and_1_out, ALU_Out[13]);
  and and_11 (and_11_out, and_2_out, ALU_Out[13]);
  or or_3 (C[13], and_8_out, and_10_out, and_12_out);
  and and_12 (and_12_out, and_3_out, ALU_Out[12]);
  and and_13 (and_13_out, and_1_out, ALU_Out[12]);
  or or_4 (C[12], and_11_out, and_13_out, and_14_out);
  and and_14 (and_14_out, and_3_out, ALU_Out[11]);
  and and_15 (and_15_out, and_2_out, ALU_Out[12]);
  and and_16 (and_16_out, and_1_out, ALU_Out[11]);
  or or_5 (C[11], and_15_out, and_16_out, and_18_out);
  and and_17 (and_17_out, and_2_out, ALU_Out[11]);
  and and_18 (and_18_out, and_3_out, ALU_Out[10]);
  and and_19 (and_19_out, and_1_out, ALU_Out[10]);
  or or_6 (C[10], and_17_out, and_19_out, and_21_out);
  and and_20 (and_20_out, and_2_out, ALU_Out[10]);
  and and_21 (and_21_out, and_3_out, ALU_Out[9]);
  and and_22 (and_22_out, and_1_out, ALU_Out[9]);
  or or_7 (C[9], and_20_out, and_22_out, and_24_out);
  and and_23 (and_23_out, and_2_out, ALU_Out[9]);
  and and_24 (and_24_out, and_3_out, ALU_Out[8]);
  and and_25 (and_25_out, and_1_out, ALU_Out[8]);
  or or_8 (C[8], and_23_out, and_25_out, and_27_out);
  and and_26 (and_26_out, and_2_out, ALU_Out[8]);
  and and_27 (and_27_out, and_3_out, ALU_Out[7]);
  and and_28 (and_28_out, and_1_out, ALU_Out[7]);
  and and_29 (and_29_out, and_2_out, ALU_Out[7]);
  or or_9 (C[7], and_26_out, and_28_out, and_30_out);
  and and_30 (and_30_out, and_3_out, ALU_Out[6]);
  and and_31 (and_31_out, and_1_out, ALU_Out[6]);
  and and_32 (and_32_out, and_2_out, ALU_Out[6]);
  or or_10 (C[6], and_29_out, and_31_out, and_33_out);
  and and_33 (and_33_out, and_3_out, ALU_Out[5]);
  and and_34 (and_34_out, and_1_out, ALU_Out[5]);
  and and_35 (and_35_out, and_2_out, ALU_Out[5]);
  or or_11 (C[5], and_32_out, and_34_out, and_36_out);
  and and_36 (and_36_out, and_3_out, ALU_Out[4]);
  and and_37 (and_37_out, and_1_out, ALU_Out[4]);
  or or_12 (C[4], and_35_out, and_37_out, and_39_out);
  and and_38 (and_38_out, and_2_out, ALU_Out[4]);
  and and_39 (and_39_out, and_3_out, ALU_Out[3]);
  and and_40 (and_40_out, and_1_out, ALU_Out[3]);
  or or_13 (C[3], and_38_out, and_40_out, and_42_out);
  and and_41 (and_41_out, and_2_out, ALU_Out[3]);
  and and_42 (and_42_out, and_3_out, ALU_Out[2]);
  and and_43 (and_43_out, and_1_out, ALU_Out[2]);
  or or_14 (C[2], and_41_out, and_43_out, and_45_out);
  and and_44 (and_44_out, and_2_out, ALU_Out[2]);
  and and_45 (and_45_out, and_3_out, ALU_Out[1]);
  and and_46 (and_46_out, and_1_out, ALU_Out[1]);
  or or_15 (C[1], and_44_out, and_46_out, and_48_out);
  and and_47 (and_47_out, and_2_out, ALU_Out[1]);
  and and_48 (and_48_out, and_3_out, ALU_Out[0]);
  and and_49 (and_49_out, and_1_out, ALU_Out[0]);
  or or_16 (C[0], and_47_out, and_49_out);

  // Notes on the sheet:
  //   BEZ POMJERANJA
  //   POMJERANJE DESNO
  //   POMJERANJE LIJEVO
endmodule

module OgledniProcesor_ALUiShifter (
  input  [15:0] A,
  input  [15:0] B,
  input  [1:0] F,
  input  [1:0] S,
  output N,
  output Z,
  output [15:0] C
);

  wire [15:0] ogledniprocesor_alu16bit_1_result;

  // Probe on A
  // Probe on A
  // Probe on B
  // Probe on B
  OgledniProcesor_ALU16bit ogledniprocesor_alu16bit_1 (
    .A(A), .B(B), .F(F), .N(N), .z(Z), .Result(ogledniprocesor_alu16bit_1_result));
  OgledniProcesor_Shifter ogledniprocesor_shifter_1 (.ALU_Out(ogledniprocesor_alu16bit_1_result), .S(S), .C(C));
  // Probe on C
  // Probe on C
endmodule

module OgledniProcesor_Registar16bit (
  input  [15:0] U,
  input  CLK,
  input  Reset,
  output [15:0] I
);

  // Probe on U
  // Probe on U
  // Probe on I
  // Probe on I
  D_Flip_Flop d_ff_1 (.D(U[15]), .clk(CLK), .Q(I[15]), .reset(Reset));  // open: Qn, preset
  D_Flip_Flop d_ff_2 (.D(U[14]), .clk(CLK), .Q(I[14]), .reset(Reset));  // open: Qn, preset
  D_Flip_Flop d_ff_3 (.D(U[13]), .clk(CLK), .Q(I[13]), .reset(Reset));  // open: Qn, preset
  D_Flip_Flop d_ff_4 (.D(U[12]), .clk(CLK), .Q(I[12]), .reset(Reset));  // open: Qn, preset
  D_Flip_Flop d_ff_5 (.D(U[11]), .clk(CLK), .Q(I[11]), .reset(Reset));  // open: Qn, preset
  D_Flip_Flop d_ff_6 (.D(U[10]), .clk(CLK), .Q(I[10]), .reset(Reset));  // open: Qn, preset
  D_Flip_Flop d_ff_7 (.D(U[9]), .clk(CLK), .Q(I[9]), .reset(Reset));  // open: Qn, preset
  D_Flip_Flop d_ff_8 (.D(U[8]), .clk(CLK), .Q(I[8]), .reset(Reset));  // open: Qn, preset
  D_Flip_Flop d_ff_9 (.D(U[7]), .clk(CLK), .Q(I[7]), .reset(Reset));  // open: Qn, preset
  D_Flip_Flop d_ff_10 (.D(U[6]), .clk(CLK), .Q(I[6]), .reset(Reset));  // open: Qn, preset
  D_Flip_Flop d_ff_11 (.D(U[5]), .clk(CLK), .Q(I[5]), .reset(Reset));  // open: Qn, preset
  D_Flip_Flop d_ff_12 (.D(U[4]), .clk(CLK), .Q(I[4]), .reset(Reset));  // open: Qn, preset
  D_Flip_Flop d_ff_13 (.D(U[3]), .clk(CLK), .Q(I[3]), .reset(Reset));  // open: Qn, preset
  D_Flip_Flop d_ff_14 (.D(U[2]), .clk(CLK), .Q(I[2]), .reset(Reset));  // open: Qn, preset
  D_Flip_Flop d_ff_15 (.D(U[1]), .clk(CLK), .Q(I[1]), .reset(Reset));  // open: Qn, preset
  D_Flip_Flop d_ff_16 (.D(U[0]), .clk(CLK), .Q(I[0]), .reset(Reset));  // open: Qn, preset
endmodule

module OgledniProcesor_OziceniRegistar16bit (
  input  [15:0] U,
  output [15:0] I
);

  wire [15:0] not_1_out;

  // Probe on U
  // Probe on U
  assign not_1_out = ~U;  // NOT_Gate not_1, 16 bits wide
  // Probe on I
  // Probe on I
  D_Flip_Flop d_ff_1 (.Q(I[15]), .preset(U[15]), .reset(not_1_out[15]));  // open: D, clk, Qn
  D_Flip_Flop d_ff_2 (.Q(I[14]), .preset(U[14]), .reset(not_1_out[14]));  // open: D, clk, Qn
  D_Flip_Flop d_ff_3 (.Q(I[13]), .preset(U[13]), .reset(not_1_out[13]));  // open: D, clk, Qn
  D_Flip_Flop d_ff_4 (.Q(I[12]), .preset(U[12]), .reset(not_1_out[12]));  // open: D, clk, Qn
  D_Flip_Flop d_ff_5 (.Q(I[11]), .preset(U[11]), .reset(not_1_out[11]));  // open: D, clk, Qn
  D_Flip_Flop d_ff_6 (.Q(I[10]), .preset(U[10]), .reset(not_1_out[10]));  // open: D, clk, Qn
  D_Flip_Flop d_ff_7 (.Q(I[9]), .preset(U[9]), .reset(not_1_out[9]));  // open: D, clk, Qn
  D_Flip_Flop d_ff_8 (.Q(I[8]), .preset(U[8]), .reset(not_1_out[8]));  // open: D, clk, Qn
  D_Flip_Flop d_ff_9 (.Q(I[7]), .preset(U[7]), .reset(not_1_out[7]));  // open: D, clk, Qn
  D_Flip_Flop d_ff_10 (.Q(I[6]), .preset(U[6]), .reset(not_1_out[6]));  // open: D, clk, Qn
  D_Flip_Flop d_ff_11 (.Q(I[5]), .preset(U[5]), .reset(not_1_out[5]));  // open: D, clk, Qn
  D_Flip_Flop d_ff_12 (.Q(I[4]), .preset(U[4]), .reset(not_1_out[4]));  // open: D, clk, Qn
  D_Flip_Flop d_ff_13 (.Q(I[3]), .preset(U[3]), .reset(not_1_out[3]));  // open: D, clk, Qn
  D_Flip_Flop d_ff_14 (.Q(I[2]), .preset(U[2]), .reset(not_1_out[2]));  // open: D, clk, Qn
  D_Flip_Flop d_ff_15 (.Q(I[1]), .preset(U[1]), .reset(not_1_out[1]));  // open: D, clk, Qn
  D_Flip_Flop d_ff_16 (.Q(I[0]), .preset(U[0]), .reset(not_1_out[0]));  // open: D, clk, Qn
endmodule

module OgledniProcesor_RegistarskaDatoteka (
  input  [15:0] sC,
  input  [3:0] srcA,
  input  [3:0] srcB,
  input  enC,
  input  [3:0] dst,
  input  Reset,
  output [15:0] sA,
  output [15:0] sB,
  output [15:0] PC,
  output [15:0] ACC,
  output [15:0] SP,
  output [15:0] IR,
  output [15:0] TIR,
  output [15:0] A,
  output [15:0] B,
  output [15:0] C,
  output [15:0] D,
  output [15:0] E,
  output [15:0] F
);

  wire decoder_1_out0, decoder_1_out1, decoder_1_out2, decoder_1_out3, decoder_1_out4, decoder_1_out10,
       decoder_1_out11, decoder_1_out12, decoder_1_out13, decoder_1_out14, decoder_1_out15;
  wire [15:0] Reg_Amask_i, Reg_Minus1_i, Reg_Plus1_i, Reg_Smask_i, Reg_Zero_i;

  // Probe on sC
  Decoder #(.select(4)) decoder_1 (
    .out0(decoder_1_out0), .out1(decoder_1_out1), .out2(decoder_1_out2), .out3(decoder_1_out3),
    .out4(decoder_1_out4), .out10(decoder_1_out10), .out11(decoder_1_out11), .out12(decoder_1_out12),
    .out13(decoder_1_out13), .out14(decoder_1_out14), .out15(decoder_1_out15), .sel(dst), .en(enC));  // open: out5, out6, out7, out8, out9
  OgledniProcesor_Registar16bit Reg_PC (.CLK(decoder_1_out0), .Reset(Reset), .U(sC), .I(PC));
  OgledniProcesor_Registar16bit Reg_ACC (.CLK(decoder_1_out1), .Reset(Reset), .U(sC), .I(ACC));
  OgledniProcesor_Registar16bit Reg_SP (.CLK(decoder_1_out2), .Reset(Reset), .U(sC), .I(SP));
  OgledniProcesor_Registar16bit Reg_IR (.CLK(decoder_1_out3), .Reset(Reset), .U(sC), .I(IR));
  OgledniProcesor_Registar16bit Reg_TIR (.CLK(decoder_1_out4), .Reset(Reset), .U(sC), .I(TIR));
  OgledniProcesor_OziceniRegistar16bit Reg_Zero (.U({16{1'b0}}), .I(Reg_Zero_i));
  OgledniProcesor_OziceniRegistar16bit Reg_Plus1 (.U(16'h1), .I(Reg_Plus1_i));
  OgledniProcesor_OziceniRegistar16bit Reg_Minus1 (.U({16{1'b1}}), .I(Reg_Minus1_i));
  OgledniProcesor_OziceniRegistar16bit Reg_Amask (.U(16'hfff), .I(Reg_Amask_i));
  OgledniProcesor_OziceniRegistar16bit Reg_Smask (.U(16'hff), .I(Reg_Smask_i));
  OgledniProcesor_Registar16bit Reg_A (.CLK(decoder_1_out10), .Reset(Reset), .U(sC), .I(A));
  OgledniProcesor_Registar16bit Reg_B (.CLK(decoder_1_out11), .Reset(Reset), .U(sC), .I(B));
  OgledniProcesor_Registar16bit Reg_C (.CLK(decoder_1_out12), .Reset(Reset), .U(sC), .I(C));
  OgledniProcesor_Registar16bit Reg_D (.CLK(decoder_1_out13), .Reset(Reset), .U(sC), .I(D));
  OgledniProcesor_Registar16bit Reg_E (.CLK(decoder_1_out14), .Reset(Reset), .U(sC), .I(E));
  OgledniProcesor_Registar16bit Reg_F (.CLK(decoder_1_out15), .Reset(Reset), .U(sC), .I(F));
  // Probe on sA
  Multiplexer #(.enable("true"), .select(4), .width(16)) multiplexer_1 (
    .in0(PC), .in1(ACC), .in2(SP), .in3(IR), .in4(TIR), .in5(Reg_Zero_i), .in6(Reg_Plus1_i),
    .in7(Reg_Minus1_i), .in8(Reg_Amask_i), .in9(Reg_Smask_i), .in10(A), .in11(B), .in12(C), .in13(D),
    .in14(E), .in15(F), .out(sA), .sel(srcA));  // open: en
  // Probe on sB
  Multiplexer #(.enable("true"), .select(4), .width(16)) multiplexer_2 (
    .in0(PC), .in1(ACC), .in2(SP), .in3(IR), .in4(TIR), .in5(Reg_Zero_i), .in6(Reg_Plus1_i),
    .in7(Reg_Minus1_i), .in8(Reg_Amask_i), .in9(Reg_Smask_i), .in10(A), .in11(B), .in12(C), .in13(D),
    .in14(E), .in15(F), .out(sB), .sel(srcB));  // open: en
endmodule

module OgledniProcesor_ALUiReg (
  input  [3:0] dst,
  input  [3:0] srcA,
  input  [3:0] srcB,
  input  A,
  input  [1:0] F,
  input  [1:0] S
);

  wire clk_A, clk_B, clk_C, clk_D, clock_1_out, Power;
  wire [3:0] ogledniprocesor_registar16bit_2_i_2;
  wire [11:0] ogledniprocesor_registar16bit_2_i;
  wire [15:0] MBR_i, multiplexer_1_out, ogledniprocesor_aluishifter_1_c, ogledniprocesor_registar16bit_1_i,
       ogledniprocesor_registarskadatoteka_1_a, ogledniprocesor_registarskadatoteka_1_acc,
       ogledniprocesor_registarskadatoteka_1_b, ogledniprocesor_registarskadatoteka_1_c,
       ogledniprocesor_registarskadatoteka_1_d, ogledniprocesor_registarskadatoteka_1_e,
       ogledniprocesor_registarskadatoteka_1_f, ogledniprocesor_registarskadatoteka_1_ir,
       ogledniprocesor_registarskadatoteka_1_pc, ogledniprocesor_registarskadatoteka_1_sa,
       ogledniprocesor_registarskadatoteka_1_sb, ogledniprocesor_registarskadatoteka_1_sp,
       ogledniprocesor_registarskadatoteka_1_tir, undriven;

  Clock clock_1 (.out(clock_1_out));
  Button u_Power (.out(Power));
  OgledniProcesor_Clk ogledniprocesor_clk_1 (
    .CLK(clock_1_out), .Reset(Power), .clkA(clk_A), .clkB(clk_B), .clkC(clk_C), .clkD(clk_D));
  OgledniProcesor_Registar12bit MAR (.CLK(Power), .Reset(clk_C), .U(ogledniprocesor_registar16bit_2_i));  // open: I
  OgledniProcesor_Registar16bit MBR (.CLK(clk_D), .Reset(Power), .U(undriven), .I(MBR_i));
  // Probe on ogledniprocesor_registarskadatoteka_1_pc
  // Probe on ogledniprocesor_registarskadatoteka_1_a
  // Probe on ogledniprocesor_registarskadatoteka_1_acc
  // Probe on ogledniprocesor_registarskadatoteka_1_b
  // Probe on ogledniprocesor_registarskadatoteka_1_sp
  // Probe on ogledniprocesor_registarskadatoteka_1_c
  // Probe on ogledniprocesor_registarskadatoteka_1_ir
  // Probe on ogledniprocesor_registarskadatoteka_1_d
  // Probe on ogledniprocesor_registarskadatoteka_1_tir
  // Probe on ogledniprocesor_registarskadatoteka_1_e
  // Probe on ogledniprocesor_registarskadatoteka_1_f
  OgledniProcesor_RegistarskaDatoteka ogledniprocesor_registarskadatoteka_1 (
    .srcB(srcB), .sC(ogledniprocesor_aluishifter_1_c), .enC(clk_D), .dst(dst), .Reset(Power), .srcA(srcA),
    .sB(ogledniprocesor_registarskadatoteka_1_sb), .PC(ogledniprocesor_registarskadatoteka_1_pc),
    .ACC(ogledniprocesor_registarskadatoteka_1_acc), .SP(ogledniprocesor_registarskadatoteka_1_sp),
    .IR(ogledniprocesor_registarskadatoteka_1_ir), .TIR(ogledniprocesor_registarskadatoteka_1_tir),
    .A(ogledniprocesor_registarskadatoteka_1_a), .B(ogledniprocesor_registarskadatoteka_1_b),
    .C(ogledniprocesor_registarskadatoteka_1_c), .D(ogledniprocesor_registarskadatoteka_1_d),
    .E(ogledniprocesor_registarskadatoteka_1_e), .F(ogledniprocesor_registarskadatoteka_1_f),
    .sA(ogledniprocesor_registarskadatoteka_1_sa));
  // Probe on ogledniprocesor_registarskadatoteka_1_sa
  OgledniProcesor_Registar16bit ogledniprocesor_registar16bit_1 (
    .CLK(clk_B), .U(ogledniprocesor_registarskadatoteka_1_sa), .I(ogledniprocesor_registar16bit_1_i));  // open: Reset
  // Probe on ogledniprocesor_registar16bit_1_i
  Multiplexer #(.width(16)) multiplexer_1 (
    .in0(ogledniprocesor_registar16bit_1_i), .in1(MBR_i), .out(multiplexer_1_out), .sel(A));
  // Probe on ogledniprocesor_aluishifter_1_c
  // Probe on ogledniprocesor_registarskadatoteka_1_sb
  OgledniProcesor_Registar16bit ogledniprocesor_registar16bit_2 (
    .CLK(clk_B), .U(ogledniprocesor_registarskadatoteka_1_sb),
    .I({ogledniprocesor_registar16bit_2_i_2, ogledniprocesor_registar16bit_2_i}));  // open: Reset
  // Probe on {ogledniprocesor_registar16bit_2_i_2, ogledniprocesor_registar16bit_2_i}
  OgledniProcesor_ALUiShifter ogledniprocesor_aluishifter_1 (
    .A(multiplexer_1_out), .B({ogledniprocesor_registar16bit_2_i_2, ogledniprocesor_registar16bit_2_i}),
    .F(F), .S(S), .C(ogledniprocesor_aluishifter_1_c));  // open: N, Z
endmodule

module OgledniProcesor_Clk (
  input  CLK,
  input  Reset,
  output clkA,
  output clkB,
  output clkC,
  output clkD
);

  D_Flip_Flop d_ff_1 (.D(clkD), .clk(CLK), .Q(clkA), .reset(Reset));  // open: Qn, preset
  D_Flip_Flop d_ff_2 (.D(clkA), .clk(CLK), .Q(clkB), .reset(Reset));  // open: Qn, preset
  D_Flip_Flop d_ff_3 (.D(clkB), .clk(CLK), .Q(clkC), .reset(Reset));  // open: Qn, preset
  D_Flip_Flop d_ff_4 (.D(clkC), .clk(CLK), .Q(clkD), .preset(Reset));  // open: Qn, reset
endmodule

module OgledniProcesor_Registar12bit (
  input  [11:0] U,
  input  CLK,
  input  Reset,
  output [11:0] I
);

  // Probe on U
  // Probe on U
  // Probe on I
  // Probe on I
  D_Flip_Flop d_ff_1 (.D(U[11]), .clk(CLK), .Q(I[11]), .reset(Reset));  // open: Qn, preset
  D_Flip_Flop d_ff_2 (.D(U[10]), .clk(CLK), .Q(I[10]), .reset(Reset));  // open: Qn, preset
  D_Flip_Flop d_ff_3 (.D(U[9]), .clk(CLK), .Q(I[9]), .reset(Reset));  // open: Qn, preset
  D_Flip_Flop d_ff_4 (.D(U[8]), .clk(CLK), .Q(I[8]), .reset(Reset));  // open: Qn, preset
  D_Flip_Flop d_ff_5 (.D(U[7]), .clk(CLK), .Q(I[7]), .reset(Reset));  // open: Qn, preset
  D_Flip_Flop d_ff_6 (.D(U[6]), .clk(CLK), .Q(I[6]), .reset(Reset));  // open: Qn, preset
  D_Flip_Flop d_ff_7 (.D(U[5]), .clk(CLK), .Q(I[5]), .reset(Reset));  // open: Qn, preset
  D_Flip_Flop d_ff_8 (.D(U[4]), .clk(CLK), .Q(I[4]), .reset(Reset));  // open: Qn, preset
  D_Flip_Flop d_ff_9 (.D(U[3]), .clk(CLK), .Q(I[3]), .reset(Reset));  // open: Qn, preset
  D_Flip_Flop d_ff_10 (.D(U[2]), .clk(CLK), .Q(I[2]), .reset(Reset));  // open: Qn, preset
  D_Flip_Flop d_ff_11 (.D(U[1]), .clk(CLK), .Q(I[1]), .reset(Reset));  // open: Qn, preset
  D_Flip_Flop d_ff_12 (.D(U[0]), .clk(CLK), .Q(I[0]), .reset(Reset));  // open: Qn, preset
endmodule

module Dff_with_CE (
  input  D,
  input  CE,
  input  CLK,
  output Q
);

  wire multiplexer_1_out;

  D_Flip_Flop d_ff_1 (.D(multiplexer_1_out), .clk(CLK), .Q(Q));  // open: Qn, preset, reset
  Multiplexer multiplexer_1 (.in0(Q), .in1(D), .out(multiplexer_1_out), .sel(CE));

  // Notes on the sheet:
  //   Ako je CE=1, FF se okida uzlaznom ivicom sata
endmodule

module ShReg_SISO (
  input  S_In,
  input  Shift,
  input  Clk,
  output S_Out
);

  wire dff_with_ce_1_q, dff_with_ce_2_q, dff_with_ce_3_q, dff_with_ce_4_q, dff_with_ce_5_q, dff_with_ce_6_q,
       dff_with_ce_7_q;

  Dff_with_CE dff_with_ce_1 (.D(S_In), .CE(Shift), .CLK(Clk), .Q(dff_with_ce_1_q));
  Dff_with_CE dff_with_ce_2 (.D(dff_with_ce_1_q), .CE(Shift), .CLK(Clk), .Q(dff_with_ce_2_q));
  Dff_with_CE dff_with_ce_3 (.D(dff_with_ce_2_q), .CE(Shift), .CLK(Clk), .Q(dff_with_ce_3_q));
  Dff_with_CE dff_with_ce_4 (.D(dff_with_ce_3_q), .CE(Shift), .CLK(Clk), .Q(dff_with_ce_4_q));
  Dff_with_CE dff_with_ce_5 (.D(dff_with_ce_4_q), .CE(Shift), .CLK(Clk), .Q(dff_with_ce_5_q));
  Dff_with_CE dff_with_ce_6 (.D(dff_with_ce_5_q), .CE(Shift), .CLK(Clk), .Q(dff_with_ce_6_q));
  Dff_with_CE dff_with_ce_7 (.D(dff_with_ce_6_q), .CE(Shift), .CLK(Clk), .Q(dff_with_ce_7_q));
  Dff_with_CE dff_with_ce_8 (.D(dff_with_ce_7_q), .CE(Shift), .CLK(Clk), .Q(S_Out));
endmodule

module ShReg_SIPO (
  input  S_In,
  input  Shift,
  input  Clk,
  output [7:0] P_Out
);

  Dff_with_CE dff_with_ce_1 (.D(S_In), .CE(Shift), .CLK(Clk), .Q(P_Out[0]));
  Dff_with_CE dff_with_ce_2 (.D(P_Out[0]), .CE(Shift), .CLK(Clk), .Q(P_Out[1]));
  Dff_with_CE dff_with_ce_3 (.D(P_Out[1]), .CE(Shift), .CLK(Clk), .Q(P_Out[2]));
  Dff_with_CE dff_with_ce_4 (.D(P_Out[2]), .CE(Shift), .CLK(Clk), .Q(P_Out[3]));
  Dff_with_CE dff_with_ce_5 (.D(P_Out[3]), .CE(Shift), .CLK(Clk), .Q(P_Out[4]));
  Dff_with_CE dff_with_ce_6 (.D(P_Out[4]), .CE(Shift), .CLK(Clk), .Q(P_Out[5]));
  Dff_with_CE dff_with_ce_7 (.D(P_Out[5]), .CE(Shift), .CLK(Clk), .Q(P_Out[6]));
  Dff_with_CE dff_with_ce_8 (.D(P_Out[6]), .CE(Shift), .CLK(Clk), .Q(P_Out[7]));
endmodule

module ShReg_PISO (
  input  [7:0] P_In,
  input  Shift,
  input  Clk,
  output S_Out
);

  wire d_ff_1_q, d_ff_2_q, d_ff_3_q, d_ff_4_q, d_ff_5_q, d_ff_6_q, d_ff_7_q, multiplexer_1_out,
       multiplexer_2_out, multiplexer_3_out, multiplexer_4_out, multiplexer_5_out, multiplexer_6_out,
       multiplexer_7_out;

  D_Flip_Flop d_ff_1 (.D(P_In[0]), .clk(Clk), .Q(d_ff_1_q));  // open: Qn, preset, reset
  Multiplexer multiplexer_1 (.in0(P_In[1]), .in1(d_ff_1_q), .out(multiplexer_1_out), .sel(Shift));
  D_Flip_Flop d_ff_2 (.D(multiplexer_1_out), .clk(Clk), .Q(d_ff_2_q));  // open: Qn, preset, reset
  Multiplexer multiplexer_2 (.in0(P_In[2]), .in1(d_ff_2_q), .out(multiplexer_2_out), .sel(Shift));
  D_Flip_Flop d_ff_3 (.D(multiplexer_2_out), .clk(Clk), .Q(d_ff_3_q));  // open: Qn, preset, reset
  Multiplexer multiplexer_3 (.in0(P_In[3]), .in1(d_ff_3_q), .out(multiplexer_3_out), .sel(Shift));
  D_Flip_Flop d_ff_4 (.D(multiplexer_3_out), .clk(Clk), .Q(d_ff_4_q));  // open: Qn, preset, reset
  Multiplexer multiplexer_4 (.in0(P_In[4]), .in1(d_ff_4_q), .out(multiplexer_4_out), .sel(Shift));
  D_Flip_Flop d_ff_5 (.D(multiplexer_4_out), .clk(Clk), .Q(d_ff_5_q));  // open: Qn, preset, reset
  Multiplexer multiplexer_5 (.in0(P_In[5]), .in1(d_ff_5_q), .out(multiplexer_5_out), .sel(Shift));
  D_Flip_Flop d_ff_6 (.D(multiplexer_5_out), .clk(Clk), .Q(d_ff_6_q));  // open: Qn, preset, reset
  Multiplexer multiplexer_6 (.in0(P_In[6]), .in1(d_ff_6_q), .out(multiplexer_6_out), .sel(Shift));
  D_Flip_Flop d_ff_7 (.D(multiplexer_6_out), .clk(Clk), .Q(d_ff_7_q));  // open: Qn, preset, reset
  Multiplexer multiplexer_7 (.in0(P_In[7]), .in1(d_ff_7_q), .out(multiplexer_7_out), .sel(Shift));
  D_Flip_Flop d_ff_8 (.D(multiplexer_7_out), .clk(Clk), .Q(S_Out));  // open: Qn, preset, reset
endmodule

module ShReg_PIPO (
  input  [7:0] P_In,
  input  S_In,
  input  Shift,
  input  ParLoad,
  input  Clk,
  output [7:0] P_Out,
  output S_Out
);

  wire multiplexer_1_out, multiplexer_2_out, multiplexer_3_out, multiplexer_4_out, multiplexer_5_out,
       multiplexer_6_out, multiplexer_7_out, multiplexer_8_out;

  D_Flip_Flop d_ff_1 (.D(multiplexer_1_out), .clk(Clk), .Q(P_Out[0]));  // open: Qn, preset, reset
  Multiplexer #(.select(2)) multiplexer_1 (
    .in0(P_Out[0]), .in1(S_In), .in2(P_In[0]), .in3(S_In), .out(multiplexer_1_out), .sel({ParLoad, Shift}));
  D_Flip_Flop d_ff_2 (.D(multiplexer_2_out), .clk(Clk), .Q(P_Out[1]));  // open: Qn, preset, reset
  Multiplexer #(.select(2)) multiplexer_2 (
    .in0(P_Out[1]), .in1(P_Out[0]), .in2(P_In[1]), .in3(P_Out[0]), .out(multiplexer_2_out),
    .sel({ParLoad, Shift}));
  D_Flip_Flop d_ff_3 (.D(multiplexer_3_out), .clk(Clk), .Q(P_Out[2]));  // open: Qn, preset, reset
  Multiplexer #(.select(2)) multiplexer_3 (
    .in0(P_Out[2]), .in1(P_Out[1]), .in2(P_In[2]), .in3(P_Out[1]), .out(multiplexer_3_out),
    .sel({ParLoad, Shift}));
  D_Flip_Flop d_ff_4 (.D(multiplexer_4_out), .clk(Clk), .Q(P_Out[3]));  // open: Qn, preset, reset
  Multiplexer #(.select(2)) multiplexer_4 (
    .in0(P_Out[3]), .in1(P_Out[2]), .in2(P_In[3]), .in3(P_Out[2]), .out(multiplexer_4_out),
    .sel({ParLoad, Shift}));
  D_Flip_Flop d_ff_5 (.D(multiplexer_5_out), .clk(Clk), .Q(P_Out[4]));  // open: Qn, preset, reset
  Multiplexer #(.select(2)) multiplexer_5 (
    .in0(P_Out[4]), .in1(P_Out[3]), .in2(P_In[4]), .in3(P_Out[3]), .out(multiplexer_5_out),
    .sel({ParLoad, Shift}));
  Multiplexer #(.select(2)) multiplexer_6 (
    .in0(P_Out[5]), .in1(P_Out[4]), .in2(P_In[5]), .in3(P_Out[4]), .out(multiplexer_6_out),
    .sel({ParLoad, Shift}));
  D_Flip_Flop d_ff_6 (.D(multiplexer_6_out), .clk(Clk), .Q(P_Out[5]));  // open: Qn, preset, reset
  D_Flip_Flop d_ff_7 (.D(multiplexer_7_out), .clk(Clk), .Q(P_Out[6]));  // open: Qn, preset, reset
  Multiplexer #(.select(2)) multiplexer_7 (
    .in0(P_Out[6]), .in1(P_Out[5]), .in2(P_In[6]), .in3(P_Out[5]), .out(multiplexer_7_out),
    .sel({ParLoad, Shift}));
  D_Flip_Flop d_ff_8 (.D(multiplexer_8_out), .clk(Clk), .Q(P_Out[7]));  // open: Qn, preset, reset
  Multiplexer #(.select(2)) multiplexer_8 (
    .in0(P_Out[7]), .in1(P_Out[6]), .in2(P_In[7]), .in3(P_Out[6]), .out(multiplexer_8_out),
    .sel({ParLoad, Shift}));

  assign S_Out = P_Out[7];
endmodule

module ShReg_WithSide (
  input  [7:0] P_In,
  input  S_In,
  input  Shift,
  input  Side,
  input  ParLoad,
  input  Clk,
  output [7:0] P_Out,
  output S_Out
);

  wire and_1_out, multiplexer_1_out, multiplexer_2_out, multiplexer_3_out, multiplexer_4_out,
       multiplexer_5_out, multiplexer_6_out, multiplexer_7_out, multiplexer_8_out;
  wire [1:0] and_2_out;

  and and_1 (and_1_out, Shift, Side);
  and and_2 (and_2_out[0], Shift, ~ParLoad);  // AND_Gate
  or or_1 (and_2_out[1], and_1_out, ParLoad);
  D_Flip_Flop d_ff_1 (.D(multiplexer_1_out), .clk(Clk), .Q(P_Out[0]));  // open: Qn, preset, reset
  Multiplexer #(.select(2)) multiplexer_1 (
    .in0(P_Out[0]), .in1(S_In), .in2(P_In[0]), .in3(P_Out[1]), .out(multiplexer_1_out), .sel(and_2_out));
  D_Flip_Flop d_ff_2 (.D(multiplexer_2_out), .clk(Clk), .Q(P_Out[1]));  // open: Qn, preset, reset
  Multiplexer #(.select(2)) multiplexer_2 (
    .in0(P_Out[1]), .in1(P_Out[0]), .in2(P_In[1]), .in3(P_Out[2]), .out(multiplexer_2_out), .sel(and_2_out));
  D_Flip_Flop d_ff_3 (.D(multiplexer_3_out), .clk(Clk), .Q(P_Out[2]));  // open: Qn, preset, reset
  Multiplexer #(.select(2)) multiplexer_3 (
    .in0(P_Out[2]), .in1(P_Out[1]), .in2(P_In[2]), .in3(P_Out[3]), .out(multiplexer_3_out), .sel(and_2_out));
  D_Flip_Flop d_ff_4 (.D(multiplexer_4_out), .clk(Clk), .Q(P_Out[3]));  // open: Qn, preset, reset
  Multiplexer #(.select(2)) multiplexer_4 (
    .in0(P_Out[3]), .in1(P_Out[2]), .in2(P_In[3]), .in3(P_Out[4]), .out(multiplexer_4_out), .sel(and_2_out));
  D_Flip_Flop d_ff_5 (.D(multiplexer_5_out), .clk(Clk), .Q(P_Out[4]));  // open: Qn, preset, reset
  Multiplexer #(.select(2)) multiplexer_5 (
    .in0(P_Out[4]), .in1(P_Out[3]), .in2(P_In[4]), .in3(P_Out[5]), .out(multiplexer_5_out), .sel(and_2_out));
  Multiplexer #(.select(2)) multiplexer_6 (
    .in0(P_Out[5]), .in1(P_Out[4]), .in2(P_In[5]), .in3(P_Out[6]), .out(multiplexer_6_out), .sel(and_2_out));
  D_Flip_Flop d_ff_6 (.D(multiplexer_6_out), .clk(Clk), .Q(P_Out[5]));  // open: Qn, preset, reset
  D_Flip_Flop d_ff_7 (.D(multiplexer_7_out), .clk(Clk), .Q(P_Out[6]));  // open: Qn, preset, reset
  Multiplexer #(.select(2)) multiplexer_7 (
    .in0(P_Out[6]), .in1(P_Out[5]), .in2(P_In[6]), .in3(P_Out[7]), .out(multiplexer_7_out), .sel(and_2_out));
  // Probe on P_Out
  D_Flip_Flop d_ff_8 (.D(multiplexer_8_out), .clk(Clk), .Q(P_Out[7]));  // open: Qn, preset, reset
  Multiplexer #(.select(2)) multiplexer_8 (
    .in0(P_Out[7]), .in1(P_Out[6]), .in2(P_In[7]), .in3(S_In), .out(multiplexer_8_out), .sel(and_2_out));
  Multiplexer multiplexer_9 (.in0(P_Out[7]), .in1(P_Out[0]), .out(S_Out), .sel(Side));
endmodule
