// Logisim project z1.circ as structural Verilog: 1 circuit, main circuit main
module main (
  input  [2:0] ulaz,
  output [2:0] izlaz
);

  wire nor_1_out, not_1_out;

  nor nor_1 (nor_1_out, ulaz[0], ulaz[1]);
  xor xor_1 (izlaz[2], nor_1_out, not_1_out);
  not not_1 (not_1_out, ulaz[2]);
  xor xor_2 (izlaz[1], ulaz[0], ulaz[1]);

  assign izlaz[0] = ulaz[0];
endmodule
