// Logisim project z3.circ as structural Verilog
module fulladder (
  input  incarry,
  input  in1,
  input  in2,
  output out1,
  output outcarry
);

  wire and_1_out, and_2_out, xor_1_out;

  xor xor_1 (xor_1_out, in1, in2);
  and and_1 (and_1_out, in1, in2);
  xor xor_2 (out1, xor_1_out, incarry);
  and and_2 (and_2_out, incarry, xor_1_out);
  or or_1 (outcarry, and_2_out, and_1_out);
endmodule

module fulladderNAND (
  input  incarry,
  input  in1,
  input  in2,
  output out1,
  output outcarry
);

  wire nand_1_out, nand_2_out, nand_3_out, nand_4_out, xorprekonand_1_out_3;

  xorprekoNAND xorprekonand_1 (.in_1(in1), .in_2(in2), .out_3(xorprekonand_1_out_3));
  nand nand_1 (nand_1_out, in1, in2);
  nand nand_2 (nand_2_out, nand_1_out, nand_1_out);
  xorprekoNAND xorprekonand_2 (.in_1(xorprekonand_1_out_3), .in_2(incarry), .out_3(out1));
  nand nand_3 (nand_3_out, incarry, xorprekonand_1_out_3);
  nand nand_4 (nand_4_out, nand_3_out, nand_3_out);
  iliprekoNAND iliprekonand_1 (.in_1(nand_4_out), .in_2(nand_2_out), .out_3(outcarry));
endmodule

module fourbitadder (
  input  [3:0] x,
  input  [3:0] y,
  output [3:0] xPlusy,
  output overflow
);

  wire fulladder_1_outcarry, fulladder_2_outcarry, fulladder_3_outcarry, fulladder_4_outcarry;

  fulladder fulladder_1 (.incarry(1'b0), .in1(x[0]), .in2(y[0]), .out1(xPlusy[0]), .outcarry(fulladder_1_outcarry));
  fulladder fulladder_2 (
    .incarry(fulladder_1_outcarry), .in1(x[1]), .in2(y[1]), .out1(xPlusy[1]), .outcarry(fulladder_2_outcarry));
  fulladder fulladder_3 (
    .incarry(fulladder_2_outcarry), .in1(x[2]), .in2(y[2]), .out1(xPlusy[2]), .outcarry(fulladder_3_outcarry));
  fulladder fulladder_4 (
    .incarry(fulladder_3_outcarry), .in1(x[3]), .in2(y[3]), .out1(xPlusy[3]), .outcarry(fulladder_4_outcarry));
  xor xor_1 (overflow, fulladder_4_outcarry, fulladder_3_outcarry);
endmodule

module fourbit2kk (
  input  [3:0] x,
  output [3:0] complement
);

  wire [3:0] not_1_out;

  assign not_1_out = ~x;  // NOT_Gate not_1, 4 bits wide
  fourbitadder fourbitadder_1 (.x(4'b0001), .y(not_1_out), .xPlusy(complement));  // open: overflow
endmodule

module iliprekoNAND (
  input  in_1,
  input  in_2,
  output out_3
);

  wire nand_1_out, nand_2_out;

  nand nand_1 (nand_1_out, in_1, in_1);
  nand nand_2 (nand_2_out, in_2, in_2);
  nand nand_3 (out_3, nand_1_out, nand_2_out);
endmodule

module xorprekoNAND (
  input  in_1,
  input  in_2,
  output out_3
);

  wire nand_1_out, nand_2_out, nand_3_out, nand_5_out;

  nand nand_1 (nand_1_out, in_1, in_1);
  nand nand_2 (nand_2_out, in_2, in_2);
  nand nand_3 (nand_3_out, nand_1_out, in_2);
  nand nand_4 (out_3, nand_3_out, nand_5_out);
  nand nand_5 (nand_5_out, in_1, nand_2_out);
endmodule

module fourbitadderNAND (
  input  [3:0] x,
  input  [3:0] y,
  output [3:0] xPlusy,
  output overflow
);

  wire fulladdernand_1_outcarry, fulladdernand_2_outcarry, fulladdernand_3_outcarry;

  fulladderNAND fulladdernand_1 (
    .incarry(1'b0), .in1(x[0]), .in2(y[0]), .out1(xPlusy[0]), .outcarry(fulladdernand_1_outcarry));
  fulladderNAND fulladdernand_2 (
    .incarry(fulladdernand_1_outcarry), .in1(x[1]), .in2(y[1]), .out1(xPlusy[1]),
    .outcarry(fulladdernand_2_outcarry));
  fulladderNAND fulladdernand_3 (
    .incarry(fulladdernand_2_outcarry), .in1(x[2]), .in2(y[2]), .out1(xPlusy[2]),
    .outcarry(fulladdernand_3_outcarry));
  fulladderNAND fulladdernand_4 (
    .incarry(fulladdernand_3_outcarry), .in1(x[3]), .in2(y[3]), .out1(xPlusy[3]), .outcarry(overflow));
endmodule

module shifterUdesno (
  input  [3:0] ulaz,
  input  [1:0] K,
  output [3:0] shiftano
);

  Multiplexer #(.select(2)) multiplexer_1 (
    .in0(ulaz[0]), .in1(ulaz[1]), .in2(ulaz[2]), .in3(ulaz[3]), .out(shiftano[0]), .sel(K));
  Multiplexer #(.select(2)) multiplexer_2 (
    .in0(ulaz[1]), .in1(ulaz[2]), .in2(ulaz[3]), .in3(1'b0), .out(shiftano[1]), .sel(K));
  Multiplexer #(.select(2)) multiplexer_3 (
    .in0(ulaz[2]), .in1(ulaz[3]), .in2(1'b0), .in3(1'b0), .out(shiftano[2]), .sel(K));
  Multiplexer #(.select(2)) multiplexer_4 (
    .in0(ulaz[3]), .in1(1'b0), .in2(1'b0), .in3(1'b0), .out(shiftano[3]), .sel(K));
endmodule

module shifterUlijevo (
  input  [3:0] ulaz,
  input  [1:0] K,
  output [3:0] shiftano
);

  Multiplexer #(.select(2)) multiplexer_1 (
    .in0(ulaz[0]), .in1(1'b0), .in2(1'b0), .in3(1'b0), .out(shiftano[0]), .sel(K));
  Multiplexer #(.select(2)) multiplexer_2 (
    .in0(ulaz[1]), .in1(ulaz[0]), .in2(1'b0), .in3(1'b0), .out(shiftano[1]), .sel(K));
  Multiplexer #(.select(2)) multiplexer_3 (
    .in0(ulaz[2]), .in1(ulaz[1]), .in2(ulaz[0]), .in3(1'b0), .out(shiftano[2]), .sel(K));
  Multiplexer #(.select(2)) multiplexer_4 (
    .in0(ulaz[3]), .in1(ulaz[2]), .in2(ulaz[1]), .in3(ulaz[0]), .out(shiftano[3]), .sel(K));
endmodule

module alu (
  input  [3:0] A,
  input  [3:0] B,
  input  [1:0] C,
  input  [1:0] K,
  input  M,
  output [3:0] decA,
  output [3:0] decB,
  output [3:0] razlikaAiBdec,
  output overflow,
  output [3:0] negiranA,
  output [3:0] ABnegirano,
  output [3:0] zbirAiBdec,
  output [3:0] tempBin,
  output [3:0] tempDec,
  output [3:0] izlaz
);

  wire [3:0] fourbit2kk_1_complement, nor_1_out, nor_2_out, nor_3_out, shifterudesno_1_shiftano,
       shifterulijevo_1_shiftano;

  assign negiranA = ~A;  // NOT_Gate not_1, 4 bits wide
  shifterUlijevo shifterulijevo_1 (.ulaz(tempBin), .K(K), .shiftano(shifterulijevo_1_shiftano));
  shifterUdesno shifterudesno_1 (.ulaz(tempBin), .K(K), .shiftano(shifterudesno_1_shiftano));
  fourbit2kk fourbit2kk_1 (.x(B), .complement(fourbit2kk_1_complement));
  assign nor_1_out = ~(A | A);  // NOR_Gate nor_1, 4 bits wide
  assign nor_2_out = ~(B | B);  // NOR_Gate nor_2, 4 bits wide
  fourbitadderNAND fourbitaddernand_1 (.x(A), .y(B), .xPlusy(zbirAiBdec));  // open: overflow
  Multiplexer #(.width(4)) multiplexer_1 (
    .in0(shifterulijevo_1_shiftano), .in1(shifterudesno_1_shiftano), .out(izlaz), .sel(M));
  fourbitadder fourbitadder_1 (.x(A), .y(fourbit2kk_1_complement), .xPlusy(razlikaAiBdec), .overflow(overflow));
  assign nor_3_out = ~(nor_1_out | nor_2_out);  // NOR_Gate nor_3, 4 bits wide
  assign ABnegirano = ~(nor_3_out | nor_3_out);  // NOR_Gate nor_4, 4 bits wide
  Multiplexer #(.select(2), .width(4)) multiplexer_2 (
    .in0(razlikaAiBdec), .in1(negiranA), .in2(ABnegirano), .in3(zbirAiBdec), .out(tempBin), .sel(C));

  assign decA = A;
  assign decB = B;
  assign tempDec = tempBin;
endmodule
