// Logisim project zadaca.circ as structural Verilog
module osamkk (
  input  [2:0] ulaz,
  output [2:0] izlaz
);

  wire nor_1_out, not_1_out;

  nor nor_1 (nor_1_out, ulaz[0], ulaz[1]);
  xor xor_1 (izlaz[2], nor_1_out, not_1_out);
  not not_1 (not_1_out, ulaz[2]);
  xor xor_2 (izlaz[1], ulaz[0], ulaz[1]);

  assign izlaz[0] = ulaz[0];
endmodule

module kolo32u1preko4u1 (
  input  [31:0] ulaz,
  input  [4:0] kontrola,
  output izlaz
);

  wire multiplexer_1_out, multiplexer_2_out, multiplexer_3_out, multiplexer_4_out, multiplexer_5_out,
       multiplexer_6_out, multiplexer_7_out, multiplexer_8_out, multiplexer_9_out, multiplexer_10_out;

  Multiplexer #(.select(2)) multiplexer_1 (
    .in0(ulaz[0]), .in1(ulaz[1]), .in2(ulaz[2]), .in3(ulaz[3]), .out(multiplexer_1_out), .sel(kontrola[1:0]));
  Multiplexer #(.select(2)) multiplexer_2 (
    .in0(ulaz[28]), .in1(ulaz[29]), .in2(ulaz[30]), .in3(ulaz[31]), .out(multiplexer_2_out),
    .sel(kontrola[1:0]));
  Multiplexer #(.select(2)) multiplexer_3 (
    .in0(ulaz[4]), .in1(ulaz[5]), .in2(ulaz[6]), .in3(ulaz[7]), .out(multiplexer_3_out), .sel(kontrola[1:0]));
  Multiplexer #(.select(2)) multiplexer_4 (
    .in0(ulaz[24]), .in1(ulaz[25]), .in2(ulaz[26]), .in3(ulaz[27]), .out(multiplexer_4_out),
    .sel(kontrola[1:0]));
  Multiplexer #(.select(2)) multiplexer_5 (
    .in0(ulaz[8]), .in1(ulaz[9]), .in2(ulaz[10]), .in3(ulaz[11]), .out(multiplexer_5_out), .sel(kontrola[1:0]));
  Multiplexer #(.select(2)) multiplexer_6 (
    .in0(ulaz[20]), .in1(ulaz[21]), .in2(ulaz[22]), .in3(ulaz[23]), .out(multiplexer_6_out),
    .sel(kontrola[1:0]));
  Multiplexer #(.select(2)) multiplexer_7 (
    .in0(ulaz[12]), .in1(ulaz[13]), .in2(ulaz[14]), .in3(ulaz[15]), .out(multiplexer_7_out),
    .sel(kontrola[1:0]));
  Multiplexer #(.select(2)) multiplexer_8 (
    .in0(ulaz[16]), .in1(ulaz[17]), .in2(ulaz[18]), .in3(ulaz[19]), .out(multiplexer_8_out),
    .sel(kontrola[1:0]));
  Multiplexer #(.select(2)) multiplexer_9 (
    .in0(multiplexer_1_out), .in1(multiplexer_3_out), .in2(multiplexer_5_out), .in3(multiplexer_7_out),
    .out(multiplexer_9_out), .sel(kontrola[3:2]));
  Multiplexer #(.select(2)) multiplexer_10 (
    .in0(multiplexer_8_out), .in1(multiplexer_6_out), .in2(multiplexer_4_out), .in3(multiplexer_2_out),
    .out(multiplexer_10_out), .sel(kontrola[3:2]));
  Multiplexer #(.select(2)) multiplexer_11 (
    .in0(multiplexer_9_out), .in1(multiplexer_10_out), .in2(1'b0), .in3(1'b0), .out(izlaz),
    .sel({1'b0, kontrola[4]}));
endmodule

module alu (
  input  [3:0] A,
  input  [3:0] B,
  input  [1:0] C,
  input  [1:0] K,
  input  M,
  output [3:0] decA,
  output [3:0] decB,
  output [3:0] razlikaAiBdec,
  output overflow,
  output [3:0] negiranA,
  output [3:0] ABnegirano,
  output [3:0] zbirAiBdec,
  output [3:0] tempBin,
  output [3:0] tempDec,
  output [3:0] izlaz
);

  wire [3:0] fourbit2kk_1_complement, nor_1_out, nor_2_out, nor_3_out, shifterudesno_1_shiftano,
       shifterulijevo_1_shiftano;

  assign negiranA = ~A;  // NOT_Gate not_1, 4 bits wide
  shifterUlijevo shifterulijevo_1 (.ulaz(tempBin), .K(K), .shiftano(shifterulijevo_1_shiftano));
  shifterUdesno shifterudesno_1 (.ulaz(tempBin), .K(K), .shiftano(shifterudesno_1_shiftano));
  fourbit2kk fourbit2kk_1 (.x(B), .complement(fourbit2kk_1_complement));
  assign nor_1_out = ~(A | A);  // NOR_Gate nor_1, 4 bits wide
  assign nor_2_out = ~(B | B);  // NOR_Gate nor_2, 4 bits wide
  fourbitadderNAND fourbitaddernand_1 (.x(A), .y(B), .xPlusy(zbirAiBdec));  // open: overflow
  Multiplexer #(.width(4)) multiplexer_1 (
    .in0(shifterulijevo_1_shiftano), .in1(shifterudesno_1_shiftano), .out(izlaz), .sel(M));
  fourbitadder fourbitadder_1 (.x(A), .y(fourbit2kk_1_complement), .xPlusy(razlikaAiBdec), .overflow(overflow));
  assign nor_3_out = ~(nor_1_out | nor_2_out);  // NOR_Gate nor_3, 4 bits wide
  assign ABnegirano = ~(nor_3_out | nor_3_out);  // NOR_Gate nor_4, 4 bits wide
  Multiplexer #(.select(2), .width(4)) multiplexer_2 (
    .in0(razlikaAiBdec), .in1(negiranA), .in2(ABnegirano), .in3(zbirAiBdec), .out(tempBin), .sel(C));

  assign decA = A;
  assign decB = B;
  assign tempDec = tempBin;
endmodule

module fulladder (
  input  incarry,
  input  in1,
  input  in2,
  output out1,
  output outcarry
);

  wire and_1_out, and_2_out, xor_1_out;

  xor xor_1 (xor_1_out, in1, in2);
  and and_1 (and_1_out, in1, in2);
  xor xor_2 (out1, xor_1_out, incarry);
  and and_2 (and_2_out, incarry, xor_1_out);
  or or_1 (outcarry, and_2_out, and_1_out);
endmodule

module fourbitadder (
  input  [3:0] x,
  input  [3:0] y,
  output [3:0] xPlusy,
  output overflow
);

  wire fulladder_1_outcarry, fulladder_2_outcarry, fulladder_3_outcarry, fulladder_4_outcarry;

  fulladder fulladder_1 (.out1(xPlusy[0]), .outcarry(fulladder_1_outcarry));  // open: incarry, in1, in2
  fulladder fulladder_2 (.out1(xPlusy[1]), .outcarry(fulladder_2_outcarry));  // open: incarry, in1, in2
  fulladder fulladder_3 (.out1(xPlusy[2]), .outcarry(fulladder_3_outcarry));  // open: incarry, in1, in2
  fulladder fulladder_4 (.out1(xPlusy[3]), .outcarry(fulladder_4_outcarry));  // open: incarry, in1, in2
  xor xor_1 (overflow, fulladder_4_outcarry, fulladder_3_outcarry);
endmodule

module fourbit2kk (
  input  [3:0] x,
  output [3:0] complement
);

  wire [3:0] not_1_out;

  assign not_1_out = ~x;  // NOT_Gate not_1, 4 bits wide
  fourbitadder fourbitadder_1 (.x(4'b0001), .y(not_1_out), .xPlusy(complement));  // open: overflow
endmodule

module fulladderNAND (
  input  incarry,
  input  in1,
  input  in2,
  output out1,
  output outcarry
);

  wire iksor_out_3, nand_1_out, nand_2_out, nand_3_out, nand_4_out;

  xorprekoNAND iksor (.in_1(in1), .in_2(in2), .out_3(iksor_out_3));
  nand nand_1 (nand_1_out, in1, in2);
  nand nand_2 (nand_2_out, nand_1_out, nand_1_out);
  xorprekoNAND iksor2 (.in_1(iksor_out_3), .in_2(incarry), .out_3(out1));
  nand nand_3 (nand_3_out, incarry, iksor_out_3);
  nand nand_4 (nand_4_out, nand_3_out, nand_3_out);
  iliprekoNAND ili (.in_1(nand_4_out), .in_2(nand_2_out), .out_3(outcarry));
endmodule

module iliprekoNAND (
  input  in_1,
  input  in_2,
  output out_3
);

  wire nand_1_out, nand_2_out;

  nand nand_1 (nand_1_out, in_1, in_1);
  nand nand_2 (nand_2_out, in_2, in_2);
  nand nand_3 (out_3, nand_1_out, nand_2_out);
endmodule

module xorprekoNAND (
  input  in_1,
  input  in_2,
  output out_3
);

  wire nand_1_out, nand_2_out, nand_3_out, nand_5_out;

  nand nand_1 (nand_1_out, in_1, in_1);
  nand nand_2 (nand_2_out, in_2, in_2);
  nand nand_3 (nand_3_out, nand_1_out, in_2);
  nand nand_4 (out_3, nand_3_out, nand_5_out);
  nand nand_5 (nand_5_out, in_1, nand_2_out);
endmodule

module fourbitadderNAND (
  input  [3:0] x,
  input  [3:0] y,
  output [3:0] xPlusy,
  output overflow
);

  wire fulladdernand_1_outcarry, fulladdernand_2_outcarry, fulladdernand_3_outcarry;

  fulladderNAND fulladdernand_1 (
    .incarry(1'b0), .in1(x[0]), .in2(y[0]), .out1(xPlusy[0]), .outcarry(fulladdernand_1_outcarry));
  fulladderNAND fulladdernand_2 (
    .incarry(fulladdernand_1_outcarry), .in1(x[1]), .in2(y[1]), .out1(xPlusy[1]),
    .outcarry(fulladdernand_2_outcarry));
  fulladderNAND fulladdernand_3 (
    .incarry(fulladdernand_2_outcarry), .in1(x[2]), .in2(y[2]), .out1(xPlusy[2]),
    .outcarry(fulladdernand_3_outcarry));
  fulladderNAND fulladdernand_4 (
    .incarry(fulladdernand_3_outcarry), .in1(x[3]), .in2(y[3]), .out1(xPlusy[3]), .outcarry(overflow));
endmodule

module shifterUdesno (
  input  [3:0] ulaz,
  input  [1:0] K,
  output [3:0] shiftano
);

  Multiplexer #(.select(2)) multiplexer_1 (
    .in0(ulaz[0]), .in1(ulaz[1]), .in2(ulaz[2]), .in3(ulaz[3]), .out(shiftano[0]), .sel(K));
  Multiplexer #(.select(2)) multiplexer_2 (
    .in0(ulaz[1]), .in1(ulaz[2]), .in2(ulaz[3]), .in3(1'b0), .out(shiftano[1]), .sel(K));
  Multiplexer #(.select(2)) multiplexer_3 (
    .in0(ulaz[2]), .in1(ulaz[3]), .in2(1'b0), .in3(1'b0), .out(shiftano[2]), .sel(K));
  Multiplexer #(.select(2)) multiplexer_4 (
    .in0(ulaz[3]), .in1(1'b0), .in2(1'b0), .in3(1'b0), .out(shiftano[3]), .sel(K));
endmodule

module shifterUlijevo (
  input  [3:0] ulaz,
  input  [1:0] K,
  output [3:0] shiftano
);

  Multiplexer #(.select(2)) multiplexer_1 (
    .in0(ulaz[0]), .in1(1'b0), .in2(1'b0), .in3(1'b0), .out(shiftano[0]), .sel(K));
  Multiplexer #(.select(2)) multiplexer_2 (
    .in0(ulaz[1]), .in1(ulaz[0]), .in2(1'b0), .in3(1'b0), .out(shiftano[1]), .sel(K));
  Multiplexer #(.select(2)) multiplexer_3 (
    .in0(ulaz[2]), .in1(ulaz[1]), .in2(ulaz[0]), .in3(1'b0), .out(shiftano[2]), .sel(K));
  Multiplexer #(.select(2)) multiplexer_4 (
    .in0(ulaz[3]), .in1(ulaz[2]), .in2(ulaz[1]), .in3(ulaz[0]), .out(shiftano[3]), .sel(K));
endmodule

module mul (
  input  [3:0] in_1,
  input  [3:0] in_2,
  output [3:0] out_3,
  output [3:0] out_4,
  output [7:0] out_5
);

  wire and_1_out, and_2_out, and_3_out, and_4_out, and_5_out, and_6_out, and_7_out, and_8_out, and_9_out,
       and_10_out, and_11_out, and_12_out, and_13_out, and_14_out, and_15_out, fulladder_2_out1,
       fulladder_2_outcarry, fulladder_3_outcarry, fulladder_4_out1, fulladder_4_outcarry, fulladder_5_out1,
       fulladder_5_outcarry, fulladder_6_outcarry, fulladder_7_out1, fulladder_7_outcarry, fulladder_8_out1,
       fulladder_8_outcarry, ha_1_carryu, ha_1_xplusy, ha_2_carryu, ha_3_carryu, ha_4_carryu;

  and and_1 (and_1_out, in_1[3], in_2[2]);
  and and_2 (and_2_out, in_1[3], in_2[3]);
  fulladder fulladder_1 (
    .incarry(fulladder_3_outcarry), .in1(and_2_out), .in2(fulladder_2_outcarry), .out1(out_5[6]),
    .outcarry(out_5[7]));
  and and_3 (and_3_out, in_1[3], in_2[1]);
  HA ha_1 (.X(fulladder_4_outcarry), .Y(and_3_out), .XplusY(ha_1_xplusy), .carryu(ha_1_carryu));
  and and_4 (and_4_out, in_1[2], in_2[2]);
  fulladder fulladder_2 (
    .incarry(fulladder_5_outcarry), .in1(ha_1_carryu), .in2(and_1_out), .out1(fulladder_2_out1),
    .outcarry(fulladder_2_outcarry));
  and and_5 (and_5_out, in_1[2], in_2[3]);
  fulladder fulladder_3 (
    .incarry(fulladder_6_outcarry), .in1(and_5_out), .in2(fulladder_2_out1), .out1(out_5[5]),
    .outcarry(fulladder_3_outcarry));
  and and_6 (and_6_out, in_1[3], in_2[0]);
  and and_7 (and_7_out, in_1[2], in_2[1]);
  fulladder fulladder_4 (
    .incarry(fulladder_7_outcarry), .in1(and_7_out), .in2(and_6_out), .out1(fulladder_4_out1),
    .outcarry(fulladder_4_outcarry));
  fulladder fulladder_5 (
    .incarry(fulladder_8_outcarry), .in1(and_4_out), .in2(ha_1_xplusy), .out1(fulladder_5_out1),
    .outcarry(fulladder_5_outcarry));
  and and_8 (and_8_out, in_1[1], in_2[3]);
  fulladder fulladder_6 (
    .incarry(ha_3_carryu), .in1(and_8_out), .in2(fulladder_5_out1), .out1(out_5[4]),
    .outcarry(fulladder_6_outcarry));
  and and_9 (and_9_out, in_1[2], in_2[0]);
  and and_10 (and_10_out, in_1[1], in_2[1]);
  fulladder fulladder_7 (
    .incarry(ha_4_carryu), .in1(and_10_out), .in2(and_9_out), .out1(fulladder_7_out1),
    .outcarry(fulladder_7_outcarry));
  and and_11 (and_11_out, in_1[1], in_2[2]);
  fulladder fulladder_8 (
    .incarry(ha_2_carryu), .in1(and_11_out), .in2(fulladder_4_out1), .out1(fulladder_8_out1),
    .outcarry(fulladder_8_outcarry));
  HA ha_2 (.X(and_14_out), .Y(fulladder_7_out1), .XplusY(out_5[2]), .carryu(ha_2_carryu));
  and and_12 (and_12_out, in_1[0], in_2[3]);
  HA ha_3 (.X(and_12_out), .Y(fulladder_8_out1), .XplusY(out_5[3]), .carryu(ha_3_carryu));
  and and_13 (and_13_out, in_1[1], in_2[0]);
  HA ha_4 (.X(and_15_out), .Y(and_13_out), .XplusY(out_5[1]), .carryu(ha_4_carryu));
  and and_14 (and_14_out, in_1[0], in_2[2]);
  and and_15 (and_15_out, in_1[0], in_2[1]);
  and and_16 (out_5[0], in_1[0], in_2[0]);

  assign out_3 = in_1;
  assign out_4 = in_2;
endmodule

module HA (
  input  X,
  input  Y,
  output XplusY,
  output carryu
);

  xor xor_1 (XplusY, X, Y);
  and and_1 (carryu, X, Y);
endmodule

module poredjac (
  input  x,
  input  y,
  input  biloXmanjeY,
  input  biloXveceY,
  input  biliJednaki,
  output XmanjeY,
  output XveceY,
  output jednaki
);

  wire and_1_out, and_2_out, and_4_out, and_5_out, not_1_out, not_2_out, not_3_out, xor_1_out;

  not not_1 (not_1_out, x);
  not not_2 (not_2_out, y);
  xor xor_1 (xor_1_out, x, y);
  not not_3 (not_3_out, xor_1_out);
  and and_1 (and_1_out, not_3_out, biloXmanjeY);
  and and_2 (and_2_out, not_3_out, biloXveceY);
  and and_3 (jednaki, not_3_out, biliJednaki);
  and and_4 (and_4_out, not_1_out, y);
  and and_5 (and_5_out, not_2_out, x);
  or or_1 (XmanjeY, and_4_out, and_1_out);
  or or_2 (XveceY, and_5_out, and_2_out);
endmodule

module fourbitcomp (
  input  [3:0] x,
  input  [3:0] y
);

  wire poredjac_1_jednaki, poredjac_1_xmanjey, poredjac_1_xvecey, poredjac_2_jednaki, poredjac_2_xmanjey,
       poredjac_2_xvecey, poredjac_3_jednaki, poredjac_3_xmanjey, poredjac_3_xvecey, poredjac_4_jednaki,
       poredjac_4_xmanjey, poredjac_4_xvecey;

  poredjac poredjac_1 (
    .x(x[0]), .y(y[0]), .biloXmanjeY(1'b0), .biloXveceY(1'b0), .biliJednaki(1'b1),
    .XmanjeY(poredjac_1_xmanjey), .XveceY(poredjac_1_xvecey), .jednaki(poredjac_1_jednaki));
  poredjac poredjac_2 (
    .x(x[1]), .y(y[1]), .biloXmanjeY(poredjac_1_xmanjey), .biloXveceY(poredjac_1_xvecey),
    .biliJednaki(poredjac_1_jednaki), .XmanjeY(poredjac_2_xmanjey), .XveceY(poredjac_2_xvecey),
    .jednaki(poredjac_2_jednaki));
  poredjac poredjac_3 (
    .x(x[2]), .y(y[2]), .biloXmanjeY(poredjac_2_xmanjey), .biloXveceY(poredjac_2_xvecey),
    .biliJednaki(poredjac_2_jednaki), .XmanjeY(poredjac_3_xmanjey), .XveceY(poredjac_3_xvecey),
    .jednaki(poredjac_3_jednaki));
  poredjac poredjac_4 (
    .x(x[3]), .y(y[3]), .biloXmanjeY(poredjac_3_xmanjey), .biloXveceY(poredjac_3_xvecey),
    .biliJednaki(poredjac_3_jednaki), .XmanjeY(poredjac_4_xmanjey), .XveceY(poredjac_4_xvecey),
    .jednaki(poredjac_4_jednaki));
endmodule

module signedporedjac (
  input  [3:0] x,
  input  [3:0] y,
  output [3:0] out_3,
  output XmanjeY,
  output [3:0] out_5,
  output XveceY,
  output jednaki
);

  wire not_1_out, not_2_out, poredjac_1_jednaki, poredjac_1_xmanjey, poredjac_1_xvecey, poredjac_2_jednaki,
       poredjac_2_xmanjey, poredjac_2_xvecey, poredjac_3_jednaki, poredjac_3_xmanjey, poredjac_3_xvecey,
       poredjac_4_jednaki, poredjac_4_xmanjey, poredjac_4_xvecey;

  poredjac poredjac_1 (
    .x(x[0]), .y(y[0]), .biloXmanjeY(1'b0), .biloXveceY(1'b0), .biliJednaki(1'b1),
    .XmanjeY(poredjac_1_xmanjey), .XveceY(poredjac_1_xvecey), .jednaki(poredjac_1_jednaki));
  poredjac poredjac_2 (
    .x(x[1]), .y(y[1]), .biloXmanjeY(poredjac_1_xmanjey), .biloXveceY(poredjac_1_xvecey),
    .biliJednaki(poredjac_1_jednaki), .XmanjeY(poredjac_2_xmanjey), .XveceY(poredjac_2_xvecey),
    .jednaki(poredjac_2_jednaki));
  poredjac poredjac_3 (
    .x(x[2]), .y(y[2]), .biloXmanjeY(poredjac_2_xmanjey), .biloXveceY(poredjac_2_xvecey),
    .biliJednaki(poredjac_2_jednaki), .XmanjeY(poredjac_3_xmanjey), .XveceY(poredjac_3_xvecey),
    .jednaki(poredjac_3_jednaki));
  poredjac poredjac_4 (
    .x(x[3]), .y(y[3]), .biloXmanjeY(poredjac_3_xmanjey), .biloXveceY(poredjac_3_xvecey),
    .biliJednaki(poredjac_3_jednaki), .XmanjeY(poredjac_4_xmanjey), .XveceY(poredjac_4_xvecey),
    .jednaki(poredjac_4_jednaki));
  not not_1 (not_1_out, poredjac_4_xvecey);
  not not_2 (not_2_out, poredjac_4_xmanjey);
  Multiplexer #(.select(2)) multiplexer_1 (
    .in0(poredjac_4_xmanjey), .in1(1'b1), .in2(1'b0), .in3(not_1_out), .out(XmanjeY), .sel({y[3], x[3]}));
  Multiplexer #(.select(2)) multiplexer_2 (
    .in0(poredjac_4_xvecey), .in1(1'b0), .in2(1'b1), .in3(not_2_out), .out(XveceY), .sel({y[3], x[3]}));
  Multiplexer #(.select(2)) multiplexer_3 (
    .in0(poredjac_4_jednaki), .in1(1'b0), .in2(1'b0), .in3(poredjac_4_jednaki), .out(jednaki),
    .sel({y[3], x[3]}));

  assign out_3 = x;
  assign out_5 = y;
endmodule

module mux2u1 (
  input  x0,
  input  x1,
  input  control,
  output xout
);

  wire and_1_out, and_2_out, not_1_out;

  and and_1 (and_1_out, x0, not_1_out);
  not not_1 (not_1_out, control);
  and and_2 (and_2_out, x1, control);
  or or_1 (xout, and_1_out, and_2_out);
endmodule

module mux2u1NOR (
  input  x0,
  input  x1,
  input  control,
  output xout
);

  wire nor_1_out, nor_2_out, nor_3_out, nor_4_out, nor_5_out, nor_6_out, nor_7_out, nor_8_out;

  nor nor_1 (nor_1_out, control, control);
  nor nor_2 (nor_2_out, x0, x0);
  nor nor_3 (nor_3_out, nor_1_out, nor_1_out);
  nor nor_4 (nor_4_out, x1, x1);
  nor nor_5 (nor_5_out, control, control);
  nor nor_6 (nor_6_out, nor_2_out, nor_3_out);
  nor nor_7 (nor_7_out, nor_6_out, nor_8_out);
  nor nor_8 (nor_8_out, nor_4_out, nor_5_out);
  nor nor_9 (xout, nor_7_out, nor_7_out);
endmodule

module mux4u1 (
  input  in_1,
  input  in_2,
  input  in_3,
  input  in_4,
  input  in_5,
  input  in_6,
  output out_7
);

  wire mux2u1_1_xout, mux2u1_2_xout;

  mux2u1 mux2u1_1 (.x0(in_1), .x1(in_2), .control(in_5), .xout(mux2u1_1_xout));
  mux2u1 mux2u1_2 (.x0(in_3), .x1(in_4), .control(in_5), .xout(mux2u1_2_xout));
  mux2u1 mux2u1_3 (.x0(mux2u1_1_xout), .x1(mux2u1_2_xout), .control(in_6), .xout(out_7));
endmodule

module mux8u1 (
  input  [7:0] in_1,
  input  [2:0] in_2,
  input  in_3,
  input  in_4,
  input  in_5,
  input  A,
  input  B,
  input  C,
  output out_9
);

  wire and_1_out, and_2_out, and_3_out, and_4_out, mux4u1_1_out_7, mux4u1_2_out_7, nand_1_out, nand_2_out,
       nand_3_out, not_1_out, not_2_out, or_1_out, or_2_out, xor_1_out, xor_2_out;

  nand nand_1 (nand_1_out, in_3, in_4);
  not not_1 (not_1_out, B);
  and and_1 (and_1_out, A, C);
  nand nand_2 (nand_2_out, nand_1_out, in_5);
  nand nand_3 (nand_3_out, in_3, in_4, in_5);
  not not_2 (not_2_out, A);
  and and_2 (and_2_out, A, not_1_out);
  and and_3 (and_3_out, not_1_out, C);
  xor xor_1 (xor_1_out, nand_2_out, nand_3_out);
  or or_1 (or_1_out, and_2_out, and_4_out);
  and and_4 (and_4_out, not_2_out, C);
  or or_2 (or_2_out, and_1_out, and_3_out);
  mux4u1 mux4u1_1 (
    .in_1(in_1[0]), .in_2(in_1[1]), .in_3(in_1[2]), .in_4(in_1[3]), .in_5(in_2[0]), .in_6(in_2[1]),
    .out_7(mux4u1_1_out_7));
  mux4u1 mux4u1_2 (
    .in_1(in_1[4]), .in_2(in_1[5]), .in_3(in_1[6]), .in_4(in_1[7]), .in_5(in_2[0]), .in_6(in_2[1]),
    .out_7(mux4u1_2_out_7));
  xor xor_2 (xor_2_out, or_1_out, or_2_out);
  mux2u1 mux2u1_1 (.x0(mux4u1_1_out_7), .x1(mux4u1_2_out_7), .control(in_2[2]), .xout(out_9));
endmodule
