// Logisim project OgledniProcesor.circ as structural Verilog: 13 circuits, main circuit OgledniProcesor
module OgledniProcesor_ALU1bit (
  input  A,
  input  B,
  input  Cin,
  input  F1,
  input  F0,
  output Result,
  output Cout
);

  wire and_1_out, and_2_out, and_3_out, not_1_out, or_1_out, xor_1_out, xor_2_out;

  xor xor_1 (xor_1_out, A, B);
  xor xor_2 (xor_2_out, xor_1_out, Cin);
  and and_1 (and_1_out, A, B);
  and and_2 (and_2_out, Cin, xor_1_out);
  or or_1 (or_1_out, and_1_out, and_2_out);
  and and_3 (and_3_out, ~F0, ~F1);  // AND_Gate
  not not_1 (not_1_out, A);
  and and_4 (Cout, or_1_out, and_3_out);
  Multiplexer #(.select(2)) multiplexer_1 (
    .in0(xor_2_out), .in1(and_1_out), .in2(A), .in3(not_1_out), .out(Result), .sel({F1, F0}));
endmodule

module OgledniProcesor_ALU16bit (
  input  [15:0] A,
  input  [15:0] B,
  input  [1:0] F,
  output [15:0] Result,
  output N,
  output z
);

  wire ogledniprocesor_alu1bit_1_cout, ogledniprocesor_alu1bit_2_cout, ogledniprocesor_alu1bit_3_cout,
       ogledniprocesor_alu1bit_4_cout, ogledniprocesor_alu1bit_5_cout, ogledniprocesor_alu1bit_6_cout,
       ogledniprocesor_alu1bit_7_cout, ogledniprocesor_alu1bit_8_cout, ogledniprocesor_alu1bit_9_cout,
       ogledniprocesor_alu1bit_10_cout, ogledniprocesor_alu1bit_11_cout, ogledniprocesor_alu1bit_12_cout,
       ogledniprocesor_alu1bit_13_cout, ogledniprocesor_alu1bit_14_cout, ogledniprocesor_alu1bit_15_cout;

  // Probe on A
  // Probe on A
  // Probe on {N, Result[14:0]}
  // Probe on {N, Result[14:0]}
  nor nor_1 (z, N, Result[14], Result[13], Result[12], Result[11], Result[10], Result[9], Result[8], Result[7], Result[6], Result[5], Result[4], Result[3], Result[2], Result[1], Result[0]);
  OgledniProcesor_ALU1bit ogledniprocesor_alu1bit_1 (
    .A(A[0]), .B(B[0]), .Cin(1'b0), .F1(F[1]), .F0(F[0]), .Result(Result[0]),
    .Cout(ogledniprocesor_alu1bit_1_cout));
  OgledniProcesor_ALU1bit ogledniprocesor_alu1bit_2 (
    .A(A[1]), .B(B[1]), .Cin(ogledniprocesor_alu1bit_1_cout), .F1(F[1]), .F0(F[0]), .Result(Result[1]),
    .Cout(ogledniprocesor_alu1bit_2_cout));
  OgledniProcesor_ALU1bit ogledniprocesor_alu1bit_3 (
    .A(A[2]), .B(B[2]), .Cin(ogledniprocesor_alu1bit_2_cout), .F1(F[1]), .F0(F[0]), .Result(Result[2]),
    .Cout(ogledniprocesor_alu1bit_3_cout));
  // Probe on B
  // Probe on B
  OgledniProcesor_ALU1bit ogledniprocesor_alu1bit_4 (
    .A(A[3]), .B(B[3]), .Cin(ogledniprocesor_alu1bit_3_cout), .F1(F[1]), .F0(F[0]), .Result(Result[3]),
    .Cout(ogledniprocesor_alu1bit_4_cout));
  OgledniProcesor_ALU1bit ogledniprocesor_alu1bit_5 (
    .A(A[4]), .B(B[4]), .Cin(ogledniprocesor_alu1bit_4_cout), .F1(F[1]), .F0(F[0]), .Result(Result[4]),
    .Cout(ogledniprocesor_alu1bit_5_cout));
  OgledniProcesor_ALU1bit ogledniprocesor_alu1bit_6 (
    .A(A[5]), .B(B[5]), .Cin(ogledniprocesor_alu1bit_5_cout), .F1(F[1]), .F0(F[0]), .Result(Result[5]),
    .Cout(ogledniprocesor_alu1bit_6_cout));
  OgledniProcesor_ALU1bit ogledniprocesor_alu1bit_7 (
    .A(A[6]), .B(B[6]), .Cin(ogledniprocesor_alu1bit_6_cout), .F1(F[1]), .F0(F[0]), .Result(Result[6]),
    .Cout(ogledniprocesor_alu1bit_7_cout));
  OgledniProcesor_ALU1bit ogledniprocesor_alu1bit_8 (
    .A(A[7]), .B(B[7]), .Cin(ogledniprocesor_alu1bit_7_cout), .F1(F[1]), .F0(F[0]), .Result(Result[7]),
    .Cout(ogledniprocesor_alu1bit_8_cout));
  OgledniProcesor_ALU1bit ogledniprocesor_alu1bit_9 (
    .A(A[8]), .B(B[8]), .Cin(ogledniprocesor_alu1bit_8_cout), .F1(F[1]), .F0(F[0]), .Result(Result[8]),
    .Cout(ogledniprocesor_alu1bit_9_cout));
  OgledniProcesor_ALU1bit ogledniprocesor_alu1bit_10 (
    .A(A[9]), .B(B[9]), .Cin(ogledniprocesor_alu1bit_9_cout), .F1(F[1]), .F0(F[0]), .Result(Result[9]),
    .Cout(ogledniprocesor_alu1bit_10_cout));
  OgledniProcesor_ALU1bit ogledniprocesor_alu1bit_11 (
    .A(A[10]), .B(B[10]), .Cin(ogledniprocesor_alu1bit_10_cout), .F1(F[1]), .F0(F[0]), .Result(Result[10]),
    .Cout(ogledniprocesor_alu1bit_11_cout));
  OgledniProcesor_ALU1bit ogledniprocesor_alu1bit_12 (
    .A(A[11]), .B(B[11]), .Cin(ogledniprocesor_alu1bit_11_cout), .F1(F[1]), .F0(F[0]), .Result(Result[11]),
    .Cout(ogledniprocesor_alu1bit_12_cout));
  OgledniProcesor_ALU1bit ogledniprocesor_alu1bit_13 (
    .A(A[12]), .B(B[12]), .Cin(ogledniprocesor_alu1bit_12_cout), .F1(F[1]), .F0(F[0]), .Result(Result[12]),
    .Cout(ogledniprocesor_alu1bit_13_cout));
  OgledniProcesor_ALU1bit ogledniprocesor_alu1bit_14 (
    .A(A[13]), .B(B[13]), .Cin(ogledniprocesor_alu1bit_13_cout), .F1(F[1]), .F0(F[0]), .Result(Result[13]),
    .Cout(ogledniprocesor_alu1bit_14_cout));
  OgledniProcesor_ALU1bit ogledniprocesor_alu1bit_15 (
    .A(A[14]), .B(B[14]), .Cin(ogledniprocesor_alu1bit_14_cout), .F1(F[1]), .F0(F[0]), .Result(Result[14]),
    .Cout(ogledniprocesor_alu1bit_15_cout));
  OgledniProcesor_ALU1bit ogledniprocesor_alu1bit_16 (
    .A(A[15]), .B(B[15]), .Cin(ogledniprocesor_alu1bit_15_cout), .F1(F[1]), .F0(F[0]), .Result(N));  // open: Cout

  assign Result[15] = N;

  // Other names for the same wires on the sheet: R0 = Result[0]; R1 = Result[1]; R2 = Result[2]; R3 = Result[3];
  //   R4 = Result[4]; R5 = Result[5]; R6 = Result[6]; R7 = Result[7]; R8 = Result[8]; R9 = Result[9];
  //   R10 = Result[10]; R11 = Result[11]; R12 = Result[12]; R13 = Result[13]; R14 = Result[14]; R15 = N
endmodule

module OgledniProcesor_Shifter (
  input  [15:0] ALU_Out,
  input  [1:0] S,
  output [15:0] C
);

  wire and_1_out, and_2_out, and_3_out, and_4_out, and_5_out, and_6_out, and_7_out, and_8_out, and_9_out,
       and_10_out, and_11_out, and_12_out, and_13_out, and_14_out, and_15_out, and_16_out, and_17_out,
       and_18_out, and_19_out, and_20_out, and_21_out, and_22_out, and_23_out, and_24_out, and_25_out,
       and_26_out, and_27_out, and_28_out, and_29_out, and_30_out, and_31_out, and_32_out, and_33_out,
       and_34_out, and_35_out, and_36_out, and_37_out, and_38_out, and_39_out, and_40_out, and_41_out,
       and_42_out, and_43_out, and_44_out, and_45_out, and_46_out, and_47_out, and_48_out, and_49_out,
       not_1_out, not_2_out;

  not not_1 (not_1_out, S[1]);
  and and_1 (and_1_out, not_1_out, not_2_out);
  and and_2 (and_2_out, not_1_out, S[0]);
  and and_3 (and_3_out, S[1], not_2_out);
  not not_2 (not_2_out, S[0]);
  and and_4 (and_4_out, and_1_out, ALU_Out[15]);
  and and_5 (and_5_out, and_2_out, ALU_Out[15]);
  or or_1 (C[15], and_4_out, and_5_out, and_6_out);
  and and_6 (and_6_out, and_3_out, ALU_Out[14]);
  and and_7 (and_7_out, and_1_out, ALU_Out[14]);
  and and_8 (and_8_out, and_2_out, ALU_Out[14]);
  or or_2 (C[14], and_5_out, and_7_out, and_9_out);
  and and_9 (and_9_out, and_3_out, ALU_Out[13]);
  and and_10 (and_10_out, and_1_out, ALU_Out[13]);
  and and_11 (and_11_out, and_2_out, ALU_Out[13]);
  or or_3 (C[13], and_8_out, and_10_out, and_12_out);
  and and_12 (and_12_out, and_3_out, ALU_Out[12]);
  and and_13 (and_13_out, and_1_out, ALU_Out[12]);
  or or_4 (C[12], and_11_out, and_13_out, and_14_out);
  and and_14 (and_14_out, and_3_out, ALU_Out[11]);
  and and_15 (and_15_out, and_2_out, ALU_Out[12]);
  and and_16 (and_16_out, and_1_out, ALU_Out[11]);
  or or_5 (C[11], and_15_out, and_16_out, and_18_out);
  and and_17 (and_17_out, and_2_out, ALU_Out[11]);
  and and_18 (and_18_out, and_3_out, ALU_Out[10]);
  and and_19 (and_19_out, and_1_out, ALU_Out[10]);
  or or_6 (C[10], and_17_out, and_19_out, and_21_out);
  and and_20 (and_20_out, and_2_out, ALU_Out[10]);
  and and_21 (and_21_out, and_3_out, ALU_Out[9]);
  and and_22 (and_22_out, and_1_out, ALU_Out[9]);
  or or_7 (C[9], and_20_out, and_22_out, and_24_out);
  and and_23 (and_23_out, and_2_out, ALU_Out[9]);
  and and_24 (and_24_out, and_3_out, ALU_Out[8]);
  and and_25 (and_25_out, and_1_out, ALU_Out[8]);
  or or_8 (C[8], and_23_out, and_25_out, and_27_out);
  and and_26 (and_26_out, and_2_out, ALU_Out[8]);
  and and_27 (and_27_out, and_3_out, ALU_Out[7]);
  and and_28 (and_28_out, and_1_out, ALU_Out[7]);
  and and_29 (and_29_out, and_2_out, ALU_Out[7]);
  or or_9 (C[7], and_26_out, and_28_out, and_30_out);
  and and_30 (and_30_out, and_3_out, ALU_Out[6]);
  and and_31 (and_31_out, and_1_out, ALU_Out[6]);
  and and_32 (and_32_out, and_2_out, ALU_Out[6]);
  or or_10 (C[6], and_29_out, and_31_out, and_33_out);
  and and_33 (and_33_out, and_3_out, ALU_Out[5]);
  and and_34 (and_34_out, and_1_out, ALU_Out[5]);
  and and_35 (and_35_out, and_2_out, ALU_Out[5]);
  or or_11 (C[5], and_32_out, and_34_out, and_36_out);
  and and_36 (and_36_out, and_3_out, ALU_Out[4]);
  and and_37 (and_37_out, and_1_out, ALU_Out[4]);
  or or_12 (C[4], and_35_out, and_37_out, and_39_out);
  and and_38 (and_38_out, and_2_out, ALU_Out[4]);
  and and_39 (and_39_out, and_3_out, ALU_Out[3]);
  and and_40 (and_40_out, and_1_out, ALU_Out[3]);
  or or_13 (C[3], and_38_out, and_40_out, and_42_out);
  and and_41 (and_41_out, and_2_out, ALU_Out[3]);
  and and_42 (and_42_out, and_3_out, ALU_Out[2]);
  and and_43 (and_43_out, and_1_out, ALU_Out[2]);
  or or_14 (C[2], and_41_out, and_43_out, and_45_out);
  and and_44 (and_44_out, and_2_out, ALU_Out[2]);
  and and_45 (and_45_out, and_3_out, ALU_Out[1]);
  and and_46 (and_46_out, and_1_out, ALU_Out[1]);
  or or_15 (C[1], and_44_out, and_46_out, and_48_out);
  and and_47 (and_47_out, and_2_out, ALU_Out[1]);
  and and_48 (and_48_out, and_3_out, ALU_Out[0]);
  and and_49 (and_49_out, and_1_out, ALU_Out[0]);
  or or_16 (C[0], and_47_out, and_49_out);

  // Notes on the sheet:
  //   BEZ POMJERANJA
  //   POMJERANJE DESNO
  //   POMJERANJE LIJEVO
endmodule

module OgledniProcesor_ALUiShifter (
  input  [15:0] A,
  input  [15:0] B,
  input  [1:0] F,
  input  [1:0] S,
  output N,
  output Z,
  output [15:0] C
);

  wire [15:0] ogledniprocesor_alu16bit_1_result;

  // Probe on A
  // Probe on A
  // Probe on B
  // Probe on B
  OgledniProcesor_ALU16bit ogledniprocesor_alu16bit_1 (
    .A(A), .B(B), .F(F), .N(N), .z(Z), .Result(ogledniprocesor_alu16bit_1_result));
  OgledniProcesor_Shifter ogledniprocesor_shifter_1 (.ALU_Out(ogledniprocesor_alu16bit_1_result), .S(S), .C(C));
  // Probe on C
  // Probe on C
endmodule

module OgledniProcesor_Inkrementer (
  input  [7:0] U,
  output [7:0] I
);

  wire and_1_out, and_2_out, and_3_out, and_4_out, and_5_out, and_6_out, and_7_out;

  // Probe on U
  // Probe on U
  // Probe on I
  // Probe on I
  xor xor_1 (I[7], U[7], and_1_out);
  and and_1 (and_1_out, U[6], and_2_out);
  and and_2 (and_2_out, U[5], and_3_out);
  xor xor_2 (I[6], U[6], and_2_out);
  and and_3 (and_3_out, U[4], and_4_out);
  xor xor_3 (I[5], U[5], and_3_out);
  and and_4 (and_4_out, U[3], and_5_out);
  xor xor_4 (I[4], U[4], and_4_out);
  and and_5 (and_5_out, U[2], and_6_out);
  xor xor_5 (I[3], U[3], and_5_out);
  and and_6 (and_6_out, U[1], and_7_out);
  xor xor_6 (I[2], U[2], and_6_out);
  and and_7 (and_7_out, U[0], 1'b1);
  xor xor_7 (I[1], U[1], and_7_out);
  xor xor_8 (I[0], U[0], 1'b1);
endmodule

module OgledniProcesor_Clk (
  input  CLK,
  input  Reset,
  output clkA,
  output clkB,
  output clkC,
  output clkD
);

  D_Flip_Flop d_ff_1 (.D(clkD), .clk(CLK), .Q(clkA), .reset(Reset));  // open: Qn, preset
  D_Flip_Flop d_ff_2 (.D(clkA), .clk(CLK), .Q(clkB), .reset(Reset));  // open: Qn, preset
  D_Flip_Flop d_ff_3 (.D(clkB), .clk(CLK), .Q(clkC), .reset(Reset));  // open: Qn, preset
  D_Flip_Flop d_ff_4 (.D(clkC), .clk(CLK), .Q(clkD), .preset(Reset));  // open: Qn, reset
endmodule

module OgledniProcesor_Registar8bit (
  input  [7:0] U,
  input  CLK,
  input  Reset,
  output [7:0] I
);

  // Probe on U
  // Probe on U
  // Probe on I
  // Probe on I
  D_Flip_Flop d_ff_1 (.D(U[7]), .clk(CLK), .Q(I[7]), .reset(Reset));  // open: Qn, preset
  D_Flip_Flop d_ff_2 (.D(U[6]), .clk(CLK), .Q(I[6]), .reset(Reset));  // open: Qn, preset
  D_Flip_Flop d_ff_3 (.D(U[5]), .clk(CLK), .Q(I[5]), .reset(Reset));  // open: Qn, preset
  D_Flip_Flop d_ff_4 (.D(U[4]), .clk(CLK), .Q(I[4]), .reset(Reset));  // open: Qn, preset
  D_Flip_Flop d_ff_5 (.D(U[3]), .clk(CLK), .Q(I[3]), .reset(Reset));  // open: Qn, preset
  D_Flip_Flop d_ff_6 (.D(U[2]), .clk(CLK), .Q(I[2]), .reset(Reset));  // open: Qn, preset
  D_Flip_Flop d_ff_7 (.D(U[1]), .clk(CLK), .Q(I[1]), .reset(Reset));  // open: Qn, preset
  D_Flip_Flop d_ff_8 (.D(U[0]), .clk(CLK), .Q(I[0]), .reset(Reset));  // open: Qn, preset
endmodule

module OgledniProcesor_Registar16bit (
  input  [15:0] U,
  input  CLK,
  input  Reset,
  output [15:0] I
);

  // Probe on U
  // Probe on U
  // Probe on I
  // Probe on I
  D_Flip_Flop d_ff_1 (.D(U[15]), .clk(CLK), .Q(I[15]), .reset(Reset));  // open: Qn, preset
  D_Flip_Flop d_ff_2 (.D(U[14]), .clk(CLK), .Q(I[14]), .reset(Reset));  // open: Qn, preset
  D_Flip_Flop d_ff_3 (.D(U[13]), .clk(CLK), .Q(I[13]), .reset(Reset));  // open: Qn, preset
  D_Flip_Flop d_ff_4 (.D(U[12]), .clk(CLK), .Q(I[12]), .reset(Reset));  // open: Qn, preset
  D_Flip_Flop d_ff_5 (.D(U[11]), .clk(CLK), .Q(I[11]), .reset(Reset));  // open: Qn, preset
  D_Flip_Flop d_ff_6 (.D(U[10]), .clk(CLK), .Q(I[10]), .reset(Reset));  // open: Qn, preset
  D_Flip_Flop d_ff_7 (.D(U[9]), .clk(CLK), .Q(I[9]), .reset(Reset));  // open: Qn, preset
  D_Flip_Flop d_ff_8 (.D(U[8]), .clk(CLK), .Q(I[8]), .reset(Reset));  // open: Qn, preset
  D_Flip_Flop d_ff_9 (.D(U[7]), .clk(CLK), .Q(I[7]), .reset(Reset));  // open: Qn, preset
  D_Flip_Flop d_ff_10 (.D(U[6]), .clk(CLK), .Q(I[6]), .reset(Reset));  // open: Qn, preset
  D_Flip_Flop d_ff_11 (.D(U[5]), .clk(CLK), .Q(I[5]), .reset(Reset));  // open: Qn, preset
  D_Flip_Flop d_ff_12 (.D(U[4]), .clk(CLK), .Q(I[4]), .reset(Reset));  // open: Qn, preset
  D_Flip_Flop d_ff_13 (.D(U[3]), .clk(CLK), .Q(I[3]), .reset(Reset));  // open: Qn, preset
  D_Flip_Flop d_ff_14 (.D(U[2]), .clk(CLK), .Q(I[2]), .reset(Reset));  // open: Qn, preset
  D_Flip_Flop d_ff_15 (.D(U[1]), .clk(CLK), .Q(I[1]), .reset(Reset));  // open: Qn, preset
  D_Flip_Flop d_ff_16 (.D(U[0]), .clk(CLK), .Q(I[0]), .reset(Reset));  // open: Qn, preset
endmodule

module OgledniProcesor_RegistarskaDatoteka (
  input  enC,
  input  CLK,
  input  [15:0] sC,
  input  [3:0] srcA,
  input  [3:0] srcB,
  input  [3:0] dst,
  input  Reset,
  output [15:0] sA,
  output [15:0] sB,
  output [15:0] PC,
  output [15:0] ACC,
  output [15:0] SP,
  output [15:0] IR,
  output [15:0] TIR,
  output [15:0] A,
  output [15:0] B,
  output [15:0] C,
  output [15:0] D,
  output [15:0] E,
  output [15:0] F
);

  wire and_1_out, decoder_1_out0, decoder_1_out1, decoder_1_out2, decoder_1_out3, decoder_1_out4,
       decoder_1_out10, decoder_1_out11, decoder_1_out12, decoder_1_out13, decoder_1_out14, decoder_1_out15;

  // Probe on sC
  and and_1 (and_1_out, enC, CLK);
  Decoder #(.select(4)) decoder_1 (
    .out0(decoder_1_out0), .out1(decoder_1_out1), .out2(decoder_1_out2), .out3(decoder_1_out3),
    .out4(decoder_1_out4), .out10(decoder_1_out10), .out11(decoder_1_out11), .out12(decoder_1_out12),
    .out13(decoder_1_out13), .out14(decoder_1_out14), .out15(decoder_1_out15), .sel(dst), .en(and_1_out));  // open: out5, out6, out7, out8, out9
  OgledniProcesor_Registar16bit Reg_PC (.CLK(decoder_1_out0), .Reset(Reset), .U(sC), .I(PC));
  OgledniProcesor_Registar16bit Reg_ACC (.CLK(decoder_1_out1), .Reset(Reset), .U(sC), .I(ACC));
  OgledniProcesor_Registar16bit Reg_SP (.CLK(decoder_1_out2), .Reset(Reset), .U(sC), .I(SP));
  OgledniProcesor_Registar16bit Reg_IR (.CLK(decoder_1_out3), .Reset(Reset), .U(sC), .I(IR));
  OgledniProcesor_Registar16bit Reg_TIR (.CLK(decoder_1_out4), .Reset(Reset), .U(sC), .I(TIR));
  OgledniProcesor_Registar16bit Reg_A (.CLK(decoder_1_out10), .Reset(Reset), .U(sC), .I(A));
  OgledniProcesor_Registar16bit Reg_B (.CLK(decoder_1_out11), .Reset(Reset), .U(sC), .I(B));
  OgledniProcesor_Registar16bit Reg_C (.CLK(decoder_1_out12), .Reset(Reset), .U(sC), .I(C));
  OgledniProcesor_Registar16bit Reg_D (.CLK(decoder_1_out13), .Reset(Reset), .U(sC), .I(D));
  OgledniProcesor_Registar16bit Reg_E (.CLK(decoder_1_out14), .Reset(Reset), .U(sC), .I(E));
  OgledniProcesor_Registar16bit Reg_F (.CLK(decoder_1_out15), .Reset(Reset), .U(sC), .I(F));
  // Probe on sA
  Multiplexer #(.enable("true"), .select(4), .width(16)) multiplexer_1 (
    .in0(PC), .in1(ACC), .in2(SP), .in3(IR), .in4(TIR), .in5({16{1'b0}}), .in6(16'h1), .in7({16{1'b1}}),
    .in8(16'hfff), .in9(16'hff), .in10(A), .in11(B), .in12(C), .in13(D), .in14(E), .in15(F), .out(sA),
    .sel(srcA));  // open: en
  // Probe on sB
  Multiplexer #(.enable("true"), .select(4), .width(16)) multiplexer_2 (
    .in0(PC), .in1(ACC), .in2(SP), .in3(IR), .in4(TIR), .in5({16{1'b0}}), .in6(16'h1), .in7({16{1'b1}}),
    .in8(16'hfff), .in9(16'hff), .in10(A), .in11(B), .in12(C), .in13(D), .in14(E), .in15(F), .out(sB),
    .sel(srcB));  // open: en

  // Notes on the sheet:
  //   Reg 0
  //   Reg 1
  //   Reg -1
  //   Reg Amask
  //   Reg Smask
endmodule

module OgledniProcesor_RegistarMAR (
  input  [11:0] U,
  input  MAR,
  input  CLK,
  input  Reset,
  output [11:0] I
);

  wire and_1_out;

  // Probe on U
  // Probe on U
  and and_1 (and_1_out, MAR, CLK);
  // Probe on I
  // Probe on I
  D_Flip_Flop d_ff_1 (.D(U[11]), .clk(and_1_out), .Q(I[11]), .reset(Reset));  // open: Qn, preset
  D_Flip_Flop d_ff_2 (.D(U[10]), .clk(and_1_out), .Q(I[10]), .reset(Reset));  // open: Qn, preset
  D_Flip_Flop d_ff_3 (.D(U[9]), .clk(and_1_out), .Q(I[9]), .reset(Reset));  // open: Qn, preset
  D_Flip_Flop d_ff_4 (.D(U[8]), .clk(and_1_out), .Q(I[8]), .reset(Reset));  // open: Qn, preset
  D_Flip_Flop d_ff_5 (.D(U[7]), .clk(and_1_out), .Q(I[7]), .reset(Reset));  // open: Qn, preset
  D_Flip_Flop d_ff_6 (.D(U[6]), .clk(and_1_out), .Q(I[6]), .reset(Reset));  // open: Qn, preset
  D_Flip_Flop d_ff_7 (.D(U[5]), .clk(and_1_out), .Q(I[5]), .reset(Reset));  // open: Qn, preset
  D_Flip_Flop d_ff_8 (.D(U[4]), .clk(and_1_out), .Q(I[4]), .reset(Reset));  // open: Qn, preset
  D_Flip_Flop d_ff_9 (.D(U[3]), .clk(and_1_out), .Q(I[3]), .reset(Reset));  // open: Qn, preset
  D_Flip_Flop d_ff_10 (.D(U[2]), .clk(and_1_out), .Q(I[2]), .reset(Reset));  // open: Qn, preset
  D_Flip_Flop d_ff_11 (.D(U[1]), .clk(and_1_out), .Q(I[1]), .reset(Reset));  // open: Qn, preset
  D_Flip_Flop d_ff_12 (.D(U[0]), .clk(and_1_out), .Q(I[0]), .reset(Reset));  // open: Qn, preset
endmodule

module OgledniProcesor_RegistarMBR (
  input  [15:0] U_C,
  input  [15:0] U_mem,
  input  MBR,
  input  Rd,
  input  CLK,
  input  Reset,
  output [15:0] I
);

  wire and_1_out, xor_1_out;
  wire [15:0] controlled_buffer_1_out;

  // Probe on U_C
  // Probe on U_C
  // Probe on U_mem
  // Probe on U_mem
  assign controlled_buffer_1_out = MBR ? U_C : 16'bz;  // Controlled_Buffer controlled_buffer_1
  assign controlled_buffer_1_out = Rd ? U_mem : 16'bz;  // Controlled_Buffer controlled_buffer_2
  xor xor_1 (xor_1_out, MBR, Rd);
  and and_1 (and_1_out, xor_1_out, CLK);
  // Probe on I
  // Probe on I
  D_Flip_Flop d_ff_1 (.D(controlled_buffer_1_out[15]), .clk(and_1_out), .Q(I[15]), .reset(Reset));  // open: Qn, preset
  D_Flip_Flop d_ff_2 (.D(controlled_buffer_1_out[14]), .clk(and_1_out), .Q(I[14]), .reset(Reset));  // open: Qn, preset
  D_Flip_Flop d_ff_3 (.D(controlled_buffer_1_out[13]), .clk(and_1_out), .Q(I[13]), .reset(Reset));  // open: Qn, preset
  D_Flip_Flop d_ff_4 (.D(controlled_buffer_1_out[12]), .clk(and_1_out), .Q(I[12]), .reset(Reset));  // open: Qn, preset
  D_Flip_Flop d_ff_5 (.D(controlled_buffer_1_out[11]), .clk(and_1_out), .Q(I[11]), .reset(Reset));  // open: Qn, preset
  D_Flip_Flop d_ff_6 (.D(controlled_buffer_1_out[10]), .clk(and_1_out), .Q(I[10]), .reset(Reset));  // open: Qn, preset
  D_Flip_Flop d_ff_7 (.D(controlled_buffer_1_out[9]), .clk(and_1_out), .Q(I[9]), .reset(Reset));  // open: Qn, preset
  D_Flip_Flop d_ff_8 (.D(controlled_buffer_1_out[8]), .clk(and_1_out), .Q(I[8]), .reset(Reset));  // open: Qn, preset
  D_Flip_Flop d_ff_9 (.D(controlled_buffer_1_out[7]), .clk(and_1_out), .Q(I[7]), .reset(Reset));  // open: Qn, preset
  D_Flip_Flop d_ff_10 (.D(controlled_buffer_1_out[6]), .clk(and_1_out), .Q(I[6]), .reset(Reset));  // open: Qn, preset
  D_Flip_Flop d_ff_11 (.D(controlled_buffer_1_out[5]), .clk(and_1_out), .Q(I[5]), .reset(Reset));  // open: Qn, preset
  D_Flip_Flop d_ff_12 (.D(controlled_buffer_1_out[4]), .clk(and_1_out), .Q(I[4]), .reset(Reset));  // open: Qn, preset
  D_Flip_Flop d_ff_13 (.D(controlled_buffer_1_out[3]), .clk(and_1_out), .Q(I[3]), .reset(Reset));  // open: Qn, preset
  D_Flip_Flop d_ff_14 (.D(controlled_buffer_1_out[2]), .clk(and_1_out), .Q(I[2]), .reset(Reset));  // open: Qn, preset
  D_Flip_Flop d_ff_15 (.D(controlled_buffer_1_out[1]), .clk(and_1_out), .Q(I[1]), .reset(Reset));  // open: Qn, preset
  D_Flip_Flop d_ff_16 (.D(controlled_buffer_1_out[0]), .clk(and_1_out), .Q(I[0]), .reset(Reset));  // open: Qn, preset
endmodule

module OgledniProcesor_RegistarMIR (
  input  [31:0] U_ROM,
  input  CLK,
  input  Reset,
  output AMUX,
  output [1:0] COND,
  output [1:0] ALU,
  output [1:0] SHIFT,
  output MBR,
  output MAR,
  output RD,
  output WR,
  output ENC,
  output [3:0] C,
  output [3:0] B,
  output [3:0] A,
  output [7:0] Adr
);

  // Probe on U_ROM
  // Probe on U_ROM
  D_Flip_Flop d_ff_1 (.D(U_ROM[31]), .clk(CLK), .Q(AMUX), .reset(Reset));  // open: Qn, preset
  D_Flip_Flop d_ff_2 (.D(U_ROM[30]), .clk(CLK), .Q(COND[1]), .reset(Reset));  // open: Qn, preset
  D_Flip_Flop d_ff_3 (.D(U_ROM[29]), .clk(CLK), .Q(COND[0]), .reset(Reset));  // open: Qn, preset
  D_Flip_Flop d_ff_4 (.D(U_ROM[28]), .clk(CLK), .Q(ALU[1]), .reset(Reset));  // open: Qn, preset
  D_Flip_Flop d_ff_5 (.D(U_ROM[27]), .clk(CLK), .Q(ALU[0]), .reset(Reset));  // open: Qn, preset
  D_Flip_Flop d_ff_6 (.D(U_ROM[26]), .clk(CLK), .Q(SHIFT[1]), .reset(Reset));  // open: Qn, preset
  D_Flip_Flop d_ff_7 (.D(U_ROM[25]), .clk(CLK), .Q(SHIFT[0]), .reset(Reset));  // open: Qn, preset
  D_Flip_Flop d_ff_8 (.D(U_ROM[24]), .clk(CLK), .Q(MBR), .reset(Reset));  // open: Qn, preset
  D_Flip_Flop d_ff_9 (.D(U_ROM[23]), .clk(CLK), .Q(MAR), .reset(Reset));  // open: Qn, preset
  D_Flip_Flop d_ff_10 (.D(U_ROM[22]), .clk(CLK), .Q(RD), .reset(Reset));  // open: Qn, preset
  D_Flip_Flop d_ff_11 (.D(U_ROM[21]), .clk(CLK), .Q(WR), .reset(Reset));  // open: Qn, preset
  D_Flip_Flop d_ff_12 (.D(U_ROM[20]), .clk(CLK), .Q(ENC), .reset(Reset));  // open: Qn, preset
  D_Flip_Flop d_ff_13 (.D(U_ROM[19]), .clk(CLK), .Q(C[3]), .reset(Reset));  // open: Qn, preset
  D_Flip_Flop d_ff_14 (.D(U_ROM[18]), .clk(CLK), .Q(C[2]), .reset(Reset));  // open: Qn, preset
  D_Flip_Flop d_ff_15 (.D(U_ROM[17]), .clk(CLK), .Q(C[1]), .reset(Reset));  // open: Qn, preset
  D_Flip_Flop d_ff_16 (.D(U_ROM[16]), .clk(CLK), .Q(C[0]), .reset(Reset));  // open: Qn, preset
  D_Flip_Flop d_ff_17 (.D(U_ROM[15]), .clk(CLK), .Q(B[3]), .reset(Reset));  // open: Qn, preset
  D_Flip_Flop d_ff_18 (.D(U_ROM[14]), .clk(CLK), .Q(B[2]), .reset(Reset));  // open: Qn, preset
  D_Flip_Flop d_ff_19 (.D(U_ROM[13]), .clk(CLK), .Q(B[1]), .reset(Reset));  // open: Qn, preset
  D_Flip_Flop d_ff_20 (.D(U_ROM[12]), .clk(CLK), .Q(B[0]), .reset(Reset));  // open: Qn, preset
  D_Flip_Flop d_ff_21 (.D(U_ROM[11]), .clk(CLK), .Q(A[3]), .reset(Reset));  // open: Qn, preset
  D_Flip_Flop d_ff_22 (.D(U_ROM[10]), .clk(CLK), .Q(A[2]), .reset(Reset));  // open: Qn, preset
  D_Flip_Flop d_ff_23 (.D(U_ROM[9]), .clk(CLK), .Q(A[1]), .reset(Reset));  // open: Qn, preset
  D_Flip_Flop d_ff_24 (.D(U_ROM[8]), .clk(CLK), .Q(A[0]), .reset(Reset));  // open: Qn, preset
  D_Flip_Flop d_ff_25 (.D(U_ROM[7]), .clk(CLK), .Q(Adr[7]), .reset(Reset));  // open: Qn, preset
  D_Flip_Flop d_ff_26 (.D(U_ROM[6]), .clk(CLK), .Q(Adr[6]), .reset(Reset));  // open: Qn, preset
  D_Flip_Flop d_ff_27 (.D(U_ROM[5]), .clk(CLK), .Q(Adr[5]), .reset(Reset));  // open: Qn, preset
  D_Flip_Flop d_ff_28 (.D(U_ROM[4]), .clk(CLK), .Q(Adr[4]), .reset(Reset));  // open: Qn, preset
  D_Flip_Flop d_ff_29 (.D(U_ROM[3]), .clk(CLK), .Q(Adr[3]), .reset(Reset));  // open: Qn, preset
  D_Flip_Flop d_ff_30 (.D(U_ROM[2]), .clk(CLK), .Q(Adr[2]), .reset(Reset));  // open: Qn, preset
  D_Flip_Flop d_ff_31 (.D(U_ROM[1]), .clk(CLK), .Q(Adr[1]), .reset(Reset));  // open: Qn, preset
  D_Flip_Flop d_ff_32 (.D(U_ROM[0]), .clk(CLK), .Q(Adr[0]), .reset(Reset));  // open: Qn, preset
endmodule

module OgledniProcesor (
);

  wire AMUX, and_1_out, and_2_out, and_3_out, clk_A, clk_B, clk_C, clk_D, CLK_out, ENC, MAR, MBR, N,
       or_1_out, Power, Rd, Wr, Z;
  wire [1:0] ALU, COND, SHIFT;
  wire [3:0] A, B, C, ogledniprocesor_registar16bit_2_i_2;
  wire [7:0] Adr, Inkrementer_i, MPC_i, multiplexer_1_out;
  wire [11:0] MAR_i, ogledniprocesor_registar16bit_2_i;
  wire [15:0] MBR_i, multiplexer_2_out, ogledniprocesor_aluishifter_1_c, ogledniprocesor_registar16bit_1_i,
       ogledniprocesor_registarskadatoteka_1_a, ogledniprocesor_registarskadatoteka_1_acc,
       ogledniprocesor_registarskadatoteka_1_b, ogledniprocesor_registarskadatoteka_1_c,
       ogledniprocesor_registarskadatoteka_1_d, ogledniprocesor_registarskadatoteka_1_e,
       ogledniprocesor_registarskadatoteka_1_f, ogledniprocesor_registarskadatoteka_1_ir,
       ogledniprocesor_registarskadatoteka_1_pc, ogledniprocesor_registarskadatoteka_1_sa,
       ogledniprocesor_registarskadatoteka_1_sb, ogledniprocesor_registarskadatoteka_1_sp,
       ogledniprocesor_registarskadatoteka_1_tir, ram_1_dout;
  wire [31:0] rom_1_data;

  RAM #(.addrWidth(12), .dataWidth(16)) ram_1 (
    .addr(MAR_i), .we(Wr), .oe(Rd), .clk(clk_C), .din(MBR_i), .dout(ram_1_dout));
  Clock CLK (.out(CLK_out));
  Button u_Power (.out(Power));
  OgledniProcesor_Clk ogledniprocesor_clk_1 (
    .CLK(CLK_out), .Reset(Power), .clkA(clk_A), .clkB(clk_B), .clkC(clk_C), .clkD(clk_D));
  // Probe on ram_1_dout
  Multiplexer #(.width(8)) multiplexer_1 (.in0(Inkrementer_i), .in1(Adr), .out(multiplexer_1_out), .sel(or_1_out));
  or or_1 (or_1_out, and_1_out, and_2_out, and_3_out);
  and and_1 (and_1_out, Z, COND[1]);
  and and_2 (and_2_out, COND[1], COND[0]);
  // Probe on COND
  // Probe on MAR_i
  OgledniProcesor_Inkrementer Inkrementer (.U(MPC_i), .I(Inkrementer_i));
  and and_3 (and_3_out, COND[0], N);
  OgledniProcesor_RegistarMAR u_MAR (
    .Reset(Power), .U(ogledniprocesor_registar16bit_2_i), .MAR(MAR), .CLK(clk_C), .I(MAR_i));
  // Probe on MBR_i
  OgledniProcesor_RegistarMBR u_MBR (
    .MBR(MBR), .Rd(Rd), .CLK(clk_D), .Reset(Power), .U_C(ogledniprocesor_aluishifter_1_c),
    .U_mem(ram_1_dout), .I(MBR_i));
  // Probe on MPC_i
  OgledniProcesor_Registar8bit MPC (.CLK(clk_D), .Reset(Power), .U(multiplexer_1_out), .I(MPC_i));
  ROM #(.dataWidth(32)) rom_1 (.addr(MPC_i), .data(rom_1_data));
  // Probe on ogledniprocesor_registarskadatoteka_1_pc
  // Probe on ogledniprocesor_registarskadatoteka_1_a
  // Probe on ogledniprocesor_registarskadatoteka_1_acc
  // Probe on ogledniprocesor_registarskadatoteka_1_b
  // Probe on ogledniprocesor_registarskadatoteka_1_sp
  // Probe on ogledniprocesor_registarskadatoteka_1_c
  // Probe on ogledniprocesor_registarskadatoteka_1_ir
  // Probe on ogledniprocesor_registarskadatoteka_1_d
  // Probe on ogledniprocesor_registarskadatoteka_1_tir
  // Probe on ogledniprocesor_registarskadatoteka_1_e
  // Probe on ogledniprocesor_registarskadatoteka_1_f
  OgledniProcesor_RegistarskaDatoteka ogledniprocesor_registarskadatoteka_1 (
    .srcB(B), .sC(ogledniprocesor_aluishifter_1_c), .enC(ENC), .CLK(clk_D), .dst(C), .Reset(Power), .srcA(A),
    .sB(ogledniprocesor_registarskadatoteka_1_sb), .PC(ogledniprocesor_registarskadatoteka_1_pc),
    .ACC(ogledniprocesor_registarskadatoteka_1_acc), .SP(ogledniprocesor_registarskadatoteka_1_sp),
    .IR(ogledniprocesor_registarskadatoteka_1_ir), .TIR(ogledniprocesor_registarskadatoteka_1_tir),
    .A(ogledniprocesor_registarskadatoteka_1_a), .B(ogledniprocesor_registarskadatoteka_1_b),
    .C(ogledniprocesor_registarskadatoteka_1_c), .D(ogledniprocesor_registarskadatoteka_1_d),
    .E(ogledniprocesor_registarskadatoteka_1_e), .F(ogledniprocesor_registarskadatoteka_1_f),
    .sA(ogledniprocesor_registarskadatoteka_1_sa));
  // Probe on ogledniprocesor_registarskadatoteka_1_sa
  OgledniProcesor_Registar16bit ogledniprocesor_registar16bit_1 (
    .CLK(clk_B), .U(ogledniprocesor_registarskadatoteka_1_sa), .I(ogledniprocesor_registar16bit_1_i));  // open: Reset
  // Probe on ogledniprocesor_registar16bit_1_i
  Multiplexer #(.width(16)) multiplexer_2 (
    .in0(ogledniprocesor_registar16bit_1_i), .in1(MBR_i), .out(multiplexer_2_out), .sel(AMUX));
  // Probe on ogledniprocesor_aluishifter_1_c
  // Probe on AMUX
  OgledniProcesor_RegistarMIR ogledniprocesor_registarmir_1 (
    .CLK(clk_A), .Reset(Power), .U_ROM(rom_1_data), .AMUX(AMUX), .COND(COND), .ALU(ALU), .SHIFT(SHIFT),
    .MBR(MBR), .MAR(MAR), .RD(Rd), .WR(Wr), .ENC(ENC), .C(C), .B(B), .A(A), .Adr(Adr));
  // Probe on COND
  // Probe on ALU
  // Probe on SHIFT
  // Probe on MBR
  // Probe on MAR
  // Probe on Rd
  // Probe on Wr
  // Probe on ENC
  // Probe on C
  // Probe on B
  // Probe on A
  // Probe on Adr
  // Probe on ogledniprocesor_registarskadatoteka_1_sb
  OgledniProcesor_Registar16bit ogledniprocesor_registar16bit_2 (
    .CLK(clk_B), .U(ogledniprocesor_registarskadatoteka_1_sb),
    .I({ogledniprocesor_registar16bit_2_i_2, ogledniprocesor_registar16bit_2_i}));  // open: Reset
  // Probe on {ogledniprocesor_registar16bit_2_i_2, ogledniprocesor_registar16bit_2_i}
  OgledniProcesor_ALUiShifter ogledniprocesor_aluishifter_1 (
    .A(multiplexer_2_out), .B({ogledniprocesor_registar16bit_2_i_2, ogledniprocesor_registar16bit_2_i}),
    .F(ALU), .S(SHIFT), .N(N), .C(ogledniprocesor_aluishifter_1_c), .Z(Z));

  // Notes on the sheet:
  //   NA DOBROM STE MJESTU, ovdje sam pravio izmjene
  //   contents of rom_1 (hex, n*v repeats v):
  //   c00000 506000 b013001c 24143313 3414040b 30000409 c03000 400000 f0110000 11a03100 60200000 3000040f
  //   c03000 400000 e0111000 c03000 516100 981a0000 6011a100 34140419 30000417 30000100 68108300 50000116
  //   60000000 3000041b 68108300 68118300 24143328 34140423 30000421 1a2300 60c0a007 1a2300 71a0a10a
  //   30000426 1a2300 60c0a00d 1a2300 60c0a010 3414042e 3000042c 60000050 ffffffff 50000100 68108300
  //   34140432 127200 11a02000 68308300 34140441 3414043b 30000438 c01000 527200 60a0200a d22600 400000
  //   60a0100a 3000043e 127200 71a0210a d22600 400000 f0110000 34140449 30000446 d22600 400000 f0100000
  //   101a0100 10110200 70120a00 3000044c 81a9300 6012a200 81a9300 181a0a00 601a6a4b 0 101a0100 c03000
  //   400000 d01b0058 1bb700 111a00 401bb700 60000055 70110500
endmodule
